// Logisim project TPU.circ as structural Verilog: 46 circuits, main circuit adder_2bit
module Ins_Tiling_finals_v2 (
);

  wire bcd_to_7_segment_decoder_3_p1, binary_to_bcd_converter_1_p2, binary_to_bcd_converter_1_p4,
       clock_1_out, comparator_1_eq, comparator_2_eq, comparator_3_lt, comparator_4_eq, comparator_5_eq,
       comparator_6_eq, comparator_7_eq, comparator_8_eq, comparator_9_eq, comparator_10_eq,
       comparator_11_eq, decoder_custom_1_y1, decoder_custom_1_y2, decoder_custom_1_y3, decoder_custom_1_y4,
       decoder_custom_1_y5, decoder_custom_1_y6, decoder_custom_1_y7, decoder_custom_1_y8,
       decoder_custom_1_y9, decoder_custom_1_y10, decoder_custom_1_y11, decoder_custom_1_y12,
       decoder_custom_1_y13, decoder_custom_1_y14, decoder_custom_1_y15, decoder_custom_1_y16,
       decoder_custom_2_y1, decoder_custom_2_y2, decoder_custom_2_y3, decoder_custom_2_y4,
       decoder_custom_2_y5, decoder_custom_2_y6, decoder_custom_2_y7, decoder_custom_2_y8,
       decoder_custom_2_y9, decoder_custom_2_y10, decoder_custom_2_y11, decoder_custom_2_y12,
       decoder_custom_2_y13, decoder_custom_2_y14, decoder_custom_2_y15, decoder_custom_2_y16, or_1_out,
       or_2_out, undriven, undriven_2, undriven_3, undriven_4, xor_1_out, xor_2_out;
  wire [3:0] controlled_buffer_1_out, counter_5_q, counter_6_q, info_loada_1_dim_a_out,
       info_loadb_1_dim_b_out, info_mmult_1_dim_mmult, info_stoc_1_dim_store_out, ins_splitter_1_dimension,
       ins_splitter_1_opcode;
  wire [7:0] bit_extender_1_out, bit_extender_2_out, counter_1_q, counter_2_q, counter_3_q,
       info_loada_1_addres_a_out, info_loadb_1_addres_b_out, info_mmult_1_addres_mmult,
       info_stoc_1_addres_store_out, ins_splitter_1_adress;
  wire [8:0] counter_4_q;
  wire [15:0] InstructionRam_dout, RamA_dout, RamB_dout;

  xor xor_1 (xor_1_out, undriven, comparator_1_eq);
  xor xor_2 (xor_2_out, undriven_2, comparator_2_eq);
  RAM #(.dataWidth(16), .\type ("nonvolatile")) InstructionRam (
    .addr(counter_1_q), .clk(clock_1_out), .dout(InstructionRam_dout));  // open: we, oe, din
  Counter counter_1 (.count(comparator_3_lt), .Q(counter_1_q), .clk(clock_1_out));  // open: load, D, carry, up, clr
  Clock clock_1 (.out(clock_1_out));
  RAM #(.dataWidth(16)) RamA (.addr(counter_2_q), .dout(RamA_dout));  // open: we, oe, clk, din
  Counter counter_2 (.count(xor_1_out), .Q(counter_2_q), .clk(undriven_4));  // open: load, D, carry, up, clr
  assign bit_extender_1_out = {{4{counter_5_q[3]}}, counter_5_q};  // Bit_Extender bit_extender_1
  RAM #(.dataWidth(16)) RamB (.addr(counter_3_q), .dout(RamB_dout));  // open: we, oe, clk, din
  Counter counter_3 (.count(xor_2_out), .Q(counter_3_q), .clk(undriven_3));  // open: load, D, carry, up, clr
  Counter #(.max('h1ff), .width(9)) counter_4 (
    .Q(counter_4_q), .clk(clock_1_out));  // open: load, D, count, carry, up, clr
  Comparator #(.mode("unsigned")) comparator_1 (
    .a(bit_extender_1_out), .b(8'h10), .eq(comparator_1_eq));  // open: gt, lt
  assign bit_extender_2_out = {{4{counter_6_q[3]}}, counter_6_q};  // Bit_Extender bit_extender_2
  _7_Segment_Display u_7_segment_display_1 ();  // open: g, f, a, b, e, d, c, dp
  // BCD_to_7_Segment_decoder bcd_to_7_segment_decoder_1: pin names not known
  // Binary_to_BCD_converter binary_to_bcd_converter_1: pin names not known; wires that end beside it: counter_4_q, binary_to_bcd_converter_1_p2, binary_to_bcd_converter_1_p2, binary_to_bcd_converter_1_p4
  Comparator #(.mode("unsigned")) comparator_2 (
    .a(bit_extender_2_out), .b(8'h10), .eq(comparator_2_eq));  // open: gt, lt
  _7_Segment_Display u_7_segment_display_2 ();  // open: g, f, a, b, e, d, c, dp
  // BCD_to_7_Segment_decoder bcd_to_7_segment_decoder_2: pin names not known; wires that end beside it: binary_to_bcd_converter_1_p4
  Comparator comparator_3 (.a(counter_1_q), .b(8'h4), .lt(comparator_3_lt));  // open: gt, eq
  // Probe on counter_5_q
  // Probe on counter_6_q
  matmult_tiling_4x4_core matmult_tiling_4x4_core_1 ();  // open: A1, A2, A3, A4, A5, A6, A7, A8, A9, A10, A11, A12, A13, A14, A15, A16, B1, B2, B3, B4, B5, B6, B7, B8, B9, B10, B11, B12, B13, B14, B15, B16, C1, C2, C3, C4, C5, C6, C7, C8, C9, C10, C11, C12, C13, C14, C15, C16
  _7_Segment_Display u_7_segment_display_3 ();  // open: g, f, a, b, e, d, c, dp
  // BCD_to_7_Segment_decoder bcd_to_7_segment_decoder_3: pin names not known; wires that end beside it: bcd_to_7_segment_decoder_3_p1, bcd_to_7_segment_decoder_3_p1
  // Probe on InstructionRam_dout
  Counter #(.max('hf), .width(4)) counter_5 (
    .count(xor_1_out), .Q(counter_5_q), .clk(undriven_4));  // open: load, D, carry, up, clr
  Counter #(.max('hf), .width(4)) counter_6 (
    .count(xor_2_out), .Q(counter_6_q), .clk(undriven_3));  // open: load, D, carry, up, clr
  // Probe on ins_splitter_1_adress
  Ins_splitter ins_splitter_1 (
    .Instruction(InstructionRam_dout), .WE(comparator_3_lt), .Clock(clock_1_out),
    .Adress(ins_splitter_1_adress), .Dimension(ins_splitter_1_dimension), .Opcode(ins_splitter_1_opcode));
  Matrix_Acumulator matrix_acumulator_1 ();  // open: V1, V2, V3, V4, V5, V6, V7, V8, V9, V10, V11, V12, V13, V14, V15, V16, Tile_Num, clock, Enable, a1, a2, a3, a4, a5, a6, a7, a8, a9, a10, a11, a12, a13, a14, a15, a16, b1, b2, b3, b4, b5, b6, b7, b8, b9, b10, b11, b12, b13, b14, b15, b16, c1, c2, c3, c4, c5, c6, c7, c8, c9, c10, c11, c12, c13, c14, c15, c16
  // Probe on ins_splitter_1_dimension
  // Probe on ins_splitter_1_opcode
  decoder_custom decoder_custom_1 (
    .x1(counter_5_q[0]), .x2(counter_5_q[1]), .x3(counter_5_q[2]), .x4(counter_5_q[3]), .Enable(xor_1_out),
    .y1(decoder_custom_1_y1), .y2(decoder_custom_1_y2), .y3(decoder_custom_1_y3), .y4(decoder_custom_1_y4),
    .y5(decoder_custom_1_y5), .y6(decoder_custom_1_y6), .y7(decoder_custom_1_y7), .y8(decoder_custom_1_y8),
    .y9(decoder_custom_1_y9), .y10(decoder_custom_1_y10), .y11(decoder_custom_1_y11),
    .y12(decoder_custom_1_y12), .y13(decoder_custom_1_y13), .y14(decoder_custom_1_y14),
    .y15(decoder_custom_1_y15), .y16(decoder_custom_1_y16));
  decoder_custom decoder_custom_2 (
    .x1(counter_6_q[0]), .x2(counter_6_q[1]), .x3(counter_6_q[2]), .x4(counter_6_q[3]), .Enable(xor_2_out),
    .y1(decoder_custom_2_y1), .y2(decoder_custom_2_y2), .y3(decoder_custom_2_y3), .y4(decoder_custom_2_y4),
    .y5(decoder_custom_2_y5), .y6(decoder_custom_2_y6), .y7(decoder_custom_2_y7), .y8(decoder_custom_2_y8),
    .y9(decoder_custom_2_y9), .y10(decoder_custom_2_y10), .y11(decoder_custom_2_y11),
    .y12(decoder_custom_2_y12), .y13(decoder_custom_2_y13), .y14(decoder_custom_2_y14),
    .y15(decoder_custom_2_y15), .y16(decoder_custom_2_y16));
  Comparator #(.width(4)) comparator_4 (.a(ins_splitter_1_opcode), .b(4'b0001), .eq(comparator_4_eq));  // open: gt, lt
  Comparator #(.width(4)) comparator_5 (.a(ins_splitter_1_opcode), .b(4'b0010), .eq(comparator_5_eq));  // open: gt, lt
  Comparator #(.width(4)) comparator_6 (.a(ins_splitter_1_opcode), .b(4'b0100), .eq(comparator_6_eq));  // open: gt, lt
  Comparator #(.width(4)) comparator_7 (.a(ins_splitter_1_opcode), .b(4'b0011), .eq(comparator_7_eq));  // open: gt, lt
  registerBanks_16 registerbanks_16_1 (
    .Value(RamA_dout), .WE1(decoder_custom_1_y1), .WE2(decoder_custom_1_y2), .WE3(decoder_custom_1_y3),
    .WE4(decoder_custom_1_y4), .WE5(decoder_custom_1_y5), .WE6(decoder_custom_1_y6),
    .WE7(decoder_custom_1_y7), .WE8(decoder_custom_1_y8), .WE9(decoder_custom_1_y9),
    .WE10(decoder_custom_1_y10), .WE11(decoder_custom_1_y11), .WE12(decoder_custom_1_y12),
    .WE13(decoder_custom_1_y13), .WE14(decoder_custom_1_y14), .WE15(decoder_custom_1_y15),
    .WE16(decoder_custom_1_y16), .clock(undriven_4));  // open: R1, R2, R3, R4, R5, R6, R7, R8, R9, R10, R11, R12, R13, R14, R15, R16
  registerBanks_16 registerbanks_16_2 (
    .Value(RamB_dout), .WE1(decoder_custom_2_y1), .WE2(decoder_custom_2_y2), .WE3(decoder_custom_2_y3),
    .WE4(decoder_custom_2_y4), .WE5(decoder_custom_2_y5), .WE6(decoder_custom_2_y6),
    .WE7(decoder_custom_2_y7), .WE8(decoder_custom_2_y8), .WE9(decoder_custom_2_y9),
    .WE10(decoder_custom_2_y10), .WE11(decoder_custom_2_y11), .WE12(decoder_custom_2_y12),
    .WE13(decoder_custom_2_y13), .WE14(decoder_custom_2_y14), .WE15(decoder_custom_2_y15),
    .WE16(decoder_custom_2_y16), .clock(undriven_3));  // open: R1, R2, R3, R4, R5, R6, R7, R8, R9, R10, R11, R12, R13, R14, R15, R16
  Info_LoadA info_loada_1 (
    .Dim_A_In(ins_splitter_1_dimension), .Add_A_In(ins_splitter_1_adress), .WE_A(comparator_4_eq),
    .Clock_A(clock_1_out), .Dim_A_out(info_loada_1_dim_a_out), .Addres_A_out(info_loada_1_addres_a_out));
  Info_loadB info_loadb_1 (
    .Dim_B_In(ins_splitter_1_dimension), .Add_B_In(ins_splitter_1_adress), .WE_B(comparator_5_eq),
    .Clock_B(clock_1_out), .Dim_B_out(info_loadb_1_dim_b_out), .Addres_B_out(info_loadb_1_addres_b_out));
  Info_mmult info_mmult_1 (
    .Dim_B_In(ins_splitter_1_dimension), .Add_B_In(ins_splitter_1_adress), .WE_M(comparator_7_eq),
    .Clock_M(clock_1_out), .Dim_Mmult(info_mmult_1_dim_mmult), .Addres_Mmult(info_mmult_1_addres_mmult));
  Info_stoC info_stoc_1 (
    .Dim_Store_In(ins_splitter_1_dimension), .Add_Store_In(ins_splitter_1_adress),
    .WE_Store(comparator_6_eq), .Clock_Store(clock_1_out), .Dim_Store_Out(info_stoc_1_dim_store_out),
    .Addres_Store_Out(info_stoc_1_addres_store_out));
  // Probe on info_loada_1_dim_a_out
  // Probe on info_loada_1_addres_a_out
  // Probe on info_loadb_1_dim_b_out
  // Probe on info_loadb_1_addres_b_out
  // Probe on info_mmult_1_dim_mmult
  // Probe on info_mmult_1_addres_mmult
  // Probe on info_stoc_1_dim_store_out
  // Probe on info_stoc_1_addres_store_out
  Comparator #(.width(4)) comparator_8 (.a(info_loada_1_dim_a_out), .b(4'b0010), .eq(comparator_8_eq));  // open: gt, lt
  Comparator #(.width(4)) comparator_9 (.a(info_loada_1_dim_a_out), .b(4'b0100), .eq(comparator_9_eq));  // open: gt, lt
  Comparator #(.width(4)) comparator_10 (
    .a(info_loada_1_dim_a_out), .b(4'b1000), .eq(comparator_10_eq));  // open: gt, lt
  Comparator #(.width(4)) comparator_11 (
    .a(info_loada_1_dim_a_out), .b(4'b1100), .eq(comparator_11_eq));  // open: gt, lt
  or or_1 (or_1_out, comparator_8_eq, comparator_9_eq);
  or or_2 (or_2_out, comparator_11_eq, comparator_10_eq, or_1_out);
  assign controlled_buffer_1_out = or_1_out ? 4'b0001 : 4'bz;  // Controlled_Buffer controlled_buffer_1
  Register #(.width(4)) Tile_Ammount (.D(controlled_buffer_1_out), .en(or_2_out), .clk(clock_1_out));  // open: Q, clr
  assign controlled_buffer_1_out = comparator_10_eq ? 4'b0100 : 4'bz;  // Controlled_Buffer controlled_buffer_2
  assign controlled_buffer_1_out = comparator_11_eq ? 4'b1001 : 4'bz;  // Controlled_Buffer controlled_buffer_3
endmodule

module Ins_Tiling_finals_v1 (
);

  wire clock_1_out, comparator_1_eq, comparator_2_eq, comparator_3_eq, comparator_4_eq, comparator_5_eq,
       comparator_5_gt, comparator_6_eq, comparator_7_eq, comparator_8_eq, counter_4_q, counter_5_q, or_1_out;
  wire [3:0] counter_3_q, ins_splitter_1_dimension, ins_splitter_1_opcode;
  wire [7:0] bit_extender_1_out, counter_1_q, counter_2_q, counter_6_q, counter_7_q, ins_splitter_1_adress,
       multiplier_1_out, subtractor_1_out;
  wire [15:0] controlled_buffer_1_out, decoder_custom_1_y1, InstructionRam_dout, RamA_dout, register_1_q,
       register_2_q, register_3_q, register_4_q, register_5_q, register_6_q, register_7_q, register_8_q,
       register_9_q, register_10_q, register_11_q, register_12_q, register_13_q, register_14_q,
       register_15_q, register_16_q, rom_1_data;

  Clock clock_1 (.out(clock_1_out));
  Counter counter_1 (
    .load(comparator_6_eq), .D(ins_splitter_1_adress), .count(comparator_7_eq), .Q(counter_1_q),
    .clk(clock_1_out));  // open: carry, up, clr
  Counter counter_2 (.count(comparator_5_eq), .Q(counter_2_q), .clk(clock_1_out));  // open: load, D, carry, up, clr
  RAM #(.dataWidth(16), .\type ("nonvolatile")) RamA (
    .addr(counter_1_q), .we(comparator_7_eq), .clk(clock_1_out), .dout(RamA_dout));  // open: oe, din
  RAM #(.dataWidth(16), .\type ("nonvolatile")) InstructionRam (
    .addr(counter_2_q), .clk(clock_1_out), .dout(InstructionRam_dout));  // open: we, oe, din
  // Probe on InstructionRam_dout
  // Probe on ins_splitter_1_adress
  Ins_splitter ins_splitter_1 (
    .Instruction(InstructionRam_dout), .WE(comparator_5_eq), .Clock(clock_1_out),
    .Adress(ins_splitter_1_adress), .Dimension(ins_splitter_1_dimension), .Opcode(ins_splitter_1_opcode));
  // Probe on ins_splitter_1_opcode
  Counter #(.max('hf), .width(4)) counter_3 (
    .count(comparator_7_eq), .Q(counter_3_q), .clk(clock_1_out));  // open: load, D, carry, up, clr
  assign bit_extender_1_out = {{4{ins_splitter_1_dimension[3]}}, ins_splitter_1_dimension};  // Bit_Extender bit_extender_1
  // Probe on ins_splitter_1_dimension
  // Probe on subtractor_1_out
  Subtractor subtractor_1 (.a(counter_1_q), .b(ins_splitter_1_adress), .out(subtractor_1_out));  // open: bin, bout
  // Probe on multiplier_1_out
  Multiplier multiplier_1 (.a(bit_extender_1_out), .b(bit_extender_1_out), .out(multiplier_1_out));  // open: cin, cout
  Comparator #(.width(4)) comparator_1 (.a(ins_splitter_1_opcode), .b(4'b0001), .eq(comparator_1_eq));  // open: gt, lt
  Comparator #(.width(4)) comparator_2 (.a(ins_splitter_1_opcode), .b(4'b0010), .eq(comparator_2_eq));  // open: gt, lt
  Comparator #(.width(4)) comparator_3 (.a(ins_splitter_1_opcode), .b(4'b0011), .eq(comparator_3_eq));  // open: gt, lt
  Comparator #(.width(4)) comparator_4 (.a(ins_splitter_1_opcode), .b(4'b0100), .eq(comparator_4_eq));  // open: gt, lt
  Comparator comparator_5 (
    .a(subtractor_1_out), .b(multiplier_1_out), .gt(comparator_5_gt), .eq(comparator_5_eq));  // open: lt
  Counter #(.max('h1), .ongoal("stay"), .width(1)) counter_4 (
    .count(comparator_1_eq), .Q(counter_4_q), .clk(clock_1_out), .clr(comparator_5_eq));  // open: load, D, carry, up
  Comparator #(.width(1)) comparator_6 (.a(1'b0), .b(counter_4_q), .eq(comparator_6_eq));  // open: gt, lt
  Comparator #(.width(1)) comparator_7 (.a(counter_4_q), .b(1'b1), .eq(comparator_7_eq));  // open: gt, lt
  decoder_custom decoder_custom_1 (
    .x1(counter_3_q[0]), .x2(counter_3_q[1]), .x3(counter_3_q[2]), .x4(counter_3_q[3]),
    .Enable(comparator_7_eq), .y1(decoder_custom_1_y1[0]), .y2(decoder_custom_1_y1[1]),
    .y3(decoder_custom_1_y1[2]), .y4(decoder_custom_1_y1[3]), .y5(decoder_custom_1_y1[4]),
    .y6(decoder_custom_1_y1[5]), .y7(decoder_custom_1_y1[6]), .y8(decoder_custom_1_y1[7]),
    .y9(decoder_custom_1_y1[8]), .y10(decoder_custom_1_y1[9]), .y11(decoder_custom_1_y1[10]),
    .y12(decoder_custom_1_y1[11]), .y13(decoder_custom_1_y1[12]), .y14(decoder_custom_1_y1[13]),
    .y15(decoder_custom_1_y1[14]), .y16(decoder_custom_1_y1[15]));
  Register #(.width(16)) register_1 (
    .D(RamA_dout), .en(decoder_custom_1_y1[0]), .clk(clock_1_out), .Q(register_1_q));  // open: clr
  Register #(.width(16)) register_2 (
    .D(RamA_dout), .en(decoder_custom_1_y1[1]), .clk(clock_1_out), .Q(register_2_q));  // open: clr
  Register #(.width(16)) register_3 (
    .D(RamA_dout), .en(decoder_custom_1_y1[2]), .clk(clock_1_out), .Q(register_3_q));  // open: clr
  Register #(.width(16)) register_4 (
    .D(RamA_dout), .en(decoder_custom_1_y1[3]), .clk(clock_1_out), .Q(register_4_q));  // open: clr
  assign controlled_buffer_1_out = rom_1_data[0] ? register_1_q : 16'bz;  // Controlled_Buffer controlled_buffer_1
  assign controlled_buffer_1_out = rom_1_data[1] ? register_2_q : 16'bz;  // Controlled_Buffer controlled_buffer_2
  assign controlled_buffer_1_out = rom_1_data[2] ? register_3_q : 16'bz;  // Controlled_Buffer controlled_buffer_3
  assign controlled_buffer_1_out = rom_1_data[3] ? register_4_q : 16'bz;  // Controlled_Buffer controlled_buffer_4
  Register #(.width(16)) register_5 (
    .D(RamA_dout), .en(decoder_custom_1_y1[4]), .clk(clock_1_out), .Q(register_5_q));  // open: clr
  Register #(.width(16)) register_6 (
    .D(RamA_dout), .en(decoder_custom_1_y1[5]), .clk(clock_1_out), .Q(register_6_q));  // open: clr
  Register #(.width(16)) register_7 (
    .D(RamA_dout), .en(decoder_custom_1_y1[6]), .clk(clock_1_out), .Q(register_7_q));  // open: clr
  Register #(.width(16)) register_8 (
    .D(RamA_dout), .en(decoder_custom_1_y1[7]), .clk(clock_1_out), .Q(register_8_q));  // open: clr
  assign controlled_buffer_1_out = rom_1_data[4] ? register_5_q : 16'bz;  // Controlled_Buffer controlled_buffer_5
  assign controlled_buffer_1_out = rom_1_data[5] ? register_6_q : 16'bz;  // Controlled_Buffer controlled_buffer_6
  assign controlled_buffer_1_out = rom_1_data[6] ? register_7_q : 16'bz;  // Controlled_Buffer controlled_buffer_7
  assign controlled_buffer_1_out = rom_1_data[7] ? register_8_q : 16'bz;  // Controlled_Buffer controlled_buffer_8
  Counter #(.max('h1), .width(1)) counter_5 (
    .count(comparator_5_gt), .Q(counter_5_q), .clk(clock_1_out));  // open: load, D, carry, up, clr
  Register #(.width(16)) register_9 (
    .D(RamA_dout), .en(decoder_custom_1_y1[8]), .clk(decoder_custom_1_y1[9]), .Q(register_9_q));  // open: clr
  Register #(.width(16)) register_10 (
    .D(RamA_dout), .en(decoder_custom_1_y1[9]), .clk(clock_1_out), .Q(register_10_q));  // open: clr
  Register #(.width(16)) register_11 (
    .D(RamA_dout), .en(decoder_custom_1_y1[10]), .clk(clock_1_out), .Q(register_11_q));  // open: clr
  Register #(.width(16)) register_12 (
    .D(RamA_dout), .en(decoder_custom_1_y1[11]), .clk(clock_1_out), .Q(register_12_q));  // open: clr
  Comparator comparator_8 (.a(8'h10), .b(counter_6_q), .eq(comparator_8_eq));  // open: gt, lt
  assign controlled_buffer_1_out = rom_1_data[8] ? register_9_q : 16'bz;  // Controlled_Buffer controlled_buffer_9
  assign controlled_buffer_1_out = rom_1_data[9] ? register_10_q : 16'bz;  // Controlled_Buffer controlled_buffer_10
  assign controlled_buffer_1_out = rom_1_data[10] ? register_11_q : 16'bz;  // Controlled_Buffer controlled_buffer_11
  assign controlled_buffer_1_out = rom_1_data[11] ? register_12_q : 16'bz;  // Controlled_Buffer controlled_buffer_12
  ROM #(.dataWidth(16)) rom_1 (.addr(counter_6_q), .data(rom_1_data));
  Counter counter_6 (
    .load(comparator_8_eq), .D(8'h1), .count(comparator_7_eq), .Q(counter_6_q), .clk(clock_1_out),
    .clr(counter_5_q));  // open: carry, up
  Register #(.width(16)) register_13 (
    .D(RamA_dout), .en(decoder_custom_1_y1[12]), .clk(clock_1_out), .Q(register_13_q));  // open: clr
  Register #(.width(16)) register_14 (
    .D(RamA_dout), .en(decoder_custom_1_y1[13]), .clk(clock_1_out), .Q(register_14_q));  // open: clr
  Register #(.width(16)) register_15 (
    .D(RamA_dout), .en(decoder_custom_1_y1[14]), .clk(clock_1_out), .Q(register_15_q));  // open: clr
  Register #(.width(16)) register_16 (
    .D(RamA_dout), .en(decoder_custom_1_y1[15]), .clk(clock_1_out), .Q(register_16_q));  // open: clr
  assign controlled_buffer_1_out = rom_1_data[12] ? register_13_q : 16'bz;  // Controlled_Buffer controlled_buffer_13
  assign controlled_buffer_1_out = rom_1_data[13] ? register_14_q : 16'bz;  // Controlled_Buffer controlled_buffer_14
  assign controlled_buffer_1_out = rom_1_data[14] ? register_15_q : 16'bz;  // Controlled_Buffer controlled_buffer_15
  assign controlled_buffer_1_out = rom_1_data[15] ? register_16_q : 16'bz;  // Controlled_Buffer controlled_buffer_16
  RAM #(.dataWidth(16)) Cache1 (
    .addr(counter_7_q), .we(or_1_out), .clk(clock_1_out), .din(controlled_buffer_1_out));  // open: oe, dout
  Counter counter_7 (.count(or_1_out), .Q(counter_7_q), .clk(clock_1_out));  // open: load, D, carry, up, clr
  or or_1 (or_1_out, rom_1_data[15], rom_1_data[14], rom_1_data[13], rom_1_data[12], rom_1_data[11], rom_1_data[10], rom_1_data[9], rom_1_data[8], rom_1_data[7], rom_1_data[6], rom_1_data[5], rom_1_data[4], rom_1_data[3], rom_1_data[2], rom_1_data[1], rom_1_data[0]);

  // Notes on the sheet:
  //   contents of rom_1 (hex, n*v repeats v):
  //   0 1 2 4 8 10 20 40 80 100 200 400 800 1000 2000 4000 8000
endmodule

module Ins_Systrolic_v1 (
);

  wire clock_1_out, nor_1_out, or_1_out, or_2_out, or_3_out;
  wire [7:0] counter_1_q, instructiondecoder_dep_1_counter_a, instructiondecoder_dep_1_counter_b,
       instructiondecoder_dep_1_counter_c, instructiondecoder_dep_1_counter_rom;
  wire [15:0] controlled_buffer_1_out, controlled_buffer_2_out, controlled_buffer_3_out,
       controlled_buffer_4_out, controlled_buffer_5_out, controlled_buffer_6_out, controlled_buffer_7_out,
       controlled_buffer_11_out, controlled_buffer_33_out, ram_1_dout, RamA_dout, RamB_dout, register_1_q,
       registerbanks_16_1_r1, registerbanks_16_1_r2, registerbanks_16_1_r3, registerbanks_16_1_r4,
       registerbanks_16_1_r5, registerbanks_16_1_r6, registerbanks_16_1_r7, registerbanks_16_1_r8,
       registerbanks_16_1_r9, registerbanks_16_1_r10, registerbanks_16_1_r11, registerbanks_16_1_r12,
       registerbanks_16_1_r13, registerbanks_16_1_r14, registerbanks_16_1_r15, registerbanks_16_1_r16,
       registerbanks_16_2_r1, registerbanks_16_2_r2, registerbanks_16_2_r3, registerbanks_16_2_r4,
       registerbanks_16_2_r5, registerbanks_16_2_r6, registerbanks_16_2_r7, registerbanks_16_2_r8,
       registerbanks_16_2_r9, registerbanks_16_2_r10, registerbanks_16_2_r11, registerbanks_16_2_r12,
       registerbanks_16_2_r13, registerbanks_16_2_r14, registerbanks_16_2_r15, registerbanks_16_2_r16,
       systrolic_4x4gausian_1_c1, systrolic_4x4gausian_1_c2, systrolic_4x4gausian_1_c3,
       systrolic_4x4gausian_1_c4, systrolic_4x4gausian_1_c5, systrolic_4x4gausian_1_c6,
       systrolic_4x4gausian_1_c7, systrolic_4x4gausian_1_c8, systrolic_4x4gausian_1_c9,
       systrolic_4x4gausian_1_c10, systrolic_4x4gausian_1_c11, systrolic_4x4gausian_1_c12,
       systrolic_4x4gausian_1_c13, systrolic_4x4gausian_1_c14, systrolic_4x4gausian_1_c15,
       systrolic_4x4gausian_1_c16;
  wire [63:0] rom_1_data;

  Clock clock_1 (.out(clock_1_out));
  RAM #(.dataWidth(16)) RamB (
    .addr(instructiondecoder_dep_1_counter_b), .clk(clock_1_out), .dout(RamB_dout));  // open: we, oe, din
  RAM #(.dataWidth(16)) RamA (
    .addr(instructiondecoder_dep_1_counter_a), .clk(clock_1_out), .dout(RamA_dout));  // open: we, oe, din
  or or_1 (or_1_out, rom_1_data[48], rom_1_data[49], rom_1_data[50], rom_1_data[51], rom_1_data[52], rom_1_data[53], rom_1_data[54], rom_1_data[55], rom_1_data[56], rom_1_data[57], rom_1_data[58], rom_1_data[59], rom_1_data[60], rom_1_data[61], rom_1_data[62], rom_1_data[63]);
  or or_2 (or_2_out, rom_1_data[47], rom_1_data[46], rom_1_data[45], rom_1_data[44], rom_1_data[43], rom_1_data[42], rom_1_data[41], rom_1_data[40], rom_1_data[39], rom_1_data[38], rom_1_data[37], rom_1_data[36], rom_1_data[35], rom_1_data[34], rom_1_data[33], rom_1_data[32]);
  registerBanks_16 registerbanks_16_1 (
    .Value(RamB_dout), .WE1(rom_1_data[63]), .WE2(rom_1_data[62]), .WE3(rom_1_data[61]),
    .WE4(rom_1_data[60]), .WE5(rom_1_data[59]), .WE6(rom_1_data[58]), .WE7(rom_1_data[57]),
    .WE8(rom_1_data[56]), .WE9(rom_1_data[55]), .WE10(rom_1_data[54]), .WE11(rom_1_data[53]),
    .WE12(rom_1_data[52]), .WE13(rom_1_data[51]), .WE14(rom_1_data[50]), .WE15(rom_1_data[49]),
    .WE16(rom_1_data[48]), .clock(clock_1_out), .R1(registerbanks_16_1_r1), .R2(registerbanks_16_1_r2),
    .R3(registerbanks_16_1_r3), .R4(registerbanks_16_1_r4), .R5(registerbanks_16_1_r5),
    .R6(registerbanks_16_1_r6), .R7(registerbanks_16_1_r7), .R8(registerbanks_16_1_r8),
    .R9(registerbanks_16_1_r9), .R10(registerbanks_16_1_r10), .R11(registerbanks_16_1_r11),
    .R12(registerbanks_16_1_r12), .R13(registerbanks_16_1_r13), .R14(registerbanks_16_1_r14),
    .R15(registerbanks_16_1_r15), .R16(registerbanks_16_1_r16));
  registerBanks_16 registerbanks_16_2 (
    .Value(RamA_dout), .WE1(rom_1_data[47]), .WE2(rom_1_data[46]), .WE3(rom_1_data[45]),
    .WE4(rom_1_data[44]), .WE5(rom_1_data[43]), .WE6(rom_1_data[42]), .WE7(rom_1_data[41]),
    .WE8(rom_1_data[40]), .WE9(rom_1_data[39]), .WE10(rom_1_data[38]), .WE11(rom_1_data[37]),
    .WE12(rom_1_data[36]), .WE13(rom_1_data[35]), .WE14(rom_1_data[34]), .WE15(rom_1_data[33]),
    .WE16(rom_1_data[32]), .clock(clock_1_out), .R1(registerbanks_16_2_r1), .R2(registerbanks_16_2_r2),
    .R3(registerbanks_16_2_r3), .R4(registerbanks_16_2_r4), .R5(registerbanks_16_2_r5),
    .R6(registerbanks_16_2_r6), .R7(registerbanks_16_2_r7), .R8(registerbanks_16_2_r8),
    .R9(registerbanks_16_2_r9), .R10(registerbanks_16_2_r10), .R11(registerbanks_16_2_r11),
    .R12(registerbanks_16_2_r12), .R13(registerbanks_16_2_r13), .R14(registerbanks_16_2_r14),
    .R15(registerbanks_16_2_r15), .R16(registerbanks_16_2_r16));
  assign controlled_buffer_1_out = rom_1_data[31] ? registerbanks_16_1_r1 : 16'bz;  // Controlled_Buffer controlled_buffer_1
  assign controlled_buffer_2_out = rom_1_data[30] ? registerbanks_16_1_r2 : 16'bz;  // Controlled_Buffer controlled_buffer_2
  assign controlled_buffer_3_out = rom_1_data[29] ? registerbanks_16_1_r3 : 16'bz;  // Controlled_Buffer controlled_buffer_3
  assign controlled_buffer_4_out = rom_1_data[31] ? registerbanks_16_2_r1 : 16'bz;  // Controlled_Buffer controlled_buffer_4
  assign controlled_buffer_5_out = rom_1_data[30] ? registerbanks_16_2_r2 : 16'bz;  // Controlled_Buffer controlled_buffer_5
  assign controlled_buffer_6_out = rom_1_data[29] ? registerbanks_16_2_r3 : 16'bz;  // Controlled_Buffer controlled_buffer_6
  assign controlled_buffer_7_out = rom_1_data[28] ? registerbanks_16_1_r4 : 16'bz;  // Controlled_Buffer controlled_buffer_7
  assign controlled_buffer_1_out = rom_1_data[27] ? registerbanks_16_1_r5 : 16'bz;  // Controlled_Buffer controlled_buffer_8
  assign controlled_buffer_2_out = rom_1_data[26] ? registerbanks_16_1_r6 : 16'bz;  // Controlled_Buffer controlled_buffer_9
  assign controlled_buffer_3_out = rom_1_data[25] ? registerbanks_16_1_r7 : 16'bz;  // Controlled_Buffer controlled_buffer_10
  assign controlled_buffer_11_out = rom_1_data[28] ? registerbanks_16_2_r4 : 16'bz;  // Controlled_Buffer controlled_buffer_11
  assign controlled_buffer_4_out = rom_1_data[27] ? registerbanks_16_2_r5 : 16'bz;  // Controlled_Buffer controlled_buffer_12
  assign controlled_buffer_5_out = rom_1_data[26] ? registerbanks_16_2_r6 : 16'bz;  // Controlled_Buffer controlled_buffer_13
  assign controlled_buffer_6_out = rom_1_data[25] ? registerbanks_16_2_r7 : 16'bz;  // Controlled_Buffer controlled_buffer_14
  assign controlled_buffer_7_out = rom_1_data[24] ? registerbanks_16_1_r8 : 16'bz;  // Controlled_Buffer controlled_buffer_15
  assign controlled_buffer_1_out = rom_1_data[23] ? registerbanks_16_1_r9 : 16'bz;  // Controlled_Buffer controlled_buffer_16
  assign controlled_buffer_2_out = rom_1_data[22] ? registerbanks_16_1_r10 : 16'bz;  // Controlled_Buffer controlled_buffer_17
  assign controlled_buffer_3_out = rom_1_data[21] ? registerbanks_16_1_r11 : 16'bz;  // Controlled_Buffer controlled_buffer_18
  assign controlled_buffer_11_out = rom_1_data[24] ? registerbanks_16_2_r8 : 16'bz;  // Controlled_Buffer controlled_buffer_19
  assign controlled_buffer_4_out = rom_1_data[23] ? registerbanks_16_2_r9 : 16'bz;  // Controlled_Buffer controlled_buffer_20
  assign controlled_buffer_5_out = rom_1_data[22] ? registerbanks_16_2_r10 : 16'bz;  // Controlled_Buffer controlled_buffer_21
  assign controlled_buffer_6_out = rom_1_data[21] ? registerbanks_16_2_r11 : 16'bz;  // Controlled_Buffer controlled_buffer_22
  assign controlled_buffer_7_out = rom_1_data[20] ? registerbanks_16_1_r12 : 16'bz;  // Controlled_Buffer controlled_buffer_23
  assign controlled_buffer_1_out = rom_1_data[19] ? registerbanks_16_1_r13 : 16'bz;  // Controlled_Buffer controlled_buffer_24
  assign controlled_buffer_2_out = rom_1_data[18] ? registerbanks_16_1_r14 : 16'bz;  // Controlled_Buffer controlled_buffer_25
  assign controlled_buffer_3_out = rom_1_data[17] ? registerbanks_16_1_r15 : 16'bz;  // Controlled_Buffer controlled_buffer_26
  assign controlled_buffer_11_out = rom_1_data[20] ? registerbanks_16_2_r12 : 16'bz;  // Controlled_Buffer controlled_buffer_27
  assign controlled_buffer_4_out = rom_1_data[19] ? registerbanks_16_2_r13 : 16'bz;  // Controlled_Buffer controlled_buffer_28
  assign controlled_buffer_5_out = rom_1_data[18] ? registerbanks_16_2_r14 : 16'bz;  // Controlled_Buffer controlled_buffer_29
  assign controlled_buffer_6_out = rom_1_data[17] ? registerbanks_16_2_r15 : 16'bz;  // Controlled_Buffer controlled_buffer_30
  assign controlled_buffer_7_out = rom_1_data[16] ? registerbanks_16_1_r16 : 16'bz;  // Controlled_Buffer controlled_buffer_31
  assign controlled_buffer_11_out = rom_1_data[16] ? registerbanks_16_2_r16 : 16'bz;  // Controlled_Buffer controlled_buffer_32
  Counter counter_1 (.Q(counter_1_q), .clk(clock_1_out));  // open: load, D, count, carry, up, clr
  RAM #(.dataWidth(16), .\type ("nonvolatile")) ram_1 (
    .addr(counter_1_q), .clk(clock_1_out), .dout(ram_1_dout));  // open: we, oe, din
  assign controlled_buffer_33_out = rom_1_data[15] ? systrolic_4x4gausian_1_c1 : 16'bz;  // Controlled_Buffer controlled_buffer_33
  systrolic_4x4Gausian systrolic_4x4gausian_1 (
    .B1(controlled_buffer_1_out), .B2(controlled_buffer_2_out), .B3(controlled_buffer_3_out),
    .B4(controlled_buffer_7_out), .A1(controlled_buffer_4_out), .A2(controlled_buffer_5_out),
    .A3(controlled_buffer_6_out), .A4(controlled_buffer_11_out), .Clock(clock_1_out),
    .C1(systrolic_4x4gausian_1_c1), .C2(systrolic_4x4gausian_1_c2), .C3(systrolic_4x4gausian_1_c3),
    .C4(systrolic_4x4gausian_1_c4), .C5(systrolic_4x4gausian_1_c5), .C6(systrolic_4x4gausian_1_c6),
    .C7(systrolic_4x4gausian_1_c7), .C8(systrolic_4x4gausian_1_c8), .C9(systrolic_4x4gausian_1_c9),
    .C10(systrolic_4x4gausian_1_c10), .C11(systrolic_4x4gausian_1_c11), .C12(systrolic_4x4gausian_1_c12),
    .C13(systrolic_4x4gausian_1_c13), .C14(systrolic_4x4gausian_1_c14), .C15(systrolic_4x4gausian_1_c15),
    .C16(systrolic_4x4gausian_1_c16));
  assign controlled_buffer_33_out = rom_1_data[14] ? systrolic_4x4gausian_1_c2 : 16'bz;  // Controlled_Buffer controlled_buffer_34
  assign controlled_buffer_33_out = rom_1_data[13] ? systrolic_4x4gausian_1_c3 : 16'bz;  // Controlled_Buffer controlled_buffer_35
  assign controlled_buffer_33_out = rom_1_data[12] ? systrolic_4x4gausian_1_c4 : 16'bz;  // Controlled_Buffer controlled_buffer_36
  assign controlled_buffer_33_out = rom_1_data[11] ? systrolic_4x4gausian_1_c5 : 16'bz;  // Controlled_Buffer controlled_buffer_37
  assign controlled_buffer_33_out = rom_1_data[10] ? systrolic_4x4gausian_1_c6 : 16'bz;  // Controlled_Buffer controlled_buffer_38
  assign controlled_buffer_33_out = rom_1_data[9] ? systrolic_4x4gausian_1_c7 : 16'bz;  // Controlled_Buffer controlled_buffer_39
  assign controlled_buffer_33_out = rom_1_data[8] ? systrolic_4x4gausian_1_c8 : 16'bz;  // Controlled_Buffer controlled_buffer_40
  assign controlled_buffer_33_out = rom_1_data[7] ? systrolic_4x4gausian_1_c9 : 16'bz;  // Controlled_Buffer controlled_buffer_41
  assign controlled_buffer_33_out = rom_1_data[6] ? systrolic_4x4gausian_1_c10 : 16'bz;  // Controlled_Buffer controlled_buffer_42
  assign controlled_buffer_33_out = rom_1_data[5] ? systrolic_4x4gausian_1_c11 : 16'bz;  // Controlled_Buffer controlled_buffer_43
  assign controlled_buffer_33_out = rom_1_data[4] ? systrolic_4x4gausian_1_c12 : 16'bz;  // Controlled_Buffer controlled_buffer_44
  assign controlled_buffer_33_out = rom_1_data[3] ? systrolic_4x4gausian_1_c13 : 16'bz;  // Controlled_Buffer controlled_buffer_45
  assign controlled_buffer_33_out = rom_1_data[2] ? systrolic_4x4gausian_1_c14 : 16'bz;  // Controlled_Buffer controlled_buffer_46
  assign controlled_buffer_33_out = rom_1_data[1] ? systrolic_4x4gausian_1_c15 : 16'bz;  // Controlled_Buffer controlled_buffer_47
  assign controlled_buffer_33_out = rom_1_data[0] ? systrolic_4x4gausian_1_c16 : 16'bz;  // Controlled_Buffer controlled_buffer_48
  InstructionDecoder_dep instructiondecoder_dep_1 (
    .Instruction(ram_1_dout), .Nor_Global(nor_1_out), .clock(clock_1_out), .Or_A(or_1_out), .Or_B(or_2_out),
    .StoC_Line(or_3_out), .Counter_A(instructiondecoder_dep_1_counter_a),
    .Counter_B(instructiondecoder_dep_1_counter_b), .Counter_C(instructiondecoder_dep_1_counter_c),
    .Counter_Rom(instructiondecoder_dep_1_counter_rom));  // open: Reset_Line
  Register #(.width(16)) register_1 (
    .D(controlled_buffer_33_out), .en(or_3_out), .clk(clock_1_out), .Q(register_1_q));  // open: clr
  RAM #(.dataWidth(16)) ram_2 (
    .addr(instructiondecoder_dep_1_counter_c), .we(or_3_out), .clk(clock_1_out), .din(register_1_q));  // open: oe, dout
  ROM #(.dataWidth(64)) rom_1 (.addr(instructiondecoder_dep_1_counter_rom), .data(rom_1_data));
  or or_3 (or_3_out, rom_1_data[0], rom_1_data[1], rom_1_data[2], rom_1_data[3], rom_1_data[4], rom_1_data[5], rom_1_data[6], rom_1_data[7], rom_1_data[8], rom_1_data[9], rom_1_data[10], rom_1_data[11], rom_1_data[12], rom_1_data[13], rom_1_data[14], rom_1_data[15]);
  nor nor_1 (nor_1_out, rom_1_data[63], rom_1_data[62], rom_1_data[61], rom_1_data[60], rom_1_data[59], rom_1_data[58], rom_1_data[57], rom_1_data[56], rom_1_data[55], rom_1_data[54], rom_1_data[53], rom_1_data[52], rom_1_data[51], rom_1_data[50], rom_1_data[49], rom_1_data[48], rom_1_data[47], rom_1_data[46], rom_1_data[45], rom_1_data[44], rom_1_data[43], rom_1_data[42], rom_1_data[41], rom_1_data[40], rom_1_data[39], rom_1_data[38], rom_1_data[37], rom_1_data[36], rom_1_data[35], rom_1_data[34], rom_1_data[33], rom_1_data[32], rom_1_data[31], rom_1_data[30], rom_1_data[29], rom_1_data[28], rom_1_data[27], rom_1_data[26], rom_1_data[25], rom_1_data[24], rom_1_data[23], rom_1_data[22], rom_1_data[21], rom_1_data[20], rom_1_data[19], rom_1_data[18], rom_1_data[17], rom_1_data[16], rom_1_data[15], rom_1_data[14], rom_1_data[13], rom_1_data[12], rom_1_data[11], rom_1_data[10], rom_1_data[9], rom_1_data[8], rom_1_data[7], rom_1_data[6], rom_1_data[5], rom_1_data[4], rom_1_data[3], rom_1_data[2], rom_1_data[1], rom_1_data[0]);
endmodule

module Ins_Gausian_v4 (
);

  wire clock_1_out, nor_1_out, or_1_out, or_2_out;
  wire [7:0] counter_1_q, counter_2_q, instructiondecoder_dep_1_counter_a,
       instructiondecoder_dep_1_counter_b, instructiondecoder_dep_1_counter_c,
       instructiondecoder_dep_1_counter_rom;
  wire [15:0] matmult_4x4_1_element, ram_1_dout, ram_2_dout, ram_3_dout, register_1_q,
       registerbanks_4_1_out1, registerbanks_4_1_out2, registerbanks_4_1_out3, registerbanks_4_1_out4,
       registerbanks_4_2_out1, registerbanks_4_2_out2, registerbanks_4_2_out3, registerbanks_4_2_out4,
       rom_1_data;

  Counter counter_1 (.count(nor_1_out), .Q(counter_1_q), .clk(clock_1_out));  // open: load, D, carry, up, clr
  RAM #(.dataWidth(16), .\type ("nonvolatile")) ram_1 (
    .addr(counter_1_q), .clk(clock_1_out), .dout(ram_1_dout));  // open: we, oe, din
  Clock clock_1 (.out(clock_1_out));
  Counter counter_2 (.Q(counter_2_q), .clk(clock_1_out));  // open: load, D, count, carry, up, clr
  Hex_Digit_Display hex_digit_display_1 (.value(counter_2_q[7:4]));  // open: dp
  Hex_Digit_Display hex_digit_display_2 (.value(counter_2_q[3:0]));  // open: dp
  InstructionDecoder_dep instructiondecoder_dep_1 (
    .Instruction(ram_1_dout), .Nor_Global(nor_1_out), .clock(clock_1_out), .Or_A(or_1_out), .Or_B(or_2_out),
    .StoC_Line(rom_1_data[6]), .Reset_Line(rom_1_data[0]), .Counter_A(instructiondecoder_dep_1_counter_a),
    .Counter_B(instructiondecoder_dep_1_counter_b), .Counter_C(instructiondecoder_dep_1_counter_c),
    .Counter_Rom(instructiondecoder_dep_1_counter_rom));
  RAM #(.dataWidth(16), .\type ("nonvolatile")) ram_2 (
    .addr(instructiondecoder_dep_1_counter_a), .clk(clock_1_out), .dout(ram_2_dout));  // open: we, oe, din
  RAM #(.dataWidth(16), .\type ("nonvolatile")) ram_3 (
    .addr(instructiondecoder_dep_1_counter_b), .clk(clock_1_out), .dout(ram_3_dout));  // open: we, oe, din
  nor nor_1 (nor_1_out, rom_1_data[6], rom_1_data[7], rom_1_data[8], rom_1_data[9], rom_1_data[10], rom_1_data[11], rom_1_data[12], rom_1_data[13], rom_1_data[14], rom_1_data[15]);
  or or_1 (or_1_out, rom_1_data[15], rom_1_data[14], rom_1_data[13], rom_1_data[12]);
  or or_2 (or_2_out, rom_1_data[11], rom_1_data[10], rom_1_data[9], rom_1_data[8]);
  registerBanks_4 registerbanks_4_1 (
    .value(ram_2_dout), .WE1(rom_1_data[15]), .WE2(rom_1_data[14]), .WE3(rom_1_data[13]),
    .WE4(rom_1_data[12]), .clock(clock_1_out), .out1(registerbanks_4_1_out1), .out2(registerbanks_4_1_out2),
    .out3(registerbanks_4_1_out3), .out4(registerbanks_4_1_out4));  // open: reset
  registerBanks_4 registerbanks_4_2 (
    .value(ram_3_dout), .WE1(rom_1_data[11]), .WE2(rom_1_data[10]), .WE3(rom_1_data[9]), .WE4(rom_1_data[8]),
    .clock(clock_1_out), .out1(registerbanks_4_2_out1), .out2(registerbanks_4_2_out2),
    .out3(registerbanks_4_2_out3), .out4(registerbanks_4_2_out4));  // open: reset
  ROM #(.dataWidth(16)) rom_1 (.addr(instructiondecoder_dep_1_counter_rom), .data(rom_1_data));
  Register #(.width(16)) register_1 (
    .D(matmult_4x4_1_element), .en(rom_1_data[7]), .clk(clock_1_out), .Q(register_1_q));  // open: clr
  matMult_4x4 matmult_4x4_1 (
    .row1(registerbanks_4_1_out1), .row2(registerbanks_4_1_out2), .row3(registerbanks_4_1_out3),
    .row4(registerbanks_4_1_out4), .col1(registerbanks_4_2_out1), .col2(registerbanks_4_2_out2),
    .col3(registerbanks_4_2_out3), .col4(registerbanks_4_2_out4), .Element(matmult_4x4_1_element));  // open: carryout
  RAM #(.dataWidth(16)) ram_4 (
    .addr(instructiondecoder_dep_1_counter_c), .we(rom_1_data[6]), .clk(clock_1_out), .din(register_1_q));  // open: oe, dout

  // Notes on the sheet:
  //   contents of rom_1 (hex, n*v repeats v):
  //   16*0 8000 4000 2000 1000 12*0 800 400 200 100 12*0 80 15*0 40
endmodule

module Ins_Gausian_v3 (
);

  wire clock_1_out, comparator_1_gt, nor_1_out, not_1_out, not_2_out, not_3_out, or_1_out, or_2_out, or_3_out;
  wire [3:0] ins_splitter_1_dimension, ins_splitter_1_opcode;
  wire [7:0] adder_1_out, bit_extender_1_out, bit_extender_2_out, counter_1_q, counter_2_q, counter_3_q,
       counter_4_q, counter_5_q, ins_splitter_1_adress, multiplier_1_out;
  wire [15:0] matmult_4x4_1_element, ram_1_dout, ram_2_dout, ram_3_dout, register_1_q,
       registerbanks_4_1_out1, registerbanks_4_1_out2, registerbanks_4_1_out3, registerbanks_4_1_out4,
       registerbanks_4_2_out1, registerbanks_4_2_out2, registerbanks_4_2_out3, registerbanks_4_2_out4,
       rom_1_data;

  Clock clock_1 (.out(clock_1_out));
  Counter counter_1 (.count(nor_1_out), .Q(counter_1_q), .clk(clock_1_out));  // open: load, D, carry, up, clr
  RAM #(.dataWidth(16), .\type ("nonvolatile")) ram_1 (
    .addr(counter_1_q), .clk(clock_1_out), .dout(ram_1_dout));  // open: we, oe, din
  // Probe on ram_1_dout
  // Probe on ins_splitter_1_adress
  Ins_splitter ins_splitter_1 (
    .Instruction(ram_1_dout), .WE(nor_1_out), .Clock(clock_1_out), .Adress(ins_splitter_1_adress),
    .Dimension(ins_splitter_1_dimension), .Opcode(ins_splitter_1_opcode));
  nor nor_1 (nor_1_out, rom_1_data[6], rom_1_data[7], rom_1_data[8], rom_1_data[9], rom_1_data[10], rom_1_data[11], rom_1_data[12], rom_1_data[13], rom_1_data[14], rom_1_data[15]);
  // Probe on ins_splitter_1_opcode
  // Probe on ins_splitter_1_dimension
  not not_1 (not_1_out, or_1_out);
  not not_2 (not_2_out, or_2_out);
  RAM #(.dataWidth(16), .\type ("nonvolatile")) ram_2 (
    .addr(counter_2_q), .clk(clock_1_out), .dout(ram_2_dout));  // open: we, oe, din
  Counter counter_2 (
    .load(not_1_out), .D(ins_splitter_1_adress), .count(or_1_out), .Q(counter_2_q), .clk(clock_1_out));  // open: carry, up, clr
  Counter counter_3 (
    .load(not_2_out), .D(ins_splitter_1_adress), .count(or_2_out), .Q(counter_3_q), .clk(clock_1_out));  // open: carry, up, clr
  or or_1 (or_1_out, rom_1_data[15], rom_1_data[14], rom_1_data[13], rom_1_data[12]);
  RAM #(.dataWidth(16), .\type ("nonvolatile")) ram_3 (
    .addr(counter_3_q), .clk(clock_1_out), .dout(ram_3_dout));  // open: we, oe, din
  or or_2 (or_2_out, rom_1_data[11], rom_1_data[10], rom_1_data[9], rom_1_data[8]);
  assign bit_extender_1_out = {{4{ins_splitter_1_dimension[3]}}, ins_splitter_1_dimension};  // Bit_Extender bit_extender_1
  registerBanks_4 registerbanks_4_1 (
    .value(ram_2_dout), .WE1(rom_1_data[15]), .WE2(rom_1_data[14]), .WE3(rom_1_data[13]),
    .WE4(rom_1_data[12]), .clock(clock_1_out), .out1(registerbanks_4_1_out1), .out2(registerbanks_4_1_out2),
    .out3(registerbanks_4_1_out3), .out4(registerbanks_4_1_out4));  // open: reset
  registerBanks_4 registerbanks_4_2 (
    .value(ram_3_dout), .WE1(rom_1_data[11]), .WE2(rom_1_data[10]), .WE3(rom_1_data[9]), .WE4(rom_1_data[8]),
    .clock(clock_1_out), .out1(registerbanks_4_2_out1), .out2(registerbanks_4_2_out2),
    .out3(registerbanks_4_2_out3), .out4(registerbanks_4_2_out4));  // open: reset
  assign bit_extender_2_out = {{4{ins_splitter_1_opcode[3]}}, ins_splitter_1_opcode};  // Bit_Extender bit_extender_2
  Comparator comparator_1 (.a(counter_4_q), .b(bit_extender_1_out), .gt(comparator_1_gt));  // open: eq, lt
  Multiplier multiplier_1 (.a(bit_extender_2_out), .b(8'h10), .out(multiplier_1_out));  // open: cin, cout
  Counter counter_4 (
    .D({8{1'b1}}), .Q(counter_4_q), .clk(clock_1_out), .clr(or_3_out));  // open: load, count, carry, up
  or or_3 (or_3_out, comparator_1_gt, rom_1_data[0]);
  Adder adder_1 (.a(multiplier_1_out), .b(counter_4_q), .out(adder_1_out));  // open: cin, cout
  ROM #(.dataWidth(16)) rom_1 (.addr(adder_1_out), .data(rom_1_data));
  Register #(.width(16)) register_1 (
    .D(matmult_4x4_1_element), .en(rom_1_data[7]), .clk(clock_1_out), .Q(register_1_q));  // open: clr
  matMult_4x4 matmult_4x4_1 (
    .row1(registerbanks_4_1_out1), .row2(registerbanks_4_1_out2), .row3(registerbanks_4_1_out3),
    .row4(registerbanks_4_1_out4), .col1(registerbanks_4_2_out1), .col2(registerbanks_4_2_out2),
    .col3(registerbanks_4_2_out3), .col4(registerbanks_4_2_out4), .Element(matmult_4x4_1_element));  // open: carryout
  not not_3 (not_3_out, rom_1_data[6]);
  RAM #(.dataWidth(16)) ram_4 (
    .addr(counter_5_q), .we(rom_1_data[6]), .clk(clock_1_out), .din(register_1_q));  // open: oe, dout
  Counter counter_5 (
    .load(not_3_out), .D(ins_splitter_1_adress), .Q(counter_5_q), .clk(clock_1_out));  // open: count, carry, up, clr

  // Notes on the sheet:
  //   contents of rom_1 (hex, n*v repeats v):
  //   16*0 8000 4000 2000 1000 12*0 800 400 200 100 12*0 80 15*0 40
endmodule

module Ins_Gausian_v2 (
);

  wire clock_1_out, not_1_out, not_2_out, or_1_out, or_2_out, or_3_out, or_4_out, Reset_q;
  wire [7:0] adder_1_out, bit_extender_1_out, counter_1_q, counter_2_q, counter_3_q, counter_4_q,
       counter_5_q, InstrucRam_data, multiplier_1_out, subtractor_1_out;
  wire [15:0] matmult_4x4_1_element, PCU_data, RamA_dout, RamB_dout, register_1_q, registerbanks_4_1_out1,
       registerbanks_4_1_out2, registerbanks_4_1_out3, registerbanks_4_1_out4, registerbanks_4_2_out1,
       registerbanks_4_2_out2, registerbanks_4_2_out3, registerbanks_4_2_out4;
  wire [15:8] InstrucRam_data_2;

  Clock clock_1 (.out(clock_1_out));
  not not_1 (not_1_out, or_4_out);
  not not_2 (not_2_out, or_4_out);
  Counter counter_1 (.count(not_1_out), .Q(counter_1_q), .clk(clock_1_out));  // open: load, D, carry, up, clr
  ROM #(.dataWidth(16)) InstrucRam (.addr(counter_1_q), .data({InstrucRam_data_2, InstrucRam_data}));
  or or_1 (or_1_out, PCU_data[7], PCU_data[6], PCU_data[5], PCU_data[4]);
  or or_2 (or_2_out, PCU_data[0], PCU_data[1], PCU_data[2], PCU_data[3]);
  Counter counter_2 (
    .load(not_2_out), .D(subtractor_1_out), .count(or_2_out), .Q(counter_2_q), .clk(clock_1_out));  // open: carry, up, clr
  Counter counter_3 (
    .load(not_2_out), .D(subtractor_1_out), .count(or_1_out), .Q(counter_3_q), .clk(clock_1_out));  // open: carry, up, clr
  Subtractor subtractor_1 (.a(8'h1), .b(InstrucRam_data), .out(subtractor_1_out));  // open: bin, bout
  RAM #(.dataWidth(16), .\type ("nonvolatile")) RamA (
    .addr(counter_2_q), .clk(clock_1_out), .dout(RamA_dout));  // open: we, oe, din
  RAM #(.dataWidth(16), .\type ("nonvolatile")) RamB (
    .addr(counter_3_q), .clk(clock_1_out), .dout(RamB_dout));  // open: we, oe, din
  assign bit_extender_1_out = {{4{InstrucRam_data_2[15]}}, InstrucRam_data_2[15:12]};  // Bit_Extender bit_extender_1
  or or_3 (or_3_out, InstrucRam_data_2[12], InstrucRam_data_2[13], InstrucRam_data_2[14], InstrucRam_data_2[15]);
  Multiplier multiplier_1 (.a(bit_extender_1_out), .b(8'h10), .out(multiplier_1_out));  // open: cin, cout
  Counter counter_4 (.count(or_3_out), .Q(counter_4_q), .clk(clock_1_out), .clr(Reset_q));  // open: load, D, carry, up
  Adder adder_1 (.a(multiplier_1_out), .b(counter_4_q), .out(adder_1_out));  // open: cin, cout
  ROM #(.dataWidth(16)) PCU (.addr(adder_1_out), .data(PCU_data));
  Register #(.width(1)) Reset (.D(PCU_data[15]), .en(clock_1_out), .clk(clock_1_out), .Q(Reset_q));  // open: clr
  or or_4 (or_4_out, PCU_data[0], PCU_data[1], PCU_data[2], PCU_data[3], PCU_data[4], PCU_data[5], PCU_data[6], PCU_data[7], PCU_data[8], PCU_data[9], PCU_data[10], PCU_data[11]);
  registerBanks_4 registerbanks_4_1 (
    .value(RamA_dout), .WE1(PCU_data[0]), .WE2(PCU_data[1]), .WE3(PCU_data[2]), .WE4(PCU_data[3]),
    .clock(clock_1_out), .out1(registerbanks_4_1_out1), .out2(registerbanks_4_1_out2),
    .out3(registerbanks_4_1_out3), .out4(registerbanks_4_1_out4));  // open: reset
  registerBanks_4 registerbanks_4_2 (
    .value(RamB_dout), .WE1(PCU_data[4]), .WE2(PCU_data[5]), .WE3(PCU_data[6]), .WE4(PCU_data[7]),
    .clock(clock_1_out), .out1(registerbanks_4_2_out1), .out2(registerbanks_4_2_out2),
    .out3(registerbanks_4_2_out3), .out4(registerbanks_4_2_out4));  // open: reset
  matMult_4x4 matmult_4x4_1 (
    .row1(registerbanks_4_1_out1), .row2(registerbanks_4_1_out2), .row3(registerbanks_4_1_out3),
    .row4(registerbanks_4_1_out4), .col1(registerbanks_4_2_out1), .col2(registerbanks_4_2_out2),
    .col3(registerbanks_4_2_out3), .col4(registerbanks_4_2_out4), .Element(matmult_4x4_1_element));  // open: carryout
  Register #(.width(16)) register_1 (
    .D(matmult_4x4_1_element), .en(PCU_data[8]), .clk(clock_1_out), .Q(register_1_q));  // open: clr
  RAM #(.dataWidth(16)) RamC (
    .addr(counter_5_q), .we(PCU_data[9]), .clk(clock_1_out), .din(register_1_q));  // open: oe, dout
  Counter counter_5 (.count(PCU_data[9]), .Q(counter_5_q), .clk(clock_1_out));  // open: load, D, carry, up, clr

  // Notes on the sheet:
  //   contents of InstrucRam (hex, n*v repeats v):
  //   0 1 1401 1 2401 0 4400 0 3400 5 2405 0 4400 0 3400 9 2409 0 4400 0 3400 d 240d 0 4400 0 3400 6*0 5
  //   1405 1 2401 0 4400 0 3400 5 2405 0 4400 0 3400 9 2409 0 4400 0 3400 d 240d 0 4400 0 3400 6*0 9 1409
  //   1 2401 0 4400 0 3400 5 2405 0 4400 0 3400 9 2409 0 4400 0 3400 d 240d 0 4400 0 3400 6*0 d 140d 1
  //   2401 0 4400 0 3400 5 2405 0 4400 0 3400 9 2409 0 4400 0 3400 d 240d 0 4400 0 3400
  //   contents of PCU (hex, n*v repeats v):
  //   16*0 1 2 4 8 8000 11*0 10 20 40 80 8000 11*0 200 8000 14*0 100 8000
endmodule

module ins_Gausian_v1 (
);

  wire clock_1_out, nor_1_out, not_1_out, not_2_out, or_1_out, or_2_out, or_3_out, register_2_q;
  wire [3:0] ins_splitter_1_dimension, ins_splitter_1_opcode;
  wire [7:0] adder_1_out, bit_extender_1_out, counter_1_q, counter_2_q, counter_3_q, counter_4_q,
       counter_5_q, ins_splitter_1_adress, multiplier_1_out;
  wire [15:0] Instruction_Ram_dout, matmult_4x4_1_element, PCU_data, RamA_dout, RamB_dout, register_1_q,
       registerbanks_4_1_out1, registerbanks_4_1_out2, registerbanks_4_1_out3, registerbanks_4_1_out4,
       registerbanks_4_2_out1, registerbanks_4_2_out2, registerbanks_4_2_out3, registerbanks_4_2_out4;

  not not_1 (not_1_out, or_1_out);
  not not_2 (not_2_out, or_2_out);
  Clock clock_1 (.out(clock_1_out));
  RAM #(.dataWidth(16), .\type ("nonvolatile")) RamA (
    .addr(counter_1_q), .clk(clock_1_out), .dout(RamA_dout));  // open: we, oe, din
  Counter counter_1 (
    .load(not_1_out), .D(ins_splitter_1_adress), .count(or_1_out), .Q(counter_1_q), .clk(clock_1_out));  // open: carry, up, clr
  RAM #(.dataWidth(16)) RamB (.addr(counter_2_q), .clk(clock_1_out), .dout(RamB_dout));  // open: we, oe, din
  Counter counter_2 (
    .load(not_2_out), .D(ins_splitter_1_adress), .count(or_2_out), .Q(counter_2_q), .clk(clock_1_out));  // open: carry, up, clr
  RAM #(.dataWidth(16), .\type ("nonvolatile")) Instruction_Ram (
    .addr(counter_3_q), .clk(clock_1_out), .dout(Instruction_Ram_dout));  // open: we, oe, din
  Counter counter_3 (.count(nor_1_out), .Q(counter_3_q), .clk(clock_1_out));  // open: load, D, carry, up, clr
  nor nor_1 (nor_1_out, PCU_data[0], PCU_data[1], PCU_data[11], PCU_data[10], PCU_data[9], PCU_data[15], PCU_data[8], PCU_data[7], PCU_data[6], PCU_data[5], PCU_data[4]);
  or or_1 (or_1_out, PCU_data[11], PCU_data[10], PCU_data[9], PCU_data[8]);
  or or_2 (or_2_out, PCU_data[7], PCU_data[6], PCU_data[5], PCU_data[4]);
  Ins_splitter ins_splitter_1 (
    .Instruction(Instruction_Ram_dout), .WE(nor_1_out), .Clock(clock_1_out), .Adress(ins_splitter_1_adress),
    .Dimension(ins_splitter_1_dimension), .Opcode(ins_splitter_1_opcode));
  // Probe on ins_splitter_1_opcode
  or or_3 (or_3_out, ins_splitter_1_opcode[0], ins_splitter_1_opcode[1], ins_splitter_1_opcode[2], ins_splitter_1_opcode[3]);
  assign bit_extender_1_out = {{4{ins_splitter_1_opcode[3]}}, ins_splitter_1_opcode};  // Bit_Extender bit_extender_1
  Multiplier multiplier_1 (.a(bit_extender_1_out), .b(8'h10), .out(multiplier_1_out));  // open: cin, cout
  Counter counter_4 (
    .count(or_3_out), .Q(counter_4_q), .clk(clock_1_out), .clr(register_2_q));  // open: load, D, carry, up
  Adder adder_1 (.a(counter_4_q), .b(multiplier_1_out), .out(adder_1_out));  // open: cin, cout
  registerBanks_4 registerbanks_4_1 (
    .value(RamA_dout), .WE1(PCU_data[11]), .WE2(PCU_data[10]), .WE3(PCU_data[9]), .WE4(PCU_data[8]),
    .clock(clock_1_out), .out1(registerbanks_4_1_out1), .out2(registerbanks_4_1_out2),
    .out3(registerbanks_4_1_out3), .out4(registerbanks_4_1_out4));  // open: reset
  registerBanks_4 registerbanks_4_2 (
    .value(RamB_dout), .WE1(PCU_data[7]), .WE2(PCU_data[6]), .WE3(PCU_data[5]), .WE4(PCU_data[4]),
    .clock(clock_1_out), .out1(registerbanks_4_2_out1), .out2(registerbanks_4_2_out2),
    .out3(registerbanks_4_2_out3), .out4(registerbanks_4_2_out4));  // open: reset
  ROM #(.dataWidth(16)) PCU (.addr(adder_1_out), .data(PCU_data));
  matMult_4x4 matmult_4x4_1 (
    .row1(registerbanks_4_1_out1), .row2(registerbanks_4_1_out2), .row3(registerbanks_4_1_out3),
    .row4(registerbanks_4_1_out4), .col1(registerbanks_4_2_out1), .col2(registerbanks_4_2_out2),
    .col3(registerbanks_4_2_out3), .col4(registerbanks_4_2_out4), .Element(matmult_4x4_1_element));  // open: carryout
  Register #(.width(16)) register_1 (
    .D(matmult_4x4_1_element), .en(PCU_data[1]), .clk(clock_1_out), .Q(register_1_q));  // open: clr
  Register #(.width(1)) register_2 (.D(PCU_data[15]), .en(1'b1), .clk(clock_1_out), .Q(register_2_q));  // open: clr
  RAM #(.dataWidth(16)) RamC (
    .addr(counter_5_q), .we(PCU_data[0]), .clk(clock_1_out), .din(register_1_q));  // open: oe, dout
  Counter counter_5 (.count(PCU_data[0]), .Q(counter_5_q), .clk(clock_1_out));  // open: load, D, carry, up, clr

  // Notes on the sheet:
  //   Load A
  //   Load B
  //   contents of PCU (hex, n*v repeats v):
  //   16*0 800 400 200 100 8000
  //   MatMult
  //   Store C
endmodule

module MMult_TilingSys_8x8 (
);

  wire clock_1_out, or_1_out, or_2_out;
  wire [3:0] counter_3_q, counter_3_q_2;
  wire [7:0] counter_1_q, counter_2_q, counter_4_q;
  wire [15:0] A1_q, A2_q, A3_q, A4_q, B1_q, B2_q, B3_q, B4_q, C1_q, C2_q, C3_q, C4_q, C5_q, C6_q, C7_q, C8_q,
       C9_q, C10_q, C11_q, C12_q, C13_q, C14_q, C15_q, C16_q, controlled_buffer_1_out, ram_1_dout,
       ram_2_dout, register_1_q, systrolic_4x4gausian_1_c1, systrolic_4x4gausian_1_c2,
       systrolic_4x4gausian_1_c3, systrolic_4x4gausian_1_c4, systrolic_4x4gausian_1_c5,
       systrolic_4x4gausian_1_c6, systrolic_4x4gausian_1_c7, systrolic_4x4gausian_1_c8,
       systrolic_4x4gausian_1_c9, systrolic_4x4gausian_1_c10, systrolic_4x4gausian_1_c11,
       systrolic_4x4gausian_1_c12, systrolic_4x4gausian_1_c13, systrolic_4x4gausian_1_c14,
       systrolic_4x4gausian_1_c15, systrolic_4x4gausian_1_c16;
  wire [23:0] rom_1_data;

  or or_1 (or_1_out, rom_1_data[23], rom_1_data[22], rom_1_data[21], rom_1_data[20]);
  Counter counter_1 (.count(or_1_out), .Q(counter_1_q), .clk(clock_1_out));  // open: load, D, carry, up, clr
  Counter counter_2 (.count(or_1_out), .Q(counter_2_q), .clk(clock_1_out));  // open: load, D, carry, up, clr
  Clock clock_1 (.out(clock_1_out));
  RAM #(.dataWidth(16)) ram_1 (.addr(counter_1_q), .clk(clock_1_out), .dout(ram_1_dout));  // open: we, oe, din
  RAM #(.dataWidth(16)) ram_2 (.addr(counter_2_q), .clk(clock_1_out), .dout(ram_2_dout));  // open: we, oe, din
  Register #(.width(16)) A1 (.D(ram_1_dout), .en(rom_1_data[23]), .clk(clock_1_out), .Q(A1_q));  // open: clr
  Register #(.width(16)) A2 (.D(ram_1_dout), .en(rom_1_data[22]), .clk(clock_1_out), .Q(A2_q));  // open: clr
  Register #(.width(16)) A3 (.D(ram_1_dout), .en(rom_1_data[21]), .clk(clock_1_out), .Q(A3_q));  // open: clr
  Register #(.width(16)) A4 (.D(ram_1_dout), .en(rom_1_data[20]), .clk(clock_1_out), .Q(A4_q));  // open: clr
  Register #(.width(16)) B1 (.D(ram_2_dout), .en(rom_1_data[23]), .clk(clock_1_out), .Q(B1_q));  // open: clr
  Register #(.width(16)) B2 (.D(ram_2_dout), .en(rom_1_data[22]), .clk(clock_1_out), .Q(B2_q));  // open: clr
  Register #(.width(16)) B3 (.D(ram_2_dout), .en(rom_1_data[21]), .clk(clock_1_out), .Q(B3_q));  // open: clr
  Register #(.width(16)) B4 (.D(ram_2_dout), .en(rom_1_data[20]), .clk(clock_1_out), .Q(B4_q));  // open: clr
  systrolic_4x4Gausian systrolic_4x4gausian_1 (
    .B1(B1_q), .B2(B2_q), .B3(B3_q), .B4(B4_q), .A1(A1_q), .A2(A2_q), .A3(A3_q), .A4(A4_q),
    .Clock(clock_1_out), .C1(systrolic_4x4gausian_1_c1), .C2(systrolic_4x4gausian_1_c2),
    .C3(systrolic_4x4gausian_1_c3), .C4(systrolic_4x4gausian_1_c4), .C5(systrolic_4x4gausian_1_c5),
    .C6(systrolic_4x4gausian_1_c6), .C7(systrolic_4x4gausian_1_c7), .C8(systrolic_4x4gausian_1_c8),
    .C9(systrolic_4x4gausian_1_c9), .C10(systrolic_4x4gausian_1_c10), .C11(systrolic_4x4gausian_1_c11),
    .C12(systrolic_4x4gausian_1_c12), .C13(systrolic_4x4gausian_1_c13), .C14(systrolic_4x4gausian_1_c14),
    .C15(systrolic_4x4gausian_1_c15), .C16(systrolic_4x4gausian_1_c16));
  Register #(.width(16)) C1 (.D(systrolic_4x4gausian_1_c1), .Q(C1_q));  // open: en, clk, clr
  Register #(.width(16)) C3 (.D(systrolic_4x4gausian_1_c3), .Q(C3_q));  // open: en, clk, clr
  Register #(.width(16)) C5 (.D(systrolic_4x4gausian_1_c5), .Q(C5_q));  // open: en, clk, clr
  Register #(.width(16)) C7 (.D(systrolic_4x4gausian_1_c7), .Q(C7_q));  // open: en, clk, clr
  Register #(.width(16)) C9 (.D(systrolic_4x4gausian_1_c9), .Q(C9_q));  // open: en, clk, clr
  Register #(.width(16)) C11 (.D(systrolic_4x4gausian_1_c11), .Q(C11_q));  // open: en, clk, clr
  Register #(.width(16)) C13 (.D(systrolic_4x4gausian_1_c13), .Q(C13_q));  // open: en, clk, clr
  Register #(.width(16)) C15 (.D(systrolic_4x4gausian_1_c15), .Q(C15_q));  // open: en, clk, clr
  Register #(.width(16)) C2 (.D(systrolic_4x4gausian_1_c2), .Q(C2_q));  // open: en, clk, clr
  Register #(.width(16)) C4 (.D(systrolic_4x4gausian_1_c4), .Q(C4_q));  // open: en, clk, clr
  Register #(.width(16)) C6 (.D(systrolic_4x4gausian_1_c6), .Q(C6_q));  // open: en, clk, clr
  Register #(.width(16)) C8 (.D(systrolic_4x4gausian_1_c8), .Q(C8_q));  // open: en, clk, clr
  Register #(.width(16)) C10 (.D(systrolic_4x4gausian_1_c10), .Q(C10_q));  // open: en, clk, clr
  Register #(.width(16)) C12 (.D(systrolic_4x4gausian_1_c12), .Q(C12_q));  // open: en, clk, clr
  Register #(.width(16)) C14 (.D(systrolic_4x4gausian_1_c14), .Q(C14_q));  // open: en, clk, clr
  Register #(.width(16)) C16 (.D(systrolic_4x4gausian_1_c16), .Q(C16_q));  // open: en, clk, clr
  assign controlled_buffer_1_out = rom_1_data[19] ? C1_q : 16'bz;  // Controlled_Buffer controlled_buffer_1
  assign controlled_buffer_1_out = rom_1_data[18] ? C2_q : 16'bz;  // Controlled_Buffer controlled_buffer_2
  assign controlled_buffer_1_out = rom_1_data[17] ? C3_q : 16'bz;  // Controlled_Buffer controlled_buffer_3
  Hex_Digit_Display hex_digit_display_1 (.value(counter_3_q_2));  // open: dp
  Hex_Digit_Display hex_digit_display_2 (.value(counter_3_q));  // open: dp
  assign controlled_buffer_1_out = rom_1_data[16] ? C4_q : 16'bz;  // Controlled_Buffer controlled_buffer_4
  assign controlled_buffer_1_out = rom_1_data[15] ? C5_q : 16'bz;  // Controlled_Buffer controlled_buffer_5
  assign controlled_buffer_1_out = rom_1_data[14] ? C6_q : 16'bz;  // Controlled_Buffer controlled_buffer_6
  assign controlled_buffer_1_out = rom_1_data[13] ? C7_q : 16'bz;  // Controlled_Buffer controlled_buffer_7
  assign controlled_buffer_1_out = rom_1_data[12] ? C8_q : 16'bz;  // Controlled_Buffer controlled_buffer_8
  assign controlled_buffer_1_out = rom_1_data[11] ? C9_q : 16'bz;  // Controlled_Buffer controlled_buffer_9
  assign controlled_buffer_1_out = rom_1_data[10] ? C10_q : 16'bz;  // Controlled_Buffer controlled_buffer_10
  assign controlled_buffer_1_out = rom_1_data[9] ? C11_q : 16'bz;  // Controlled_Buffer controlled_buffer_11
  assign controlled_buffer_1_out = rom_1_data[8] ? C12_q : 16'bz;  // Controlled_Buffer controlled_buffer_12
  assign controlled_buffer_1_out = rom_1_data[7] ? C13_q : 16'bz;  // Controlled_Buffer controlled_buffer_13
  assign controlled_buffer_1_out = rom_1_data[6] ? C14_q : 16'bz;  // Controlled_Buffer controlled_buffer_14
  assign controlled_buffer_1_out = rom_1_data[5] ? C15_q : 16'bz;  // Controlled_Buffer controlled_buffer_15
  assign controlled_buffer_1_out = rom_1_data[4] ? C16_q : 16'bz;  // Controlled_Buffer controlled_buffer_16
  or or_2 (or_2_out, rom_1_data[4], rom_1_data[5], rom_1_data[6], rom_1_data[7], rom_1_data[8], rom_1_data[9], rom_1_data[10], rom_1_data[11], rom_1_data[12], rom_1_data[13], rom_1_data[14], rom_1_data[15], rom_1_data[16], rom_1_data[17], rom_1_data[18], rom_1_data[19]);
  Counter counter_3 (.Q({counter_3_q_2, counter_3_q}), .clk(clock_1_out));  // open: load, D, count, carry, up, clr
  Register #(.width(16)) register_1 (
    .D(controlled_buffer_1_out), .en(or_2_out), .clk(clock_1_out), .Q(register_1_q));  // open: clr
  ROM #(.dataWidth(24)) rom_1 (.addr({counter_3_q_2, counter_3_q}), .data(rom_1_data));
  RAM #(.dataWidth(16)) ram_3 (
    .addr(counter_4_q), .we(rom_1_data[3]), .clk(clock_1_out), .din(register_1_q));  // open: oe, dout
  Counter counter_4 (.count(rom_1_data[3]), .Q(counter_4_q), .clk(clock_1_out));  // open: load, D, carry, up, clr

  // Notes on the sheet:
  //   Work In Progress
endmodule

module MMult_GausianSys_4x4 (
);

  wire clock_1_out, or_1_out, or_2_out;
  wire [3:0] counter_3_q, counter_3_q_2;
  wire [7:0] counter_1_q, counter_2_q, counter_4_q;
  wire [15:0] A1_q, A2_q, A3_q, A4_q, B1_q, B2_q, B3_q, B4_q, C1_q, C2_q, C3_q, C4_q, C5_q, C6_q, C7_q, C8_q,
       C9_q, C10_q, C11_q, C12_q, C13_q, C14_q, C15_q, C16_q, controlled_buffer_1_out, ram_1_dout,
       ram_2_dout, register_1_q, systrolic_4x4gausian_1_c1, systrolic_4x4gausian_1_c2,
       systrolic_4x4gausian_1_c3, systrolic_4x4gausian_1_c4, systrolic_4x4gausian_1_c5,
       systrolic_4x4gausian_1_c6, systrolic_4x4gausian_1_c7, systrolic_4x4gausian_1_c8,
       systrolic_4x4gausian_1_c9, systrolic_4x4gausian_1_c10, systrolic_4x4gausian_1_c11,
       systrolic_4x4gausian_1_c12, systrolic_4x4gausian_1_c13, systrolic_4x4gausian_1_c14,
       systrolic_4x4gausian_1_c15, systrolic_4x4gausian_1_c16;
  wire [23:0] rom_1_data;

  or or_1 (or_1_out, rom_1_data[23], rom_1_data[22], rom_1_data[21], rom_1_data[20]);
  Counter counter_1 (.count(or_1_out), .Q(counter_1_q), .clk(clock_1_out));  // open: load, D, carry, up, clr
  Counter counter_2 (.count(or_1_out), .Q(counter_2_q), .clk(clock_1_out));  // open: load, D, carry, up, clr
  Clock clock_1 (.out(clock_1_out));
  RAM #(.dataWidth(16)) ram_1 (.addr(counter_1_q), .clk(clock_1_out), .dout(ram_1_dout));  // open: we, oe, din
  RAM #(.dataWidth(16)) ram_2 (.addr(counter_2_q), .clk(clock_1_out), .dout(ram_2_dout));  // open: we, oe, din
  Register #(.trigger("falling"), .width(16)) A1 (
    .D(ram_1_dout), .en(rom_1_data[23]), .clk(clock_1_out), .Q(A1_q));  // open: clr
  Register #(.trigger("falling"), .width(16)) A2 (
    .D(ram_1_dout), .en(rom_1_data[22]), .clk(clock_1_out), .Q(A2_q));  // open: clr
  Register #(.trigger("falling"), .width(16)) A3 (
    .D(ram_1_dout), .en(rom_1_data[21]), .clk(clock_1_out), .Q(A3_q));  // open: clr
  Register #(.trigger("falling"), .width(16)) A4 (
    .D(ram_1_dout), .en(rom_1_data[20]), .clk(clock_1_out), .Q(A4_q));  // open: clr
  Register #(.trigger("falling"), .width(16)) B1 (
    .D(ram_2_dout), .en(rom_1_data[23]), .clk(clock_1_out), .Q(B1_q));  // open: clr
  Register #(.trigger("falling"), .width(16)) B2 (
    .D(ram_2_dout), .en(rom_1_data[22]), .clk(clock_1_out), .Q(B2_q));  // open: clr
  Register #(.trigger("falling"), .width(16)) B3 (
    .D(ram_2_dout), .en(rom_1_data[21]), .clk(clock_1_out), .Q(B3_q));  // open: clr
  Register #(.trigger("falling"), .width(16)) B4 (
    .D(ram_2_dout), .en(rom_1_data[20]), .clk(clock_1_out), .Q(B4_q));  // open: clr
  systrolic_4x4Gausian systrolic_4x4gausian_1 (
    .B1(B1_q), .B2(B2_q), .B3(B3_q), .B4(B4_q), .A1(A1_q), .A2(A2_q), .A3(A3_q), .A4(A4_q),
    .Clock(clock_1_out), .C1(systrolic_4x4gausian_1_c1), .C2(systrolic_4x4gausian_1_c2),
    .C3(systrolic_4x4gausian_1_c3), .C4(systrolic_4x4gausian_1_c4), .C5(systrolic_4x4gausian_1_c5),
    .C6(systrolic_4x4gausian_1_c6), .C7(systrolic_4x4gausian_1_c7), .C8(systrolic_4x4gausian_1_c8),
    .C9(systrolic_4x4gausian_1_c9), .C10(systrolic_4x4gausian_1_c10), .C11(systrolic_4x4gausian_1_c11),
    .C12(systrolic_4x4gausian_1_c12), .C13(systrolic_4x4gausian_1_c13), .C14(systrolic_4x4gausian_1_c14),
    .C15(systrolic_4x4gausian_1_c15), .C16(systrolic_4x4gausian_1_c16));
  Register #(.width(16)) C1 (.D(systrolic_4x4gausian_1_c1), .en(1'b1), .clk(clock_1_out), .Q(C1_q));  // open: clr
  Register #(.width(16)) C3 (.D(systrolic_4x4gausian_1_c3), .en(1'b1), .clk(clock_1_out), .Q(C3_q));  // open: clr
  Register #(.width(16)) C5 (.D(systrolic_4x4gausian_1_c5), .en(1'b1), .clk(clock_1_out), .Q(C5_q));  // open: clr
  Register #(.width(16)) C7 (.D(systrolic_4x4gausian_1_c7), .en(1'b1), .clk(clock_1_out), .Q(C7_q));  // open: clr
  Register #(.width(16)) C9 (.D(systrolic_4x4gausian_1_c9), .en(1'b1), .clk(clock_1_out), .Q(C9_q));  // open: clr
  Register #(.width(16)) C11 (.D(systrolic_4x4gausian_1_c11), .en(1'b1), .clk(clock_1_out), .Q(C11_q));  // open: clr
  Register #(.width(16)) C13 (.D(systrolic_4x4gausian_1_c13), .en(1'b1), .clk(clock_1_out), .Q(C13_q));  // open: clr
  Register #(.width(16)) C15 (.D(systrolic_4x4gausian_1_c15), .en(1'b1), .clk(clock_1_out), .Q(C15_q));  // open: clr
  Register #(.width(16)) C2 (.D(systrolic_4x4gausian_1_c2), .en(1'b1), .clk(clock_1_out), .Q(C2_q));  // open: clr
  Register #(.width(16)) C4 (.D(systrolic_4x4gausian_1_c4), .en(1'b1), .clk(clock_1_out), .Q(C4_q));  // open: clr
  Register #(.width(16)) C6 (.D(systrolic_4x4gausian_1_c6), .en(1'b1), .clk(clock_1_out), .Q(C6_q));  // open: clr
  Register #(.width(16)) C8 (.D(systrolic_4x4gausian_1_c8), .en(1'b1), .clk(clock_1_out), .Q(C8_q));  // open: clr
  Register #(.width(16)) C10 (.D(systrolic_4x4gausian_1_c10), .en(1'b1), .clk(clock_1_out), .Q(C10_q));  // open: clr
  Register #(.width(16)) C12 (.D(systrolic_4x4gausian_1_c12), .en(1'b1), .clk(clock_1_out), .Q(C12_q));  // open: clr
  Register #(.width(16)) C14 (.D(systrolic_4x4gausian_1_c14), .en(1'b1), .clk(clock_1_out), .Q(C14_q));  // open: clr
  Register #(.width(16)) C16 (.D(systrolic_4x4gausian_1_c16), .en(1'b1), .clk(clock_1_out), .Q(C16_q));  // open: clr
  assign controlled_buffer_1_out = rom_1_data[19] ? C1_q : 16'bz;  // Controlled_Buffer controlled_buffer_1
  assign controlled_buffer_1_out = rom_1_data[18] ? C2_q : 16'bz;  // Controlled_Buffer controlled_buffer_2
  assign controlled_buffer_1_out = rom_1_data[17] ? C3_q : 16'bz;  // Controlled_Buffer controlled_buffer_3
  Hex_Digit_Display hex_digit_display_1 (.value(counter_3_q_2));  // open: dp
  Hex_Digit_Display hex_digit_display_2 (.value(counter_3_q));  // open: dp
  assign controlled_buffer_1_out = rom_1_data[16] ? C4_q : 16'bz;  // Controlled_Buffer controlled_buffer_4
  assign controlled_buffer_1_out = rom_1_data[15] ? C5_q : 16'bz;  // Controlled_Buffer controlled_buffer_5
  assign controlled_buffer_1_out = rom_1_data[14] ? C6_q : 16'bz;  // Controlled_Buffer controlled_buffer_6
  assign controlled_buffer_1_out = rom_1_data[13] ? C7_q : 16'bz;  // Controlled_Buffer controlled_buffer_7
  assign controlled_buffer_1_out = rom_1_data[12] ? C8_q : 16'bz;  // Controlled_Buffer controlled_buffer_8
  assign controlled_buffer_1_out = rom_1_data[11] ? C9_q : 16'bz;  // Controlled_Buffer controlled_buffer_9
  assign controlled_buffer_1_out = rom_1_data[10] ? C10_q : 16'bz;  // Controlled_Buffer controlled_buffer_10
  assign controlled_buffer_1_out = rom_1_data[9] ? C11_q : 16'bz;  // Controlled_Buffer controlled_buffer_11
  assign controlled_buffer_1_out = rom_1_data[8] ? C12_q : 16'bz;  // Controlled_Buffer controlled_buffer_12
  assign controlled_buffer_1_out = rom_1_data[7] ? C13_q : 16'bz;  // Controlled_Buffer controlled_buffer_13
  assign controlled_buffer_1_out = rom_1_data[6] ? C14_q : 16'bz;  // Controlled_Buffer controlled_buffer_14
  assign controlled_buffer_1_out = rom_1_data[5] ? C15_q : 16'bz;  // Controlled_Buffer controlled_buffer_15
  assign controlled_buffer_1_out = rom_1_data[4] ? C16_q : 16'bz;  // Controlled_Buffer controlled_buffer_16
  or or_2 (or_2_out, rom_1_data[4], rom_1_data[5], rom_1_data[6], rom_1_data[7], rom_1_data[8], rom_1_data[9], rom_1_data[10], rom_1_data[11], rom_1_data[12], rom_1_data[13], rom_1_data[14], rom_1_data[15], rom_1_data[16], rom_1_data[17], rom_1_data[18], rom_1_data[19]);
  Counter counter_3 (.Q({counter_3_q_2, counter_3_q}), .clk(clock_1_out));  // open: load, D, count, carry, up, clr
  Register #(.width(16)) register_1 (
    .D(controlled_buffer_1_out), .en(or_2_out), .clk(clock_1_out), .Q(register_1_q));  // open: clr
  ROM #(.dataWidth(24)) rom_1 (.addr({counter_3_q_2, counter_3_q}), .data(rom_1_data));
  RAM #(.dataWidth(16)) ram_3 (
    .addr(counter_4_q), .we(rom_1_data[3]), .clk(clock_1_out), .din(register_1_q));  // open: oe, dout
  Counter counter_4 (.count(rom_1_data[3]), .Q(counter_4_q), .clk(clock_1_out));  // open: load, D, carry, up, clr

  // Notes on the sheet:
  //   contents of rom_1 (hex, n*v repeats v):
  //   800000 800000 400000 800000 400000 200000 800000 480000 200008 100000 400000 240000 120008 200008
  //   110000 108008 4008 2008 1008 808 408 208 108 88 48 28 18 8
endmodule

module MMult_GausianSys_2x2 (
);

  wire clock_1_out, or_1_out, systrolic_processingelement_1_p5;
  wire [7:0] counter_1_q, counter_2_q, counter_3_q, counter_4_q, counter_5_q, counter_6_q;
  wire [15:0] controlled_buffer_1_out, ram_1_dout, ram_2_dout, ram_3_dout, ram_4_dout, register_1_q,
       rom_1_data, systrolic_processingelement_1_p4, systrolic_processingelement_1_p6,
       systrolic_processingelement_2_p4, systrolic_processingelement_2_p5,
       systrolic_processingelement_3_aout, systrolic_processingelement_3_bout,
       systrolic_processingelement_4_cout;

  Counter counter_1 (.count(rom_1_data[13]), .Q(counter_1_q), .clk(clock_1_out));  // open: load, D, carry, up, clr
  Clock clock_1 (.out(clock_1_out));
  Counter counter_2 (.count(rom_1_data[12]), .Q(counter_2_q), .clk(clock_1_out));  // open: load, D, carry, up, clr
  RAM #(.dataWidth(16), .\type ("nonvolatile")) ram_1 (
    .addr(counter_1_q), .clk(clock_1_out), .dout(ram_1_dout));  // open: we, oe, din
  RAM #(.dataWidth(16), .\type ("nonvolatile")) ram_2 (
    .addr(counter_2_q), .clk(clock_1_out), .dout(ram_2_dout));  // open: we, oe, din
  Counter counter_3 (.Q(counter_3_q), .clk(clock_1_out));  // open: load, D, count, carry, up, clr
  // Probe on ram_1_dout
  // Probe on ram_2_dout
  ROM #(.dataWidth(16)) rom_1 (.addr(counter_3_q), .data(rom_1_data));
  Counter counter_4 (.count(rom_1_data[14]), .Q(counter_4_q), .clk(clock_1_out));  // open: load, D, carry, up, clr
  RAM #(.dataWidth(16), .\type ("nonvolatile")) ram_3 (
    .addr(counter_4_q), .clk(clock_1_out), .dout(ram_3_dout));  // open: we, oe, din
  // Probe on systrolic_processingelement_2_p5
  // Probe on ram_3_dout
  // Systrolic_ProcessingElement systrolic_processingelement_1: pin names not known; wires that end beside it: ram_1_dout, ram_3_dout, clock_1_out, systrolic_processingelement_1_p4, systrolic_processingelement_1_p5, systrolic_processingelement_1_p6
  // Probe on systrolic_processingelement_1_p6
  // Systrolic_ProcessingElement systrolic_processingelement_2: pin names not known; wires that end beside it: ram_2_dout, systrolic_processingelement_1_p5, clock_1_out, systrolic_processingelement_2_p4, systrolic_processingelement_2_p5
  Counter counter_5 (.count(rom_1_data[15]), .Q(counter_5_q), .clk(clock_1_out));  // open: load, D, carry, up, clr
  assign controlled_buffer_1_out = rom_1_data[3] ? systrolic_processingelement_1_p6 : 16'bz;  // Controlled_Buffer controlled_buffer_1
  assign controlled_buffer_1_out = rom_1_data[1] ? systrolic_processingelement_2_p5 : 16'bz;  // Controlled_Buffer controlled_buffer_2
  RAM #(.dataWidth(16), .\type ("nonvolatile")) ram_4 (
    .addr(counter_5_q), .clk(clock_1_out), .dout(ram_4_dout));  // open: we, oe, din
  // Probe on systrolic_processingelement_4_cout
  // Probe on ram_4_dout
  // Probe on systrolic_processingelement_3_aout
  Systrolic_ProcessingElement systrolic_processingelement_3 (
    .Ain(systrolic_processingelement_1_p4), .Bin(ram_4_dout), .Clock(clock_1_out),
    .Aout(systrolic_processingelement_3_aout), .Bout(systrolic_processingelement_3_bout));  // open: Cout
  Systrolic_ProcessingElement systrolic_processingelement_4 (
    .Ain(systrolic_processingelement_2_p4), .Bin(systrolic_processingelement_3_bout), .Clock(clock_1_out),
    .Cout(systrolic_processingelement_4_cout));  // open: Aout, Bout
  assign controlled_buffer_1_out = rom_1_data[0] ? systrolic_processingelement_4_cout : 16'bz;  // Controlled_Buffer controlled_buffer_3
  or or_1 (or_1_out, rom_1_data[0], rom_1_data[1], rom_1_data[2], rom_1_data[3]);
  assign controlled_buffer_1_out = rom_1_data[2] ? systrolic_processingelement_3_aout : 16'bz;  // Controlled_Buffer controlled_buffer_4
  Register #(.width(16)) register_1 (
    .D(controlled_buffer_1_out), .en(or_1_out), .clk(clock_1_out), .Q(register_1_q));  // open: clr
  Counter counter_6 (.count(rom_1_data[7]), .Q(counter_6_q), .clk(clock_1_out));  // open: load, D, carry, up, clr
  RAM #(.dataWidth(16)) ram_5 (
    .addr(counter_6_q), .we(rom_1_data[7]), .clk(clock_1_out), .din(register_1_q));  // open: oe, dout

  // Notes on the sheet:
  //   contents of rom_1 (hex, n*v repeats v):
  //   6000 f008 9082 9084 81 80
endmodule

module Mmult_Tiling2x2 (
  input  in_1
);

  wire clock_1_out, or_1_out, or_2_out;
  wire [3:0] counter_3_q, counter_3_q_2;
  wire [7:0] counter_1_q, counter_2_q, counter_4_q;
  wire [15:0] A1_q, A2_q, A3_q, A4_q, adder_1_out, B1_q, B2_q, B3_q, B4_q, controlled_buffer_1_out,
       controlled_buffer_2_out, controlled_buffer_3_out, controlled_buffer_4_out, controlled_buffer_5_out,
       controlled_buffer_6_out, controlled_buffer_7_out, controlled_buffer_8_out, matmulttile_2x2_1_c1,
       matmulttile_2x2_1_c2, matmulttile_2x2_1_c3, matmulttile_2x2_1_c4, R1_q, R2_q, R3_q, R4_q, ram_1_dout,
       ram_2_dout, RomCPU_data, S1_q, S2_q, S3_q, S4_q;

  Clock clock_1 (.out(clock_1_out));
  or or_1 (or_1_out, RomCPU_data[15], RomCPU_data[14], RomCPU_data[13], in_1);
  RAM #(.dataWidth(16), .\type ("nonvolatile")) ram_1 (
    .addr(counter_1_q), .clk(clock_1_out), .dout(ram_1_dout));  // open: we, oe, din
  Counter counter_1 (
    .load(RomCPU_data[2]), .D(8'h8), .count(or_1_out), .Q(counter_1_q), .clk(clock_1_out),
    .clr(RomCPU_data[1]));  // open: carry, up
  RAM #(.dataWidth(16), .\type ("nonvolatile")) ram_2 (
    .addr(counter_2_q), .clk(clock_1_out), .dout(ram_2_dout));  // open: we, oe, din
  Counter #(.max('hf)) counter_2 (
    .count(or_1_out), .Q(counter_2_q), .clk(clock_1_out));  // open: load, D, carry, up, clr
  // Probe on ram_1_dout
  // Probe on ram_2_dout
  Register #(.width(16)) A1 (.D(ram_1_dout), .en(RomCPU_data[15]), .clk(clock_1_out), .Q(A1_q));  // open: clr
  Register #(.width(16)) A2 (.D(ram_1_dout), .en(RomCPU_data[14]), .clk(clock_1_out), .Q(A2_q));  // open: clr
  Register #(.width(16)) A3 (.D(ram_1_dout), .en(RomCPU_data[13]), .clk(clock_1_out), .Q(A3_q));  // open: clr
  Register #(.width(16)) A4 (.D(ram_1_dout), .en(RomCPU_data[12]), .clk(clock_1_out), .Q(A4_q));  // open: clr
  Register #(.width(16)) B1 (.D(ram_2_dout), .en(RomCPU_data[15]), .clk(clock_1_out), .Q(B1_q));  // open: clr
  Register #(.width(16)) B2 (.D(ram_2_dout), .en(RomCPU_data[14]), .clk(clock_1_out), .Q(B2_q));  // open: clr
  Register #(.width(16)) B3 (.D(ram_2_dout), .en(RomCPU_data[13]), .clk(clock_1_out), .Q(B3_q));  // open: clr
  Register #(.width(16)) B4 (.D(ram_2_dout), .en(RomCPU_data[12]), .clk(clock_1_out), .Q(B4_q));  // open: clr
  // Probe on A1_q
  // Probe on A2_q
  // Probe on A3_q
  // Probe on A4_q
  // Probe on B1_q
  // Probe on B2_q
  // Probe on B3_q
  // Probe on B4_q
  Hex_Digit_Display hex_digit_display_1 (.value(counter_3_q_2));  // open: dp
  Hex_Digit_Display hex_digit_display_2 (.value(counter_3_q));  // open: dp
  matMultTile_2x2 matmulttile_2x2_1 (
    .A1(A1_q), .B1(A2_q), .A2(A3_q), .B3(A4_q), .B2(B1_q), .B4(B2_q), .A3(B3_q), .A4(B4_q),
    .C1(matmulttile_2x2_1_c1), .C2(matmulttile_2x2_1_c2), .C3(matmulttile_2x2_1_c3), .C4(matmulttile_2x2_1_c4));
  // Probe on matmulttile_2x2_1_c4
  Register #(.width(16)) R1 (.D(matmulttile_2x2_1_c1), .en(RomCPU_data[11]), .clk(clock_1_out), .Q(R1_q));  // open: clr
  // Probe on matmulttile_2x2_1_c1
  Register #(.width(16)) R2 (.D(matmulttile_2x2_1_c2), .en(RomCPU_data[11]), .clk(clock_1_out), .Q(R2_q));  // open: clr
  // Probe on matmulttile_2x2_1_c2
  Register #(.width(16)) R3 (.D(matmulttile_2x2_1_c3), .en(RomCPU_data[11]), .clk(clock_1_out), .Q(R3_q));  // open: clr
  // Probe on matmulttile_2x2_1_c3
  Register #(.width(16)) R4 (.D(matmulttile_2x2_1_c4), .en(RomCPU_data[11]), .clk(clock_1_out), .Q(R4_q));  // open: clr
  Register #(.width(16)) S1 (.D(matmulttile_2x2_1_c1), .en(RomCPU_data[10]), .clk(clock_1_out), .Q(S1_q));  // open: clr
  // Probe on matmulttile_2x2_1_c1
  Register #(.width(16)) S2 (.D(matmulttile_2x2_1_c2), .en(RomCPU_data[10]), .clk(clock_1_out), .Q(S2_q));  // open: clr
  // Probe on matmulttile_2x2_1_c2
  Register #(.width(16)) S3 (.D(matmulttile_2x2_1_c3), .en(RomCPU_data[10]), .clk(clock_1_out), .Q(S3_q));  // open: clr
  // Probe on matmulttile_2x2_1_c3
  Register #(.width(16)) S4 (.D(matmulttile_2x2_1_c4), .en(RomCPU_data[10]), .clk(clock_1_out), .Q(S4_q));  // open: clr
  // Probe on matmulttile_2x2_1_c4
  Counter counter_3 (.Q({counter_3_q_2, counter_3_q}), .clk(clock_1_out));  // open: load, D, count, carry, up, clr
  assign controlled_buffer_1_out = RomCPU_data[7] ? R1_q : 16'bz;  // Controlled_Buffer controlled_buffer_1
  assign controlled_buffer_2_out = RomCPU_data[6] ? R2_q : 16'bz;  // Controlled_Buffer controlled_buffer_2
  assign controlled_buffer_3_out = RomCPU_data[5] ? R3_q : 16'bz;  // Controlled_Buffer controlled_buffer_3
  assign controlled_buffer_4_out = RomCPU_data[7] ? S1_q : 16'bz;  // Controlled_Buffer controlled_buffer_4
  assign controlled_buffer_5_out = RomCPU_data[6] ? S2_q : 16'bz;  // Controlled_Buffer controlled_buffer_5
  assign controlled_buffer_6_out = RomCPU_data[5] ? S3_q : 16'bz;  // Controlled_Buffer controlled_buffer_6
  // Probe on controlled_buffer_1_out
  // Probe on controlled_buffer_2_out
  // Probe on controlled_buffer_3_out
  // Probe on controlled_buffer_7_out
  assign controlled_buffer_7_out = RomCPU_data[4] ? R4_q : 16'bz;  // Controlled_Buffer controlled_buffer_7
  // Probe on controlled_buffer_4_out
  // Probe on controlled_buffer_5_out
  // Probe on controlled_buffer_6_out
  // Probe on controlled_buffer_8_out
  assign controlled_buffer_8_out = RomCPU_data[4] ? S4_q : 16'bz;  // Controlled_Buffer controlled_buffer_8
  ROM #(.dataWidth(16)) RomCPU (.addr({counter_3_q_2, counter_3_q}), .data(RomCPU_data));
  Adder #(.width(16)) adder_1 (
    .a(controlled_buffer_1_out), .b(controlled_buffer_4_out), .out(adder_1_out));  // open: cin, cout
  Adder #(.width(16)) adder_2 (
    .a(controlled_buffer_2_out), .b(controlled_buffer_5_out), .out(adder_1_out));  // open: cin, cout
  Adder #(.width(16)) adder_3 (
    .a(controlled_buffer_3_out), .b(controlled_buffer_6_out), .out(adder_1_out));  // open: cin, cout
  Adder #(.width(16)) adder_4 (
    .a(controlled_buffer_7_out), .b(controlled_buffer_8_out), .out(adder_1_out));  // open: cin, cout
  // Probe on adder_1_out
  Counter counter_4 (.count(or_2_out), .Q(counter_4_q), .clk(clock_1_out));  // open: load, D, carry, up, clr
  or or_2 (or_2_out, RomCPU_data[7], RomCPU_data[6], RomCPU_data[5], RomCPU_data[4]);
  RAM #(.dataWidth(16)) ram_3 (
    .addr(counter_4_q), .we(RomCPU_data[0]), .clk(clock_1_out), .din(adder_1_out));  // open: oe, dout

  // Notes on the sheet:
  //   contents of RomCPU (hex, n*v repeats v):
  //   8000 8000 4000 2000 1000 8800 8000 4000 2000 1000 400 81 41 21 11 2 8000 8000 4000 2000 1000 8800
  //   8000 4000 2000 1000 481 41 21 11 8000 8000 4000 2000 1000 8800 4000 2000 1000 400 81 41 21 11 8004
  //   8000 8000 4000 2000 1000 8800 8000 4000 2000 1000 400 81 41 21 11
endmodule

module MMult_Gausian (
);

  wire clock_1_out, or_1_out, or_2_out, or_3_out;
  wire [3:0] counter_3_q, counter_3_q_2;
  wire [7:0] counter_1_q, counter_2_q, counter_4_q;
  wire [15:0] A1_q, A2_q, A3_q, A4_q, B1_q, B2_q, B3_q, B4_q, C1_q, controlled_buffer_1_out,
       matmult_4x4_1_element, ram_1_dout, ram_2_dout, rom_1_data;

  or or_1 (or_1_out, rom_1_data[15], rom_1_data[14], rom_1_data[13], rom_1_data[12]);
  Clock clock_1 (.out(clock_1_out));
  or or_2 (or_2_out, rom_1_data[8], rom_1_data[9], rom_1_data[10], rom_1_data[11]);
  RAM #(.dataWidth(16), .\type ("nonvolatile")) ram_1 (
    .addr(counter_1_q), .oe(or_1_out), .clk(clock_1_out), .dout(ram_1_dout));  // open: we, din
  Counter counter_1 (.count(or_1_out), .Q(counter_1_q), .clk(clock_1_out));  // open: load, D, carry, up, clr
  Counter #(.max('hf)) counter_2 (
    .count(or_2_out), .Q(counter_2_q), .clk(clock_1_out));  // open: load, D, carry, up, clr
  RAM #(.dataWidth(16), .\type ("nonvolatile")) ram_2 (
    .addr(counter_2_q), .clk(clock_1_out), .dout(ram_2_dout));  // open: we, oe, din
  // Probe on ram_1_dout
  // Probe on ram_2_dout
  Register #(.width(16)) A1 (.D(ram_1_dout), .en(rom_1_data[15]), .clk(clock_1_out), .Q(A1_q));  // open: clr
  Register #(.width(16)) A2 (.D(ram_1_dout), .en(rom_1_data[14]), .clk(clock_1_out), .Q(A2_q));  // open: clr
  Register #(.width(16)) A3 (.D(ram_1_dout), .en(rom_1_data[13]), .clk(clock_1_out), .Q(A3_q));  // open: clr
  Register #(.width(16)) A4 (.D(ram_1_dout), .en(rom_1_data[12]), .clk(clock_1_out), .Q(A4_q));  // open: clr
  Register #(.width(16)) B1 (.D(ram_2_dout), .en(rom_1_data[11]), .clk(clock_1_out), .Q(B1_q));  // open: clr
  Register #(.width(16)) B2 (.D(ram_2_dout), .en(rom_1_data[10]), .clk(clock_1_out), .Q(B2_q));  // open: clr
  Register #(.width(16)) B3 (.D(ram_2_dout), .en(rom_1_data[9]), .clk(clock_1_out), .Q(B3_q));  // open: clr
  Register #(.width(16)) B4 (.D(ram_2_dout), .en(rom_1_data[8]), .clk(clock_1_out), .Q(B4_q));  // open: clr
  // Probe on A1_q
  // Probe on A2_q
  // Probe on A3_q
  // Probe on A4_q
  // Probe on B1_q
  // Probe on B2_q
  // Probe on B3_q
  // Probe on B4_q
  Hex_Digit_Display hex_digit_display_1 (.value(counter_3_q_2));  // open: dp
  Hex_Digit_Display hex_digit_display_2 (.value(counter_3_q));  // open: dp
  matMult_4x4 matmult_4x4_1 (
    .row1(A1_q), .row2(A2_q), .row3(A3_q), .row4(A4_q), .col1(B1_q), .col2(B2_q), .col3(B3_q), .col4(B4_q),
    .Element(matmult_4x4_1_element));  // open: carryout
  // Probe on matmult_4x4_1_element
  Register #(.width(16)) C1 (.D(matmult_4x4_1_element), .en(rom_1_data[7]), .clk(clock_1_out), .Q(C1_q));  // open: clr
  assign controlled_buffer_1_out = rom_1_data[3] ? C1_q : 16'bz;  // Controlled_Buffer controlled_buffer_1
  ROM #(.dataWidth(16)) rom_1 (.addr({counter_3_q_2, counter_3_q}), .data(rom_1_data));
  Counter counter_3 (.Q({counter_3_q_2, counter_3_q}), .clk(clock_1_out));  // open: load, D, count, carry, up, clr
  // Probe on controlled_buffer_1_out
  or or_3 (or_3_out, rom_1_data[0], rom_1_data[1], rom_1_data[2], rom_1_data[3]);
  RAM #(.dataWidth(16)) ram_3 (
    .addr(counter_4_q), .we(or_3_out), .clk(clock_1_out), .din(controlled_buffer_1_out));  // open: oe, dout
  Counter counter_4 (.count(or_3_out), .Q(counter_4_q), .clk(clock_1_out));  // open: load, D, carry, up, clr
  // Probe on counter_4_q

  // Notes on the sheet:
  //   contents of rom_1 (hex, n*v repeats v):
  //   8800 8800 4400 2200 1100 880 408 200 100 880 408 200 100 880 408 200 100 8880 4408 2200 1100 880 408
  //   200 100 880 408 200 100 880 408 200 100 8880 4408 2200 1100 880 408 200 100 880 408 200 100 880 408
  //   200 100 8880 4408 2200 1100 880 408 200 100 880 408 200 100 880 408 200 100 80 8
endmodule

module sumofsum_auto (
);

  wire clock_1_out, or_1_out;
  wire [7:0] counter_1_q, counter_2_q, counter_3_q, counter_4_q, counter_5_q;
  wire [15:0] A1_q, A2_q, A3_q, A4_q, B1_q, B2_q, B3_q, B4_q, controlled_buffer_1_out,
       controlled_buffer_5_out, multiadder_16bit_1_r1, multiadder_16bit_1_r2, multiadder_16bit_1_r3,
       multiadder_16bit_1_r4, R1_q, R2_q, R3_q, R4_q, ram_1_dout, ram_2_dout, register_1_q, register_2_q,
       register_3_q, register_4_q, register_5_q, rom_1_data, sum_4val_1_result;

  Clock clock_1 (.out(clock_1_out));
  RAM #(.dataWidth(16), .\type ("nonvolatile")) ram_1 (
    .addr(counter_1_q), .clk(clock_1_out), .dout(ram_1_dout));  // open: we, oe, din
  // Probe on counter_1_q
  Counter counter_1 (.Q(counter_1_q), .clk(clock_1_out));  // open: load, D, count, carry, up, clr
  RAM #(.dataWidth(16), .\type ("nonvolatile")) ram_2 (
    .addr(counter_1_q), .clk(clock_1_out), .dout(ram_2_dout));  // open: we, oe, din
  // Probe on ram_1_dout
  // Probe on ram_2_dout
  Register #(.width(16)) A1 (.D(ram_1_dout), .en(rom_1_data[15]), .clk(clock_1_out), .Q(A1_q));  // open: clr
  Register #(.width(16)) A2 (.D(ram_1_dout), .en(rom_1_data[14]), .clk(clock_1_out), .Q(A2_q));  // open: clr
  Register #(.width(16)) A3 (.D(ram_1_dout), .en(rom_1_data[13]), .clk(clock_1_out), .Q(A3_q));  // open: clr
  Register #(.width(16)) A4 (.D(ram_1_dout), .en(rom_1_data[12]), .clk(clock_1_out), .Q(A4_q));  // open: clr
  Register #(.width(16)) B1 (.D(ram_2_dout), .en(rom_1_data[11]), .clk(clock_1_out), .Q(B1_q));  // open: clr
  Register #(.width(16)) B2 (.D(ram_2_dout), .en(rom_1_data[10]), .clk(clock_1_out), .Q(B2_q));  // open: clr
  Register #(.width(16)) B3 (.D(ram_2_dout), .en(rom_1_data[9]), .clk(clock_1_out), .Q(B3_q));  // open: clr
  Register #(.width(16)) B4 (.D(ram_2_dout), .en(rom_1_data[8]), .clk(clock_1_out), .Q(B4_q));  // open: clr
  // Probe on A1_q
  // Probe on A2_q
  // Probe on A3_q
  // Probe on A4_q
  // Probe on B1_q
  // Probe on B2_q
  // Probe on B3_q
  // Probe on B4_q
  multiadder_16bit multiadder_16bit_1 (
    .A1(A1_q), .A2(A2_q), .A3(A3_q), .A4(A4_q), .B1(B1_q), .B2(B2_q), .B3(B3_q), .B4(B4_q),
    .R1(multiadder_16bit_1_r1), .R2(multiadder_16bit_1_r2), .R3(multiadder_16bit_1_r3),
    .R4(multiadder_16bit_1_r4));  // open: C1, C2, C3, C4
  // Probe on multiadder_16bit_1_r1
  // Probe on multiadder_16bit_1_r2
  // Probe on multiadder_16bit_1_r3
  // Probe on multiadder_16bit_1_r4
  Register #(.width(16)) R1 (.D(multiadder_16bit_1_r1), .en(rom_1_data[7]), .clk(clock_1_out), .Q(R1_q));  // open: clr
  Register #(.width(16)) R2 (.D(multiadder_16bit_1_r2), .en(rom_1_data[6]), .clk(clock_1_out), .Q(R2_q));  // open: clr
  Register #(.width(16)) R3 (.D(multiadder_16bit_1_r3), .en(rom_1_data[5]), .clk(clock_1_out), .Q(R3_q));  // open: clr
  Register #(.width(16)) R4 (.D(multiadder_16bit_1_r4), .en(rom_1_data[4]), .clk(clock_1_out), .Q(R4_q));  // open: clr
  assign controlled_buffer_1_out = rom_1_data[3] ? R1_q : 16'bz;  // Controlled_Buffer controlled_buffer_1
  assign controlled_buffer_1_out = rom_1_data[2] ? R2_q : 16'bz;  // Controlled_Buffer controlled_buffer_2
  ROM #(.dataWidth(16)) rom_1 (.addr(counter_2_q), .data(rom_1_data));
  Counter counter_2 (.Q(counter_2_q), .clk(clock_1_out));  // open: load, D, count, carry, up, clr
  assign controlled_buffer_1_out = rom_1_data[1] ? R3_q : 16'bz;  // Controlled_Buffer controlled_buffer_3
  assign controlled_buffer_1_out = rom_1_data[0] ? R4_q : 16'bz;  // Controlled_Buffer controlled_buffer_4
  // Probe on controlled_buffer_1_out
  // Probe on controlled_buffer_1_out
  // Probe on controlled_buffer_1_out
  // Probe on controlled_buffer_1_out
  or or_1 (or_1_out, rom_1_data[0], rom_1_data[1], rom_1_data[2], rom_1_data[3]);
  RAM #(.dataWidth(16)) ram_3 (
    .addr(counter_3_q), .we(or_1_out), .clk(clock_1_out), .din(controlled_buffer_1_out));  // open: oe, dout
  Counter counter_3 (.count(or_1_out), .Q(counter_3_q), .clk(clock_1_out));  // open: load, D, carry, up, clr
  // Probe on counter_3_q
  Register #(.width(16)) register_1 (.D(R1_q), .en(rom_1_data[3]), .clk(rom_1_data[3]), .Q(register_1_q));  // open: clr
  Register #(.width(16)) register_2 (.D(R2_q), .en(rom_1_data[2]), .clk(rom_1_data[2]), .Q(register_2_q));  // open: clr
  Register #(.width(16)) register_3 (.D(R3_q), .en(rom_1_data[1]), .clk(rom_1_data[1]), .Q(register_3_q));  // open: clr
  Register #(.width(16)) register_4 (.D(R4_q), .en(rom_1_data[0]), .clk(rom_1_data[0]), .Q(register_4_q));  // open: clr
  sum_4val sum_4val_1 (
    .sum1(register_1_q), .sum2(register_2_q), .sum3(register_3_q), .sum4(register_4_q),
    .result(sum_4val_1_result));  // open: carry
  Register #(.width(16)) register_5 (
    .D(controlled_buffer_5_out), .en(rom_1_data[0]), .clk(rom_1_data[0]), .Q(register_5_q));  // open: clr
  assign controlled_buffer_5_out = rom_1_data[0] ? sum_4val_1_result : 16'bz;  // Controlled_Buffer controlled_buffer_5
  Counter counter_4 (.Q(counter_4_q), .clk(rom_1_data[3]));  // open: load, D, count, carry, up, clr
  Counter counter_5 (.D(counter_4_q), .Q(counter_5_q), .clk(rom_1_data[3]));  // open: load, count, carry, up, clr
  RAM #(.dataWidth(16)) RamD (
    .addr(counter_5_q), .we(clock_1_out), .clk(clock_1_out), .din(register_5_q));  // open: oe, dout

  // Notes on the sheet:
  //   contents of rom_1 (hex, n*v repeats v):
  //   0 8800 4480 2248 1124 8812 4481
endmodule

module ram2multiadder_auto (
);

  wire clock_1_out, or_1_out, or_2_out;
  wire [3:0] counter_1_q, counter_1_q_2;
  wire [7:0] counter_2_q, counter_3_q;
  wire [15:0] A1_q, A2_q, A3_q, A4_q, B1_q, B2_q, B3_q, B4_q, controlled_buffer_1_out, multiadder_16bit_1_r1,
       multiadder_16bit_1_r2, multiadder_16bit_1_r3, multiadder_16bit_1_r4, R1_q, R2_q, R3_q, R4_q,
       ram_1_dout, ram_2_dout, RomCPU_data;

  or or_1 (or_1_out, RomCPU_data[11], RomCPU_data[10], RomCPU_data[9], RomCPU_data[8]);
  Clock clock_1 (.out(clock_1_out));
  RAM #(.dataWidth(16), .\type ("nonvolatile")) ram_1 (
    .addr({counter_1_q_2, counter_1_q}), .clk(clock_1_out), .dout(ram_1_dout));  // open: we, oe, din
  Counter counter_1 (
    .count(or_1_out), .Q({counter_1_q_2, counter_1_q}), .clk(clock_1_out));  // open: load, D, carry, up, clr
  RAM #(.dataWidth(16), .\type ("nonvolatile")) ram_2 (
    .addr({counter_1_q_2, counter_1_q}), .clk(clock_1_out), .dout(ram_2_dout));  // open: we, oe, din
  // Probe on ram_1_dout
  // Probe on ram_2_dout
  Register #(.width(16)) A1 (.D(ram_1_dout), .en(RomCPU_data[15]), .clk(clock_1_out), .Q(A1_q));  // open: clr
  Register #(.width(16)) A2 (.D(ram_1_dout), .en(RomCPU_data[14]), .clk(clock_1_out), .Q(A2_q));  // open: clr
  Register #(.width(16)) A3 (.D(ram_1_dout), .en(RomCPU_data[13]), .clk(clock_1_out), .Q(A3_q));  // open: clr
  Register #(.width(16)) A4 (.D(ram_1_dout), .en(RomCPU_data[12]), .clk(clock_1_out), .Q(A4_q));  // open: clr
  Register #(.width(16)) B1 (.D(ram_2_dout), .en(RomCPU_data[11]), .clk(clock_1_out), .Q(B1_q));  // open: clr
  Register #(.width(16)) B2 (.D(ram_2_dout), .en(RomCPU_data[10]), .clk(clock_1_out), .Q(B2_q));  // open: clr
  Register #(.width(16)) B3 (.D(ram_2_dout), .en(RomCPU_data[9]), .clk(clock_1_out), .Q(B3_q));  // open: clr
  Register #(.width(16)) B4 (.D(ram_2_dout), .en(RomCPU_data[8]), .clk(clock_1_out), .Q(B4_q));  // open: clr
  // Probe on B1_q
  // Probe on B2_q
  // Probe on A1_q
  // Probe on A2_q
  // Probe on A3_q
  // Probe on A4_q
  // Probe on B3_q
  // Probe on B4_q
  Hex_Digit_Display hex_digit_display_1 (.value(counter_1_q_2));  // open: dp
  Hex_Digit_Display hex_digit_display_2 (.value(counter_1_q));  // open: dp
  multiadder_16bit multiadder_16bit_1 (
    .A1(A1_q), .A2(A2_q), .A3(A3_q), .A4(A4_q), .B1(B1_q), .B2(B2_q), .B3(B3_q), .B4(B4_q),
    .R1(multiadder_16bit_1_r1), .R2(multiadder_16bit_1_r2), .R3(multiadder_16bit_1_r3),
    .R4(multiadder_16bit_1_r4));  // open: C1, C2, C3, C4
  // Probe on multiadder_16bit_1_r1
  // Probe on multiadder_16bit_1_r2
  // Probe on multiadder_16bit_1_r3
  // Probe on multiadder_16bit_1_r4
  Register #(.width(16)) R1 (.D(multiadder_16bit_1_r1), .en(RomCPU_data[7]), .clk(clock_1_out), .Q(R1_q));  // open: clr
  Register #(.width(16)) R2 (.D(multiadder_16bit_1_r2), .en(RomCPU_data[6]), .clk(clock_1_out), .Q(R2_q));  // open: clr
  Register #(.width(16)) R3 (.D(multiadder_16bit_1_r3), .en(RomCPU_data[5]), .clk(clock_1_out), .Q(R3_q));  // open: clr
  Register #(.width(16)) R4 (.D(multiadder_16bit_1_r4), .en(RomCPU_data[4]), .clk(clock_1_out), .Q(R4_q));  // open: clr
  Counter counter_2 (.Q(counter_2_q), .clk(clock_1_out));  // open: load, D, count, carry, up, clr
  assign controlled_buffer_1_out = RomCPU_data[3] ? R1_q : 16'bz;  // Controlled_Buffer controlled_buffer_1
  assign controlled_buffer_1_out = RomCPU_data[2] ? R2_q : 16'bz;  // Controlled_Buffer controlled_buffer_2
  ROM #(.dataWidth(16)) RomCPU (.addr(counter_2_q), .data(RomCPU_data));
  assign controlled_buffer_1_out = RomCPU_data[1] ? R3_q : 16'bz;  // Controlled_Buffer controlled_buffer_3
  assign controlled_buffer_1_out = RomCPU_data[0] ? R4_q : 16'bz;  // Controlled_Buffer controlled_buffer_4
  // Probe on controlled_buffer_1_out
  // Probe on controlled_buffer_1_out
  // Probe on controlled_buffer_1_out
  // Probe on controlled_buffer_1_out
  or or_2 (or_2_out, RomCPU_data[0], RomCPU_data[1], RomCPU_data[2], RomCPU_data[3]);
  Counter counter_3 (.count(or_2_out), .Q(counter_3_q), .clk(clock_1_out));  // open: load, D, carry, up, clr
  // Probe on counter_3_q
  RAM #(.dataWidth(16)) ram_3 (
    .addr(counter_3_q), .we(or_2_out), .clk(clock_1_out), .din(controlled_buffer_1_out));  // open: oe, dout

  // Notes on the sheet:
  //   contents of RomCPU (hex, n*v repeats v):
  //   0 8800 4480 2248 1124 8812 4481
endmodule

module ram2multi_prot1 (
);

  wire clock_1_out, comparator_1_eq, comparator_2_eq, comparator_3_eq, comparator_4_eq, comparator_5_eq,
       comparator_6_eq, comparator_7_eq, comparator_8_eq, comparator_9_eq, comparator_10_eq;
  wire [7:0] counter_1_q, counter_2_q, counter_3_q;
  wire [15:0] A1_q, A2_q, A3_q, A4_q, B1_q, B2_q, B3_q, B4_q, controlled_buffer_1_out, multiadder_16bit_1_r1,
       multiadder_16bit_1_r2, multiadder_16bit_1_r3, multiadder_16bit_1_r4, R1_q, R2_q, R3_q, R4_q,
       ram_1_dout, ram_2_dout;

  Clock clock_1 (.out(clock_1_out));
  RAM #(.dataWidth(16), .\type ("nonvolatile")) ram_1 (
    .addr(counter_1_q), .clk(clock_1_out), .dout(ram_1_dout));  // open: we, oe, din
  Counter counter_1 (.Q(counter_1_q), .clk(clock_1_out));  // open: load, D, count, carry, up, clr
  RAM #(.dataWidth(16), .\type ("nonvolatile")) ram_2 (
    .addr(counter_1_q), .clk(clock_1_out), .dout(ram_2_dout));  // open: we, oe, din
  Register #(.width(16)) A1 (.D(ram_1_dout), .en(comparator_2_eq), .clk(clock_1_out), .Q(A1_q));  // open: clr
  Register #(.width(16)) A2 (.D(ram_1_dout), .en(comparator_3_eq), .clk(clock_1_out), .Q(A2_q));  // open: clr
  Register #(.width(16)) A3 (.D(ram_1_dout), .en(comparator_4_eq), .clk(clock_1_out), .Q(A3_q));  // open: clr
  Register #(.width(16)) A4 (.D(ram_1_dout), .en(comparator_5_eq), .clk(clock_1_out), .Q(A4_q));  // open: clr
  Register #(.width(16)) B1 (.D(ram_2_dout), .en(comparator_2_eq), .clk(clock_1_out), .Q(B1_q));  // open: clr
  Register #(.width(16)) B2 (.D(ram_2_dout), .en(comparator_3_eq), .clk(clock_1_out), .Q(B2_q));  // open: clr
  Register #(.width(16)) B3 (.D(ram_2_dout), .en(comparator_4_eq), .clk(clock_1_out), .Q(B3_q));  // open: clr
  Register #(.width(16)) B4 (.D(ram_2_dout), .en(comparator_5_eq), .clk(clock_1_out), .Q(B4_q));  // open: clr
  // Probe on B1_q
  // Probe on B2_q
  // Probe on A1_q
  // Probe on A2_q
  // Probe on A3_q
  // Probe on A4_q
  // Probe on B3_q
  // Probe on B4_q
  Counter counter_2 (.Q(counter_2_q), .clk(clock_1_out), .clr(comparator_1_eq));  // open: load, D, count, carry, up
  Comparator comparator_1 (.a(8'h5), .b(counter_2_q), .eq(comparator_1_eq));  // open: gt, lt
  Comparator comparator_2 (.a(8'h1), .b(counter_2_q), .eq(comparator_2_eq));  // open: gt, lt
  Comparator comparator_3 (.a(8'h2), .b(counter_2_q), .eq(comparator_3_eq));  // open: gt, lt
  Comparator comparator_4 (.a(8'h3), .b(counter_2_q), .eq(comparator_4_eq));  // open: gt, lt
  Comparator comparator_5 (.a(8'h4), .b(counter_2_q), .eq(comparator_5_eq));  // open: gt, lt
  multiadder_16bit multiadder_16bit_1 (
    .A1(A1_q), .A2(A2_q), .A3(A3_q), .A4(A4_q), .B1(B1_q), .B2(B2_q), .B3(B3_q), .B4(B4_q),
    .R1(multiadder_16bit_1_r1), .R2(multiadder_16bit_1_r2), .R3(multiadder_16bit_1_r3),
    .R4(multiadder_16bit_1_r4));  // open: C1, C2, C3, C4
  // Probe on multiadder_16bit_1_r1
  // Probe on multiadder_16bit_1_r2
  // Probe on multiadder_16bit_1_r3
  // Probe on multiadder_16bit_1_r4
  Register #(.width(16)) R1 (.D(multiadder_16bit_1_r1), .clk(clock_1_out), .Q(R1_q));  // open: en, clr
  Register #(.width(16)) R2 (.D(multiadder_16bit_1_r2), .clk(clock_1_out), .Q(R2_q));  // open: en, clr
  Register #(.width(16)) R3 (.D(multiadder_16bit_1_r3), .clk(clock_1_out), .Q(R3_q));  // open: en, clr
  Register #(.width(16)) R4 (.D(multiadder_16bit_1_r4), .clk(clock_1_out), .Q(R4_q));  // open: en, clr
  Comparator comparator_6 (.a(8'h1), .b(counter_3_q), .eq(comparator_6_eq));  // open: gt, lt
  Comparator comparator_7 (.a(8'h2), .b(counter_3_q), .eq(comparator_7_eq));  // open: gt, lt
  Comparator comparator_8 (.a(8'h3), .b(counter_3_q), .eq(comparator_8_eq));  // open: gt, lt
  Comparator comparator_9 (.a(8'h4), .b(counter_3_q), .eq(comparator_9_eq));  // open: gt, lt
  assign controlled_buffer_1_out = comparator_6_eq ? R1_q : 16'bz;  // Controlled_Buffer controlled_buffer_1
  assign controlled_buffer_1_out = comparator_7_eq ? R2_q : 16'bz;  // Controlled_Buffer controlled_buffer_2
  assign controlled_buffer_1_out = comparator_8_eq ? R3_q : 16'bz;  // Controlled_Buffer controlled_buffer_3
  assign controlled_buffer_1_out = comparator_9_eq ? R4_q : 16'bz;  // Controlled_Buffer controlled_buffer_4
  Counter counter_3 (.Q(counter_3_q), .clk(clock_1_out), .clr(comparator_10_eq));  // open: load, D, count, carry, up
  Comparator comparator_10 (.a(8'h3), .b(counter_1_q), .eq(comparator_10_eq));  // open: gt, lt
  RAM #(.dataWidth(16)) ram_3 (
    .addr(counter_1_q), .clk(clock_1_out), .din(controlled_buffer_1_out));  // open: we, oe, dout

  // Notes on the sheet:
  //   Depreciated Aproach
endmodule
module ram2multiAdder_manual (
  input  d,
  input  c,
  input  b,
  input  a,
  input  z,
  input  y,
  input  x,
  input  w,
  input  Pass1,
  input  Pass2,
  input  Pass3,
  input  Pass4
);

  wire clock_1_out, or_1_out;
  wire [7:0] counter_1_q, counter_2_q;
  wire [15:0] A1_q, A2_q, A3_q, A4_q, B1_q, B2_q, B3_q, B4_q, controlled_buffer_1_out, multiadder_16bit_1_r1,
       multiadder_16bit_1_r2, multiadder_16bit_1_r3, multiadder_16bit_1_r4, R1_q, R2_q, R3_q, R4_q,
       ram_1_dout, ram_2_dout;

  Clock clock_1 (.out(clock_1_out));
  RAM #(.dataWidth(16), .\type ("nonvolatile")) ram_1 (
    .addr(counter_1_q), .clk(clock_1_out), .dout(ram_1_dout));  // open: we, oe, din
  Counter counter_1 (.Q(counter_1_q), .clk(clock_1_out));  // open: load, D, count, carry, up, clr
  RAM #(.dataWidth(16), .\type ("nonvolatile")) ram_2 (
    .addr(counter_1_q), .clk(clock_1_out), .dout(ram_2_dout));  // open: we, oe, din
  // Probe on ram_1_dout
  // Probe on ram_2_dout
  Register #(.width(16)) A1 (.D(ram_1_dout), .en(a), .clk(clock_1_out), .Q(A1_q));  // open: clr
  Register #(.width(16)) A2 (.D(ram_1_dout), .en(b), .clk(clock_1_out), .Q(A2_q));  // open: clr
  Register #(.width(16)) A3 (.D(ram_1_dout), .en(c), .clk(clock_1_out), .Q(A3_q));  // open: clr
  Register #(.width(16)) A4 (.D(ram_1_dout), .en(d), .clk(clock_1_out), .Q(A4_q));  // open: clr
  Register #(.width(16)) B1 (.D(ram_2_dout), .en(a), .clk(clock_1_out), .Q(B1_q));  // open: clr
  Register #(.width(16)) B2 (.D(ram_2_dout), .en(b), .clk(clock_1_out), .Q(B2_q));  // open: clr
  Register #(.width(16)) B3 (.D(ram_2_dout), .en(c), .clk(clock_1_out), .Q(B3_q));  // open: clr
  Register #(.width(16)) B4 (.D(ram_2_dout), .en(d), .clk(clock_1_out), .Q(B4_q));  // open: clr
  // Probe on B1_q
  // Probe on B2_q
  // Probe on A1_q
  // Probe on A2_q
  // Probe on A3_q
  // Probe on A4_q
  // Probe on B3_q
  // Probe on B4_q
  multiadder_16bit multiadder_16bit_1 (
    .A1(A1_q), .A2(A2_q), .A3(A3_q), .A4(A4_q), .B1(B1_q), .B2(B2_q), .B3(B3_q), .B4(B4_q),
    .R1(multiadder_16bit_1_r1), .R2(multiadder_16bit_1_r2), .R3(multiadder_16bit_1_r3),
    .R4(multiadder_16bit_1_r4));  // open: C1, C2, C3, C4
  // Probe on multiadder_16bit_1_r2
  // Probe on multiadder_16bit_1_r3
  // Probe on multiadder_16bit_1_r4
  // Probe on multiadder_16bit_1_r1
  Register #(.width(16)) R1 (.D(multiadder_16bit_1_r1), .en(w), .clk(clock_1_out), .Q(R1_q));  // open: clr
  Register #(.width(16)) R2 (.D(multiadder_16bit_1_r2), .en(x), .clk(clock_1_out), .Q(R2_q));  // open: clr
  Register #(.width(16)) R3 (.D(multiadder_16bit_1_r3), .en(y), .clk(clock_1_out), .Q(R3_q));  // open: clr
  Register #(.width(16)) R4 (.D(multiadder_16bit_1_r4), .en(z), .clk(clock_1_out), .Q(R4_q));  // open: clr
  assign controlled_buffer_1_out = Pass1 ? R1_q : 16'bz;  // Controlled_Buffer controlled_buffer_1
  assign controlled_buffer_1_out = Pass2 ? R2_q : 16'bz;  // Controlled_Buffer controlled_buffer_2
  assign controlled_buffer_1_out = Pass3 ? R3_q : 16'bz;  // Controlled_Buffer controlled_buffer_3
  assign controlled_buffer_1_out = Pass4 ? R4_q : 16'bz;  // Controlled_Buffer controlled_buffer_4
  or or_1 (or_1_out, Pass1, Pass2, Pass3, Pass4);
  RAM #(.dataWidth(16)) ram_3 (
    .addr(counter_2_q), .we(or_1_out), .clk(clock_1_out), .din(controlled_buffer_1_out));  // open: oe, dout
  Counter counter_2 (.count(or_1_out), .Q(counter_2_q), .clk(clock_1_out));  // open: load, D, carry, up, clr
endmodule

module ram2Adder_manual (
  input  in_1,
  input  in_2
);

  wire clock_1_out;
  wire [7:0] counter_1_q, counter_2_q;
  wire [15:0] adder_16bit_1_result, ram_1_dout, ram_2_dout, register_1_q, register_2_q, register_3_q;

  Clock clock_1 (.out(clock_1_out));
  // Probe on counter_1_q
  Counter counter_1 (.Q(counter_1_q), .clk(clock_1_out));  // open: load, D, count, carry, up, clr
  RAM #(.dataWidth(16), .\type ("nonvolatile")) ram_1 (
    .addr(counter_1_q), .clk(clock_1_out), .dout(ram_1_dout));  // open: we, oe, din
  RAM #(.dataWidth(16), .\type ("nonvolatile")) ram_2 (
    .addr(counter_1_q), .clk(clock_1_out), .dout(ram_2_dout));  // open: we, oe, din
  // Probe on ram_1_dout
  // Probe on ram_2_dout
  Register #(.width(16)) register_1 (.D(ram_1_dout), .en(in_1), .clk(clock_1_out), .Q(register_1_q));  // open: clr
  Register #(.width(16)) register_2 (.D(ram_2_dout), .en(in_1), .clk(clock_1_out), .Q(register_2_q));  // open: clr
  // Probe on adder_16bit_1_result
  adder_16bit adder_16bit_1 (
    .A(register_1_q), .B(register_2_q), .Result(adder_16bit_1_result));  // open: Carry_in, Carry_out
  Register #(.width(16)) register_3 (.D(adder_16bit_1_result), .clk(clock_1_out), .Q(register_3_q));  // open: en, clr
  RAM #(.dataWidth(16)) ram_3 (.addr(counter_2_q), .we(in_2), .clk(clock_1_out), .din(register_3_q));  // open: oe, dout
  Counter counter_2 (.Q(counter_2_q), .clk(clock_1_out));  // open: load, D, count, carry, up, clr
endmodule

module matmult_systrolicTiling_prot1 (
);

  wire clock_1_out, or_1_out, or_2_out, undriven_3, undriven_4, undriven_5, undriven_6, undriven_7,
       undriven_8, undriven_9, undriven_10, undriven_11, undriven_12, undriven_13, undriven_14, undriven_15,
       undriven_16;
  wire [3:0] undriven, undriven_2;
  wire [7:0] counter_1_q, counter_2_q, counter_3_q, counter_4_q;
  wire [15:0] A1_q, A2_q, A3_q, A4_q, adder_1_out, adder_2_out, adder_3_out, adder_4_out, B1_q, B2_q, B3_q,
       B4_q, C1_q, C2_q, C3_q, C4_q, C5_q, C6_q, C7_q, C8_q, C9_q, C10_q, C11_q, C12_q, C13_q, C14_q, C15_q,
       C16_q, controlled_buffer_1_out, ram_1_dout, ram_2_dout, ram_3_dout, register_1_q, register_2_q,
       register_3_q, register_4_q, register_5_q, register_6_q, register_7_q, register_8_q, register_9_q,
       systrolic_4x4gausian_1_c1, systrolic_4x4gausian_1_c2, systrolic_4x4gausian_1_c3,
       systrolic_4x4gausian_1_c4, systrolic_4x4gausian_1_c5, systrolic_4x4gausian_1_c6,
       systrolic_4x4gausian_1_c7, systrolic_4x4gausian_1_c8, systrolic_4x4gausian_1_c9,
       systrolic_4x4gausian_1_c10, systrolic_4x4gausian_1_c11, systrolic_4x4gausian_1_c12,
       systrolic_4x4gausian_1_c13, systrolic_4x4gausian_1_c14, systrolic_4x4gausian_1_c15,
       systrolic_4x4gausian_1_c16;
  wire [23:0] rom_1_data;

  or or_1 (or_1_out, rom_1_data[23], rom_1_data[22], rom_1_data[21], rom_1_data[20]);
  Counter counter_1 (.count(or_1_out), .Q(counter_1_q), .clk(clock_1_out));  // open: load, D, carry, up, clr
  Counter counter_2 (.count(or_1_out), .Q(counter_2_q), .clk(clock_1_out));  // open: load, D, carry, up, clr
  Clock clock_1 (.out(clock_1_out));
  RAM #(.dataWidth(16)) ram_1 (.addr(counter_1_q), .clk(clock_1_out), .dout(ram_1_dout));  // open: we, oe, din
  RAM #(.dataWidth(16)) ram_2 (.addr(counter_2_q), .clk(clock_1_out), .dout(ram_2_dout));  // open: we, oe, din
  Register #(.width(16)) A1 (.D(ram_1_dout), .en(rom_1_data[23]), .clk(clock_1_out), .Q(A1_q));  // open: clr
  Register #(.width(16)) A2 (.D(ram_1_dout), .en(rom_1_data[22]), .clk(clock_1_out), .Q(A2_q));  // open: clr
  Register #(.width(16)) A3 (.D(ram_1_dout), .en(rom_1_data[21]), .clk(clock_1_out), .Q(A3_q));  // open: clr
  Register #(.width(16)) A4 (.D(ram_1_dout), .en(rom_1_data[20]), .clk(clock_1_out), .Q(A4_q));  // open: clr
  Register #(.width(16)) B1 (.D(ram_2_dout), .en(rom_1_data[23]), .clk(clock_1_out), .Q(B1_q));  // open: clr
  Register #(.width(16)) B2 (.D(ram_2_dout), .en(rom_1_data[22]), .clk(clock_1_out), .Q(B2_q));  // open: clr
  Register #(.width(16)) B3 (.D(ram_2_dout), .en(rom_1_data[21]), .clk(clock_1_out), .Q(B3_q));  // open: clr
  Register #(.width(16)) B4 (.D(ram_2_dout), .en(rom_1_data[20]), .clk(clock_1_out), .Q(B4_q));  // open: clr
  systrolic_4x4Gausian systrolic_4x4gausian_1 (
    .B1(B1_q), .B2(B2_q), .B3(B3_q), .B4(B4_q), .A1(A1_q), .A2(A2_q), .A3(A3_q), .A4(A4_q),
    .Clock(clock_1_out), .C1(systrolic_4x4gausian_1_c1), .C2(systrolic_4x4gausian_1_c2),
    .C3(systrolic_4x4gausian_1_c3), .C4(systrolic_4x4gausian_1_c4), .C5(systrolic_4x4gausian_1_c5),
    .C6(systrolic_4x4gausian_1_c6), .C7(systrolic_4x4gausian_1_c7), .C8(systrolic_4x4gausian_1_c8),
    .C9(systrolic_4x4gausian_1_c9), .C10(systrolic_4x4gausian_1_c10), .C11(systrolic_4x4gausian_1_c11),
    .C12(systrolic_4x4gausian_1_c12), .C13(systrolic_4x4gausian_1_c13), .C14(systrolic_4x4gausian_1_c14),
    .C15(systrolic_4x4gausian_1_c15), .C16(systrolic_4x4gausian_1_c16));
  Register #(.width(16)) C1 (.D(systrolic_4x4gausian_1_c1), .Q(C1_q));  // open: en, clk, clr
  Register #(.width(16)) C3 (.D(systrolic_4x4gausian_1_c3), .Q(C3_q));  // open: en, clk, clr
  Register #(.width(16)) C5 (.D(systrolic_4x4gausian_1_c5), .Q(C5_q));  // open: en, clk, clr
  Register #(.width(16)) C7 (.D(systrolic_4x4gausian_1_c7), .Q(C7_q));  // open: en, clk, clr
  Register #(.width(16)) C9 (.D(systrolic_4x4gausian_1_c9), .Q(C9_q));  // open: en, clk, clr
  Register #(.width(16)) C11 (.D(systrolic_4x4gausian_1_c11), .Q(C11_q));  // open: en, clk, clr
  Register #(.width(16)) C13 (.D(systrolic_4x4gausian_1_c13), .Q(C13_q));  // open: en, clk, clr
  Register #(.width(16)) C15 (.D(systrolic_4x4gausian_1_c15), .Q(C15_q));  // open: en, clk, clr
  Register #(.width(16)) C2 (.D(systrolic_4x4gausian_1_c2), .Q(C2_q));  // open: en, clk, clr
  Register #(.width(16)) C4 (.D(systrolic_4x4gausian_1_c4), .Q(C4_q));  // open: en, clk, clr
  Register #(.width(16)) C6 (.D(systrolic_4x4gausian_1_c6), .Q(C6_q));  // open: en, clk, clr
  Register #(.width(16)) C8 (.D(systrolic_4x4gausian_1_c8), .Q(C8_q));  // open: en, clk, clr
  Register #(.width(16)) C10 (.D(systrolic_4x4gausian_1_c10), .Q(C10_q));  // open: en, clk, clr
  Register #(.width(16)) C12 (.D(systrolic_4x4gausian_1_c12), .Q(C12_q));  // open: en, clk, clr
  Register #(.width(16)) C14 (.D(systrolic_4x4gausian_1_c14), .Q(C14_q));  // open: en, clk, clr
  Register #(.width(16)) C16 (.D(systrolic_4x4gausian_1_c16), .Q(C16_q));  // open: en, clk, clr
  assign controlled_buffer_1_out = rom_1_data[19] ? C1_q : 16'bz;  // Controlled_Buffer controlled_buffer_1
  assign controlled_buffer_1_out = rom_1_data[18] ? C2_q : 16'bz;  // Controlled_Buffer controlled_buffer_2
  assign controlled_buffer_1_out = rom_1_data[17] ? C3_q : 16'bz;  // Controlled_Buffer controlled_buffer_3
  Hex_Digit_Display hex_digit_display_1 (.value(undriven_2));  // open: dp
  Hex_Digit_Display hex_digit_display_2 (.value(undriven));  // open: dp
  assign controlled_buffer_1_out = rom_1_data[16] ? C4_q : 16'bz;  // Controlled_Buffer controlled_buffer_4
  assign controlled_buffer_1_out = rom_1_data[15] ? C5_q : 16'bz;  // Controlled_Buffer controlled_buffer_5
  assign controlled_buffer_1_out = rom_1_data[14] ? C6_q : 16'bz;  // Controlled_Buffer controlled_buffer_6
  assign controlled_buffer_1_out = rom_1_data[13] ? C7_q : 16'bz;  // Controlled_Buffer controlled_buffer_7
  assign controlled_buffer_1_out = rom_1_data[12] ? C8_q : 16'bz;  // Controlled_Buffer controlled_buffer_8
  assign controlled_buffer_1_out = rom_1_data[11] ? C9_q : 16'bz;  // Controlled_Buffer controlled_buffer_9
  assign controlled_buffer_1_out = rom_1_data[10] ? C10_q : 16'bz;  // Controlled_Buffer controlled_buffer_10
  assign controlled_buffer_1_out = rom_1_data[9] ? C11_q : 16'bz;  // Controlled_Buffer controlled_buffer_11
  assign controlled_buffer_1_out = rom_1_data[8] ? C12_q : 16'bz;  // Controlled_Buffer controlled_buffer_12
  assign controlled_buffer_1_out = rom_1_data[7] ? C13_q : 16'bz;  // Controlled_Buffer controlled_buffer_13
  assign controlled_buffer_1_out = rom_1_data[6] ? C14_q : 16'bz;  // Controlled_Buffer controlled_buffer_14
  assign controlled_buffer_1_out = rom_1_data[5] ? C15_q : 16'bz;  // Controlled_Buffer controlled_buffer_15
  assign controlled_buffer_1_out = rom_1_data[4] ? C16_q : 16'bz;  // Controlled_Buffer controlled_buffer_16
  or or_2 (or_2_out, rom_1_data[4], rom_1_data[5], rom_1_data[6], rom_1_data[7], rom_1_data[8], rom_1_data[9], rom_1_data[10], rom_1_data[11], rom_1_data[12], rom_1_data[13], rom_1_data[14], rom_1_data[15], rom_1_data[16], rom_1_data[17], rom_1_data[18], rom_1_data[19]);
  Counter counter_3 (.Q(counter_3_q), .clk(clock_1_out));  // open: load, D, count, carry, up, clr
  Register #(.width(16)) register_1 (
    .D(controlled_buffer_1_out), .en(or_2_out), .clk(clock_1_out), .Q(register_1_q));  // open: clr
  ROM #(.dataWidth(24)) rom_1 (.addr(counter_3_q), .data(rom_1_data));
  Counter counter_4 (
    .count(rom_1_data[3]), .Q(counter_4_q), .clk(clock_1_out), .clr(undriven_3));  // open: load, D, carry, up
  RAM #(.dataWidth(16)) ram_3 (
    .addr(counter_4_q), .we(rom_1_data[3]), .oe(undriven_4), .clk(clock_1_out), .din(register_1_q),
    .dout(ram_3_dout));
  Register #(.width(16)) register_2 (
    .D(ram_3_dout), .en(undriven_5), .clk(clock_1_out), .Q(register_2_q));  // open: clr
  Register #(.width(16)) register_3 (
    .D(ram_3_dout), .en(undriven_6), .clk(clock_1_out), .Q(register_3_q));  // open: clr
  Register #(.width(16)) register_4 (
    .D(ram_3_dout), .en(undriven_7), .clk(clock_1_out), .Q(register_4_q));  // open: clr
  Register #(.width(16)) register_5 (
    .D(ram_3_dout), .en(undriven_8), .clk(clock_1_out), .Q(register_5_q));  // open: clr
  Register #(.width(16)) register_6 (
    .D(ram_3_dout), .en(undriven_9), .clk(clock_1_out), .Q(register_6_q));  // open: clr
  Register #(.width(16)) register_7 (
    .D(ram_3_dout), .en(undriven_10), .clk(clock_1_out), .Q(register_7_q));  // open: clr
  Register #(.width(16)) register_8 (
    .D(ram_3_dout), .en(undriven_11), .clk(clock_1_out), .Q(register_8_q));  // open: clr
  Register #(.width(16)) register_9 (
    .D(ram_3_dout), .en(undriven_12), .clk(clock_1_out), .Q(register_9_q));  // open: clr
  Adder #(.width(16)) adder_1 (.a(register_2_q), .b(register_6_q), .out(adder_1_out));  // open: cin, cout
  Adder #(.width(16)) adder_2 (.a(register_3_q), .b(register_7_q), .out(adder_2_out));  // open: cin, cout
  Adder #(.width(16)) adder_3 (.a(register_4_q), .b(register_8_q), .out(adder_3_out));  // open: cin, cout
  Adder #(.width(16)) adder_4 (.a(register_5_q), .b(register_9_q), .out(adder_4_out));  // open: cin, cout
  Register #(.width(16)) register_10 (.D(adder_1_out), .en(undriven_13), .clk(clock_1_out));  // open: Q, clr
  Register #(.width(16)) register_11 (.D(adder_2_out), .en(undriven_14), .clk(clock_1_out));  // open: Q, clr
  Register #(.width(16)) register_12 (.D(adder_3_out), .en(undriven_15), .clk(clock_1_out));  // open: Q, clr
  Register #(.width(16)) register_13 (.D(adder_4_out), .en(undriven_16), .clk(clock_1_out));  // open: Q, clr

  // Notes on the sheet:
  //   Not working Invalid aproach!!
endmodule

module InstructionDecoder_dep (
  input  [15:0] Instruction,
  input  Nor_Global,
  input  clock,
  input  Or_A,
  input  Or_B,
  input  StoC_Line,
  input  Reset_Line,
  output [7:0] Counter_A,
  output [7:0] Counter_B,
  output [7:0] Counter_C,
  output [7:0] Counter_Rom
);

  wire comparator_1_gt, not_1_out, not_2_out, not_3_out, or_1_out;
  wire [3:0] ins_splitter_1_dimension, ins_splitter_1_opcode;
  wire [7:0] bit_extender_1_out, bit_extender_2_out, counter_4_q, ins_splitter_1_adress, multiplier_1_out;

  Ins_splitter ins_splitter_1 (
    .Instruction(Instruction), .WE(Nor_Global), .Clock(clock), .Adress(ins_splitter_1_adress),
    .Dimension(ins_splitter_1_dimension), .Opcode(ins_splitter_1_opcode));
  not not_1 (not_1_out, Or_A);
  not not_2 (not_2_out, Or_B);
  not not_3 (not_3_out, StoC_Line);
  assign bit_extender_1_out = {{4{ins_splitter_1_dimension[3]}}, ins_splitter_1_dimension};  // Bit_Extender bit_extender_1
  Counter counter_1 (
    .load(not_1_out), .D(ins_splitter_1_adress), .count(Or_A), .Q(Counter_A), .clk(clock));  // open: carry, up, clr
  Counter counter_2 (
    .load(not_2_out), .D(ins_splitter_1_adress), .count(Or_B), .Q(Counter_B), .clk(clock));  // open: carry, up, clr
  Counter counter_3 (
    .load(not_3_out), .D(ins_splitter_1_adress), .Q(Counter_C), .clk(clock));  // open: count, carry, up, clr
  Comparator comparator_1 (.a(counter_4_q), .b(bit_extender_1_out), .gt(comparator_1_gt));  // open: eq, lt
  assign bit_extender_2_out = {{4{ins_splitter_1_opcode[3]}}, ins_splitter_1_opcode};  // Bit_Extender bit_extender_2
  Counter counter_4 (.D({8{1'b1}}), .Q(counter_4_q), .clk(clock), .clr(or_1_out));  // open: load, count, carry, up
  or or_1 (or_1_out, comparator_1_gt, Reset_Line);
  Multiplier multiplier_1 (.a(bit_extender_2_out), .b(8'h10), .out(multiplier_1_out));  // open: cin, cout
  Adder adder_1 (.a(multiplier_1_out), .b(counter_4_q), .out(Counter_Rom));  // open: cin, cout
endmodule

module Ins_splitter (
  input  [15:0] Instruction,
  input  WE,
  input  Clock,
  output [7:0] Adress,
  output [3:0] Dimension,
  output [3:0] Opcode
);

  Register #(.trigger("falling"), .width(16)) register_1 (
    .D(Instruction), .en(WE), .clk(Clock), .Q({Opcode, Dimension, Adress}));  // open: clr
endmodule

module registerBanks_16 (
  input  [15:0] Value,
  input  WE1,
  input  WE2,
  input  WE3,
  input  WE4,
  input  WE5,
  input  WE6,
  input  WE7,
  input  WE8,
  input  WE9,
  input  WE10,
  input  WE11,
  input  WE12,
  input  WE13,
  input  WE14,
  input  WE15,
  input  WE16,
  input  clock,
  output [15:0] R1,
  output [15:0] R2,
  output [15:0] R3,
  output [15:0] R4,
  output [15:0] R5,
  output [15:0] R6,
  output [15:0] R7,
  output [15:0] R8,
  output [15:0] R9,
  output [15:0] R10,
  output [15:0] R11,
  output [15:0] R12,
  output [15:0] R13,
  output [15:0] R14,
  output [15:0] R15,
  output [15:0] R16
);

  Register #(.width(16)) register_1 (.D(Value), .en(WE1), .clk(clock), .Q(R1));  // open: clr
  Register #(.width(16)) register_2 (.D(Value), .en(WE3), .clk(clock), .Q(R3));  // open: clr
  Register #(.width(16)) register_3 (.D(Value), .en(WE5), .clk(clock), .Q(R5));  // open: clr
  Register #(.width(16)) register_4 (.D(Value), .en(WE7), .clk(clock), .Q(R7));  // open: clr
  Register #(.width(16)) register_5 (.D(Value), .en(WE9), .clk(clock), .Q(R9));  // open: clr
  Register #(.width(16)) register_6 (.D(Value), .en(WE11), .clk(clock), .Q(R11));  // open: clr
  Register #(.width(16)) register_7 (.D(Value), .en(WE13), .clk(clock), .Q(R13));  // open: clr
  Register #(.width(16)) register_8 (.D(Value), .en(WE15), .clk(clock), .Q(R15));  // open: clr
  Register #(.width(16)) register_9 (.D(Value), .en(WE2), .clk(clock), .Q(R2));  // open: clr
  Register #(.width(16)) register_10 (.D(Value), .en(WE4), .clk(clock), .Q(R4));  // open: clr
  Register #(.width(16)) register_11 (.D(Value), .en(WE6), .clk(clock), .Q(R6));  // open: clr
  Register #(.width(16)) register_12 (.D(Value), .en(WE8), .clk(clock), .Q(R8));  // open: clr
  Register #(.width(16)) register_13 (.D(Value), .en(WE10), .clk(clock), .Q(R10));  // open: clr
  Register #(.width(16)) register_14 (.D(Value), .en(WE12), .clk(clock), .Q(R12));  // open: clr
  Register #(.width(16)) register_15 (.D(Value), .en(WE14), .clk(clock), .Q(R14));  // open: clr
  Register #(.width(16)) register_16 (.D(Value), .en(WE16), .clk(clock), .Q(R16));  // open: clr
endmodule

module registerBanks_4 (
  input  [15:0] value,
  input  WE1,
  input  WE2,
  input  WE3,
  input  WE4,
  input  clock,
  input  reset,
  output [15:0] out1,
  output [15:0] out2,
  output [15:0] out3,
  output [15:0] out4
);

  Register #(.width(16)) register_1 (.D(value), .en(WE1), .clk(clock), .Q(out1), .clr(reset));
  Register #(.width(16)) register_2 (.D(value), .en(WE2), .clk(clock), .Q(out2), .clr(reset));
  Register #(.width(16)) register_3 (.D(value), .en(WE3), .clk(clock), .Q(out3), .clr(reset));
  Register #(.width(16)) register_4 (.D(value), .en(WE4), .clk(clock), .Q(out4), .clr(reset));
endmodule

module systrolic_4x4Gausian (
  input  [15:0] B1,
  input  [15:0] B2,
  input  [15:0] B3,
  input  [15:0] B4,
  input  [15:0] A1,
  input  [15:0] A2,
  input  [15:0] A3,
  input  [15:0] A4,
  input  Clock,
  output [15:0] C1,
  output [15:0] C2,
  output [15:0] C3,
  output [15:0] C4,
  output [15:0] C5,
  output [15:0] C6,
  output [15:0] C7,
  output [15:0] C8,
  output [15:0] C9,
  output [15:0] C10,
  output [15:0] C11,
  output [15:0] C12,
  output [15:0] C13,
  output [15:0] C14,
  output [15:0] C15,
  output [15:0] C16
);

  wire [15:0] systrolic_processingelement_1_aout, systrolic_processingelement_1_bout,
       systrolic_processingelement_2_aout, systrolic_processingelement_2_bout,
       systrolic_processingelement_3_aout, systrolic_processingelement_3_bout,
       systrolic_processingelement_4_aout, systrolic_processingelement_5_aout,
       systrolic_processingelement_5_bout, systrolic_processingelement_6_aout,
       systrolic_processingelement_6_bout, systrolic_processingelement_7_aout,
       systrolic_processingelement_7_bout, systrolic_processingelement_8_aout,
       systrolic_processingelement_9_aout, systrolic_processingelement_9_bout,
       systrolic_processingelement_10_aout, systrolic_processingelement_10_bout,
       systrolic_processingelement_11_aout, systrolic_processingelement_11_bout,
       systrolic_processingelement_12_aout, systrolic_processingelement_13_bout,
       systrolic_processingelement_14_bout, systrolic_processingelement_15_bout;

  Systrolic_ProcessingElement systrolic_processingelement_1 (
    .Ain(A1), .Bin(B1), .Clock(Clock), .Aout(systrolic_processingelement_1_aout),
    .Bout(systrolic_processingelement_1_bout), .Cout(C1));
  Systrolic_ProcessingElement systrolic_processingelement_2 (
    .Ain(A2), .Bin(systrolic_processingelement_1_bout), .Clock(Clock),
    .Aout(systrolic_processingelement_2_aout), .Bout(systrolic_processingelement_2_bout), .Cout(C5));
  Systrolic_ProcessingElement systrolic_processingelement_3 (
    .Ain(A3), .Bin(systrolic_processingelement_2_bout), .Clock(Clock),
    .Aout(systrolic_processingelement_3_aout), .Bout(systrolic_processingelement_3_bout), .Cout(C9));
  Systrolic_ProcessingElement systrolic_processingelement_4 (
    .Ain(A4), .Bin(systrolic_processingelement_3_bout), .Clock(Clock),
    .Aout(systrolic_processingelement_4_aout), .Cout(C13));  // open: Bout
  Systrolic_ProcessingElement systrolic_processingelement_5 (
    .Ain(systrolic_processingelement_1_aout), .Bin(B2), .Clock(Clock),
    .Aout(systrolic_processingelement_5_aout), .Bout(systrolic_processingelement_5_bout), .Cout(C2));
  Systrolic_ProcessingElement systrolic_processingelement_6 (
    .Ain(systrolic_processingelement_2_aout), .Bin(systrolic_processingelement_5_bout), .Clock(Clock),
    .Aout(systrolic_processingelement_6_aout), .Bout(systrolic_processingelement_6_bout), .Cout(C6));
  Systrolic_ProcessingElement systrolic_processingelement_7 (
    .Ain(systrolic_processingelement_3_aout), .Bin(systrolic_processingelement_6_bout), .Clock(Clock),
    .Aout(systrolic_processingelement_7_aout), .Bout(systrolic_processingelement_7_bout), .Cout(C10));
  Systrolic_ProcessingElement systrolic_processingelement_8 (
    .Ain(systrolic_processingelement_4_aout), .Bin(systrolic_processingelement_7_bout), .Clock(Clock),
    .Aout(systrolic_processingelement_8_aout), .Cout(C14));  // open: Bout
  Systrolic_ProcessingElement systrolic_processingelement_9 (
    .Ain(systrolic_processingelement_5_aout), .Bin(B3), .Clock(Clock),
    .Aout(systrolic_processingelement_9_aout), .Bout(systrolic_processingelement_9_bout), .Cout(C3));
  Systrolic_ProcessingElement systrolic_processingelement_10 (
    .Ain(systrolic_processingelement_6_aout), .Bin(systrolic_processingelement_9_bout), .Clock(Clock),
    .Aout(systrolic_processingelement_10_aout), .Bout(systrolic_processingelement_10_bout), .Cout(C7));
  Systrolic_ProcessingElement systrolic_processingelement_11 (
    .Ain(systrolic_processingelement_7_aout), .Bin(systrolic_processingelement_10_bout), .Clock(Clock),
    .Aout(systrolic_processingelement_11_aout), .Bout(systrolic_processingelement_11_bout), .Cout(C11));
  Systrolic_ProcessingElement systrolic_processingelement_12 (
    .Ain(systrolic_processingelement_8_aout), .Bin(systrolic_processingelement_11_bout), .Clock(Clock),
    .Aout(systrolic_processingelement_12_aout), .Cout(C15));  // open: Bout
  Systrolic_ProcessingElement systrolic_processingelement_13 (
    .Ain(systrolic_processingelement_9_aout), .Bin(B4), .Clock(Clock),
    .Bout(systrolic_processingelement_13_bout), .Cout(C4));  // open: Aout
  Systrolic_ProcessingElement systrolic_processingelement_14 (
    .Ain(systrolic_processingelement_10_aout), .Bin(systrolic_processingelement_13_bout), .Clock(Clock),
    .Bout(systrolic_processingelement_14_bout), .Cout(C8));  // open: Aout
  Systrolic_ProcessingElement systrolic_processingelement_15 (
    .Ain(systrolic_processingelement_11_aout), .Bin(systrolic_processingelement_14_bout), .Clock(Clock),
    .Bout(systrolic_processingelement_15_bout), .Cout(C12));  // open: Aout
  Systrolic_ProcessingElement systrolic_processingelement_16 (
    .Ain(systrolic_processingelement_12_aout), .Bin(systrolic_processingelement_15_bout), .Clock(Clock),
    .Cout(C16));  // open: Aout, Bout
endmodule

module matmult_tiling_4x4_core (
  input  [15:0] A1,
  input  [15:0] A2,
  input  [15:0] A3,
  input  [15:0] A4,
  input  [15:0] A5,
  input  [15:0] A6,
  input  [15:0] A7,
  input  [15:0] A8,
  input  [15:0] A9,
  input  [15:0] A10,
  input  [15:0] A11,
  input  [15:0] A12,
  input  [15:0] A13,
  input  [15:0] A14,
  input  [15:0] A15,
  input  [15:0] A16,
  input  [15:0] B1,
  input  [15:0] B2,
  input  [15:0] B3,
  input  [15:0] B4,
  input  [15:0] B5,
  input  [15:0] B6,
  input  [15:0] B7,
  input  [15:0] B8,
  input  [15:0] B9,
  input  [15:0] B10,
  input  [15:0] B11,
  input  [15:0] B12,
  input  [15:0] B13,
  input  [15:0] B14,
  input  [15:0] B15,
  input  [15:0] B16,
  output [15:0] C1,
  output [15:0] C2,
  output [15:0] C3,
  output [15:0] C4,
  output [15:0] C5,
  output [15:0] C6,
  output [15:0] C7,
  output [15:0] C8,
  output [15:0] C9,
  output [15:0] C10,
  output [15:0] C11,
  output [15:0] C12,
  output [15:0] C13,
  output [15:0] C14,
  output [15:0] C15,
  output [15:0] C16
);

  wire [15:0] adder_1_out, adder_2_out, adder_3_out, adder_4_out, adder_5_out, adder_6_out, adder_7_out,
       adder_8_out, adder_9_out, adder_10_out, adder_11_out, adder_12_out, adder_13_out, adder_14_out,
       adder_15_out, adder_16_out, adder_17_out, adder_18_out, adder_19_out, adder_20_out, adder_21_out,
       adder_22_out, adder_23_out, adder_24_out, adder_25_out, adder_26_out, adder_27_out, adder_28_out,
       adder_29_out, adder_30_out, adder_31_out, adder_32_out, multiplier_1_out, multiplier_2_out,
       multiplier_3_out, multiplier_4_out, multiplier_5_out, multiplier_6_out, multiplier_7_out,
       multiplier_8_out, multiplier_9_out, multiplier_10_out, multiplier_11_out, multiplier_12_out,
       multiplier_13_out, multiplier_14_out, multiplier_15_out, multiplier_16_out, multiplier_17_out,
       multiplier_18_out, multiplier_19_out, multiplier_20_out, multiplier_21_out, multiplier_22_out,
       multiplier_23_out, multiplier_24_out, multiplier_25_out, multiplier_26_out, multiplier_27_out,
       multiplier_28_out, multiplier_29_out, multiplier_30_out, multiplier_31_out, multiplier_32_out,
       multiplier_33_out, multiplier_34_out, multiplier_35_out, multiplier_36_out, multiplier_37_out,
       multiplier_38_out, multiplier_39_out, multiplier_40_out, multiplier_41_out, multiplier_42_out,
       multiplier_43_out, multiplier_44_out, multiplier_45_out, multiplier_46_out, multiplier_47_out,
       multiplier_48_out, multiplier_49_out, multiplier_50_out, multiplier_51_out, multiplier_52_out,
       multiplier_53_out, multiplier_54_out, multiplier_55_out, multiplier_56_out, multiplier_57_out,
       multiplier_58_out, multiplier_59_out, multiplier_60_out, multiplier_61_out, multiplier_62_out,
       multiplier_63_out, multiplier_64_out;

  Multiplier #(.width(16)) multiplier_1 (.a(A1), .b(B1), .out(multiplier_1_out));  // open: cin, cout
  Multiplier #(.width(16)) multiplier_2 (.a(A2), .b(B5), .out(multiplier_2_out));  // open: cin, cout
  Multiplier #(.width(16)) multiplier_3 (.a(A3), .b(B9), .out(multiplier_3_out));  // open: cin, cout
  Multiplier #(.width(16)) multiplier_4 (.a(A4), .b(B13), .out(multiplier_4_out));  // open: cin, cout
  Multiplier #(.width(16)) multiplier_5 (.a(A1), .b(B2), .out(multiplier_5_out));  // open: cin, cout
  Multiplier #(.width(16)) multiplier_6 (.a(A2), .b(B6), .out(multiplier_6_out));  // open: cin, cout
  Multiplier #(.width(16)) multiplier_7 (.a(A3), .b(B10), .out(multiplier_7_out));  // open: cin, cout
  Multiplier #(.width(16)) multiplier_8 (.a(A4), .b(B14), .out(multiplier_8_out));  // open: cin, cout
  Multiplier #(.width(16)) multiplier_9 (.a(A1), .b(B3), .out(multiplier_9_out));  // open: cin, cout
  Multiplier #(.width(16)) multiplier_10 (.a(A2), .b(B7), .out(multiplier_10_out));  // open: cin, cout
  Multiplier #(.width(16)) multiplier_11 (.a(A3), .b(B11), .out(multiplier_11_out));  // open: cin, cout
  Multiplier #(.width(16)) multiplier_12 (.a(A4), .b(B15), .out(multiplier_12_out));  // open: cin, cout
  Multiplier #(.width(16)) multiplier_13 (.a(A1), .b(B4), .out(multiplier_13_out));  // open: cin, cout
  Multiplier #(.width(16)) multiplier_14 (.a(A2), .b(B8), .out(multiplier_14_out));  // open: cin, cout
  Multiplier #(.width(16)) multiplier_15 (.a(A3), .b(B12), .out(multiplier_15_out));  // open: cin, cout
  Multiplier #(.width(16)) multiplier_16 (.a(A4), .b(B16), .out(multiplier_16_out));  // open: cin, cout
  Multiplier #(.width(16)) multiplier_17 (.a(A5), .b(B1), .out(multiplier_17_out));  // open: cin, cout
  Multiplier #(.width(16)) multiplier_18 (.a(A6), .b(B5), .out(multiplier_18_out));  // open: cin, cout
  Multiplier #(.width(16)) multiplier_19 (.a(A7), .b(B9), .out(multiplier_19_out));  // open: cin, cout
  Multiplier #(.width(16)) multiplier_20 (.a(A8), .b(B13), .out(multiplier_20_out));  // open: cin, cout
  Multiplier #(.width(16)) multiplier_21 (.a(A5), .b(B2), .out(multiplier_21_out));  // open: cin, cout
  Multiplier #(.width(16)) multiplier_22 (.a(A6), .b(B6), .out(multiplier_22_out));  // open: cin, cout
  Multiplier #(.width(16)) multiplier_23 (.a(A7), .b(B10), .out(multiplier_23_out));  // open: cin, cout
  Multiplier #(.width(16)) multiplier_24 (.a(A8), .b(B14), .out(multiplier_24_out));  // open: cin, cout
  Multiplier #(.width(16)) multiplier_25 (.a(A5), .b(B3), .out(multiplier_25_out));  // open: cin, cout
  Multiplier #(.width(16)) multiplier_26 (.a(A6), .b(B7), .out(multiplier_26_out));  // open: cin, cout
  Multiplier #(.width(16)) multiplier_27 (.a(A7), .b(B11), .out(multiplier_27_out));  // open: cin, cout
  Multiplier #(.width(16)) multiplier_28 (.a(A8), .b(B15), .out(multiplier_28_out));  // open: cin, cout
  Multiplier #(.width(16)) multiplier_29 (.a(A5), .b(B4), .out(multiplier_29_out));  // open: cin, cout
  Multiplier #(.width(16)) multiplier_30 (.a(A6), .b(B8), .out(multiplier_30_out));  // open: cin, cout
  Multiplier #(.width(16)) multiplier_31 (.a(A7), .b(B12), .out(multiplier_31_out));  // open: cin, cout
  Multiplier #(.width(16)) multiplier_32 (.a(A8), .b(B16), .out(multiplier_32_out));  // open: cin, cout
  Multiplier #(.width(16)) multiplier_33 (.a(A9), .b(B1), .out(multiplier_33_out));  // open: cin, cout
  Multiplier #(.width(16)) multiplier_34 (.a(A10), .b(B5), .out(multiplier_34_out));  // open: cin, cout
  Multiplier #(.width(16)) multiplier_35 (.a(A11), .b(B9), .out(multiplier_35_out));  // open: cin, cout
  Multiplier #(.width(16)) multiplier_36 (.a(A12), .b(B13), .out(multiplier_36_out));  // open: cin, cout
  Multiplier #(.width(16)) multiplier_37 (.a(A9), .b(B2), .out(multiplier_37_out));  // open: cin, cout
  Multiplier #(.width(16)) multiplier_38 (.a(A10), .b(B6), .out(multiplier_38_out));  // open: cin, cout
  Multiplier #(.width(16)) multiplier_39 (.a(A11), .b(B10), .out(multiplier_39_out));  // open: cin, cout
  Multiplier #(.width(16)) multiplier_40 (.a(A12), .b(B14), .out(multiplier_40_out));  // open: cin, cout
  Multiplier #(.width(16)) multiplier_41 (.a(A9), .b(B3), .out(multiplier_41_out));  // open: cin, cout
  Multiplier #(.width(16)) multiplier_42 (.a(A10), .b(B7), .out(multiplier_42_out));  // open: cin, cout
  Multiplier #(.width(16)) multiplier_43 (.a(A11), .b(B11), .out(multiplier_43_out));  // open: cin, cout
  Multiplier #(.width(16)) multiplier_44 (.a(A12), .b(B15), .out(multiplier_44_out));  // open: cin, cout
  Multiplier #(.width(16)) multiplier_45 (.a(A9), .b(B4), .out(multiplier_45_out));  // open: cin, cout
  Multiplier #(.width(16)) multiplier_46 (.a(A10), .b(B8), .out(multiplier_46_out));  // open: cin, cout
  Multiplier #(.width(16)) multiplier_47 (.a(A11), .b(B12), .out(multiplier_47_out));  // open: cin, cout
  Multiplier #(.width(16)) multiplier_48 (.a(A12), .b(B16), .out(multiplier_48_out));  // open: cin, cout
  Multiplier #(.width(16)) multiplier_49 (.a(A13), .b(B1), .out(multiplier_49_out));  // open: cin, cout
  Multiplier #(.width(16)) multiplier_50 (.a(A14), .b(B5), .out(multiplier_50_out));  // open: cin, cout
  Multiplier #(.width(16)) multiplier_51 (.a(A15), .b(B9), .out(multiplier_51_out));  // open: cin, cout
  Multiplier #(.width(16)) multiplier_52 (.a(A16), .b(B13), .out(multiplier_52_out));  // open: cin, cout
  Multiplier #(.width(16)) multiplier_53 (.a(A13), .b(B2), .out(multiplier_53_out));  // open: cin, cout
  Multiplier #(.width(16)) multiplier_54 (.a(A14), .b(B6), .out(multiplier_54_out));  // open: cin, cout
  Multiplier #(.width(16)) multiplier_55 (.a(A15), .b(B10), .out(multiplier_55_out));  // open: cin, cout
  Multiplier #(.width(16)) multiplier_56 (.a(A16), .b(B14), .out(multiplier_56_out));  // open: cin, cout
  Multiplier #(.width(16)) multiplier_57 (.a(A13), .b(B3), .out(multiplier_57_out));  // open: cin, cout
  Multiplier #(.width(16)) multiplier_58 (.a(A14), .b(B7), .out(multiplier_58_out));  // open: cin, cout
  Multiplier #(.width(16)) multiplier_59 (.a(A15), .b(B11), .out(multiplier_59_out));  // open: cin, cout
  Multiplier #(.width(16)) multiplier_60 (.a(A16), .b(B15), .out(multiplier_60_out));  // open: cin, cout
  Multiplier #(.width(16)) multiplier_61 (.a(A13), .b(B4), .out(multiplier_61_out));  // open: cin, cout
  Multiplier #(.width(16)) multiplier_62 (.a(A14), .b(B8), .out(multiplier_62_out));  // open: cin, cout
  Multiplier #(.width(16)) multiplier_63 (.a(A15), .b(B12), .out(multiplier_63_out));  // open: cin, cout
  Multiplier #(.width(16)) multiplier_64 (.a(A16), .b(B16), .out(multiplier_64_out));  // open: cin, cout
  Adder #(.width(16)) adder_1 (.a(multiplier_1_out), .b(multiplier_2_out), .out(adder_1_out));  // open: cin, cout
  Adder #(.width(16)) adder_2 (.a(multiplier_3_out), .b(multiplier_4_out), .out(adder_2_out));  // open: cin, cout
  Adder #(.width(16)) adder_3 (.a(multiplier_5_out), .b(multiplier_6_out), .out(adder_3_out));  // open: cin, cout
  Adder #(.width(16)) adder_4 (.a(multiplier_7_out), .b(multiplier_8_out), .out(adder_4_out));  // open: cin, cout
  Adder #(.width(16)) adder_5 (.a(multiplier_9_out), .b(multiplier_10_out), .out(adder_5_out));  // open: cin, cout
  Adder #(.width(16)) adder_6 (.a(multiplier_11_out), .b(multiplier_12_out), .out(adder_6_out));  // open: cin, cout
  Adder #(.width(16)) adder_7 (.a(multiplier_13_out), .b(multiplier_14_out), .out(adder_7_out));  // open: cin, cout
  Adder #(.width(16)) adder_8 (.a(multiplier_15_out), .b(multiplier_16_out), .out(adder_8_out));  // open: cin, cout
  Adder #(.width(16)) adder_9 (.a(multiplier_17_out), .b(multiplier_18_out), .out(adder_9_out));  // open: cin, cout
  Adder #(.width(16)) adder_10 (.a(multiplier_19_out), .b(multiplier_20_out), .out(adder_10_out));  // open: cin, cout
  Adder #(.width(16)) adder_11 (.a(multiplier_21_out), .b(multiplier_22_out), .out(adder_11_out));  // open: cin, cout
  Adder #(.width(16)) adder_12 (.a(multiplier_23_out), .b(multiplier_24_out), .out(adder_12_out));  // open: cin, cout
  Adder #(.width(16)) adder_13 (.a(multiplier_25_out), .b(multiplier_26_out), .out(adder_13_out));  // open: cin, cout
  Adder #(.width(16)) adder_14 (.a(multiplier_27_out), .b(multiplier_28_out), .out(adder_14_out));  // open: cin, cout
  Adder #(.width(16)) adder_15 (.a(multiplier_29_out), .b(multiplier_30_out), .out(adder_15_out));  // open: cin, cout
  Adder #(.width(16)) adder_16 (.a(multiplier_31_out), .b(multiplier_32_out), .out(adder_16_out));  // open: cin, cout
  Adder #(.width(16)) adder_17 (.a(multiplier_33_out), .b(multiplier_34_out), .out(adder_17_out));  // open: cin, cout
  Adder #(.width(16)) adder_18 (.a(multiplier_35_out), .b(multiplier_36_out), .out(adder_18_out));  // open: cin, cout
  Adder #(.width(16)) adder_19 (.a(multiplier_37_out), .b(multiplier_38_out), .out(adder_19_out));  // open: cin, cout
  Adder #(.width(16)) adder_20 (.a(multiplier_39_out), .b(multiplier_40_out), .out(adder_20_out));  // open: cin, cout
  Adder #(.width(16)) adder_21 (.a(multiplier_41_out), .b(multiplier_42_out), .out(adder_21_out));  // open: cin, cout
  Adder #(.width(16)) adder_22 (.a(multiplier_43_out), .b(multiplier_44_out), .out(adder_22_out));  // open: cin, cout
  Adder #(.width(16)) adder_23 (.a(multiplier_45_out), .b(multiplier_46_out), .out(adder_23_out));  // open: cin, cout
  Adder #(.width(16)) adder_24 (.a(multiplier_47_out), .b(multiplier_48_out), .out(adder_24_out));  // open: cin, cout
  Adder #(.width(16)) adder_25 (.a(multiplier_49_out), .b(multiplier_50_out), .out(adder_25_out));  // open: cin, cout
  Adder #(.width(16)) adder_26 (.a(multiplier_51_out), .b(multiplier_52_out), .out(adder_26_out));  // open: cin, cout
  Adder #(.width(16)) adder_27 (.a(multiplier_53_out), .b(multiplier_54_out), .out(adder_27_out));  // open: cin, cout
  Adder #(.width(16)) adder_28 (.a(multiplier_55_out), .b(multiplier_56_out), .out(adder_28_out));  // open: cin, cout
  Adder #(.width(16)) adder_29 (.a(multiplier_57_out), .b(multiplier_58_out), .out(adder_29_out));  // open: cin, cout
  Adder #(.width(16)) adder_30 (.a(multiplier_59_out), .b(multiplier_60_out), .out(adder_30_out));  // open: cin, cout
  Adder #(.width(16)) adder_31 (.a(multiplier_61_out), .b(multiplier_62_out), .out(adder_31_out));  // open: cin, cout
  Adder #(.width(16)) adder_32 (.a(multiplier_63_out), .b(multiplier_64_out), .out(adder_32_out));  // open: cin, cout
  Adder #(.width(16)) adder_33 (.a(adder_1_out), .b(adder_2_out), .out(C1));  // open: cin, cout
  Adder #(.width(16)) adder_34 (.a(adder_3_out), .b(adder_4_out), .out(C2));  // open: cin, cout
  Adder #(.width(16)) adder_35 (.a(adder_5_out), .b(adder_6_out), .out(C3));  // open: cin, cout
  Adder #(.width(16)) adder_36 (.a(adder_7_out), .b(adder_8_out), .out(C4));  // open: cin, cout
  Adder #(.width(16)) adder_37 (.a(adder_9_out), .b(adder_10_out), .out(C5));  // open: cin, cout
  Adder #(.width(16)) adder_38 (.a(adder_11_out), .b(adder_12_out), .out(C6));  // open: cin, cout
  Adder #(.width(16)) adder_39 (.a(adder_13_out), .b(adder_14_out), .out(C7));  // open: cin, cout
  Adder #(.width(16)) adder_40 (.a(adder_15_out), .b(adder_16_out), .out(C8));  // open: cin, cout
  Adder #(.width(16)) adder_41 (.a(adder_17_out), .b(adder_18_out), .out(C9));  // open: cin, cout
  Adder #(.width(16)) adder_42 (.a(adder_19_out), .b(adder_20_out), .out(C10));  // open: cin, cout
  Adder #(.width(16)) adder_43 (.a(adder_21_out), .b(adder_22_out), .out(C11));  // open: cin, cout
  Adder #(.width(16)) adder_44 (.a(adder_23_out), .b(adder_24_out), .out(C12));  // open: cin, cout
  Adder #(.width(16)) adder_45 (.a(adder_25_out), .b(adder_26_out), .out(C13));  // open: cin, cout
  Adder #(.width(16)) adder_46 (.a(adder_27_out), .b(adder_28_out), .out(C14));  // open: cin, cout
  Adder #(.width(16)) adder_47 (.a(adder_29_out), .b(adder_30_out), .out(C15));  // open: cin, cout
  Adder #(.width(16)) adder_48 (.a(adder_31_out), .b(adder_32_out), .out(C16));  // open: cin, cout
endmodule

module Systrolic_ProcessingElement (
  input  [15:0] Ain,
  input  [15:0] Bin,
  input  Clock,
  output [15:0] Aout,
  output [15:0] Bout,
  output [15:0] Cout
);

  wire [15:0] adder_1_out, multiplier_1_out;

  Multiplier #(.width(16)) multiplier_1 (.a(Ain), .b(Bin), .out(multiplier_1_out));  // open: cin, cout
  Register #(.trigger("falling"), .width(16)) register_1 (.D(Ain), .en(1'b1), .clk(Clock), .Q(Aout));  // open: clr
  Register #(.trigger("falling"), .width(16)) register_2 (.D(Bin), .en(1'b1), .clk(Clock), .Q(Bout));  // open: clr
  Register #(.trigger("falling"), .width(16)) register_3 (
    .D(adder_1_out), .en(1'b1), .clk(Clock), .Q(Cout));  // open: clr
  Adder #(.width(16)) adder_1 (.a(multiplier_1_out), .b(Cout), .out(adder_1_out));  // open: cin, cout
endmodule

module matMultTile_2x2 (
  input  [15:0] A1,
  input  [15:0] B1,
  input  [15:0] A2,
  input  [15:0] B3,
  input  [15:0] B2,
  input  [15:0] B4,
  input  [15:0] A3,
  input  [15:0] A4,
  output [15:0] C1,
  output [15:0] C2,
  output [15:0] C3,
  output [15:0] C4
);

  wire [15:0] multiplier_1_out, multiplier_2_out, multiplier_3_out, multiplier_4_out, multiplier_5_out,
       multiplier_6_out, multiplier_7_out, multiplier_8_out;

  Multiplier #(.width(16)) multiplier_1 (.a(A1), .b(B1), .out(multiplier_1_out));  // open: cin, cout
  Multiplier #(.width(16)) multiplier_2 (.a(A2), .b(B3), .out(multiplier_2_out));  // open: cin, cout
  Multiplier #(.width(16)) multiplier_3 (.a(A1), .b(B2), .out(multiplier_3_out));  // open: cin, cout
  Multiplier #(.width(16)) multiplier_4 (.a(A2), .b(B4), .out(multiplier_4_out));  // open: cin, cout
  Multiplier #(.width(16)) multiplier_5 (.a(A3), .b(B1), .out(multiplier_5_out));  // open: cin, cout
  Multiplier #(.width(16)) multiplier_6 (.a(A4), .b(B3), .out(multiplier_6_out));  // open: cin, cout
  Multiplier #(.width(16)) multiplier_7 (.a(A3), .b(B2), .out(multiplier_7_out));  // open: cin, cout
  Multiplier #(.width(16)) multiplier_8 (.a(A4), .b(A4), .out(multiplier_8_out));  // open: cin, cout
  Adder #(.width(16)) adder_1 (.a(multiplier_1_out), .b(multiplier_2_out), .out(C1));  // open: cin, cout
  Adder #(.width(16)) adder_2 (.a(multiplier_3_out), .b(multiplier_4_out), .out(C2));  // open: cin, cout
  Adder #(.width(16)) adder_3 (.a(multiplier_5_out), .b(multiplier_6_out), .out(C3));  // open: cin, cout
  Adder #(.width(16)) adder_4 (.a(multiplier_7_out), .b(multiplier_8_out), .out(C4));  // open: cin, cout
endmodule

module matMult_4x4 (
  input  [15:0] row1,
  input  [15:0] row2,
  input  [15:0] row3,
  input  [15:0] row4,
  input  [15:0] col1,
  input  [15:0] col2,
  input  [15:0] col3,
  input  [15:0] col4,
  output [15:0] Element,
  output carryout
);

  wire [15:0] adder_1_out, adder_2_out, multiplier_1_out, multiplier_2_out, multiplier_3_out,
       multiplier_4_out;

  Multiplier #(.width(16)) multiplier_1 (.a(row1), .b(col1), .out(multiplier_1_out));  // open: cin, cout
  Multiplier #(.width(16)) multiplier_2 (.a(row2), .b(col2), .out(multiplier_2_out));  // open: cin, cout
  Multiplier #(.width(16)) multiplier_3 (.a(row3), .b(col3), .out(multiplier_3_out));  // open: cin, cout
  Multiplier #(.width(16)) multiplier_4 (.a(row4), .b(col4), .out(multiplier_4_out));  // open: cin, cout
  Adder #(.width(16)) adder_1 (.a(multiplier_1_out), .b(multiplier_2_out), .out(adder_1_out));  // open: cin, cout
  Adder #(.width(16)) adder_2 (.a(multiplier_3_out), .b(multiplier_4_out), .out(adder_2_out));  // open: cin, cout
  Adder #(.width(16)) adder_3 (.a(adder_1_out), .b(adder_2_out), .out(Element), .cout(carryout));  // open: cin
endmodule

module adder_16bit (
  input  Carry_in,
  input  [15:0] A,
  input  [15:0] B,
  output [15:0] Result,
  output Carry_out
);

  wire adder_8bit_1_carry_out;

  // Probe on A
  // Probe on B
  // Probe on Result
  adder_8bit adder_8bit_1 (
    .Carry_in(Carry_in), .A(A[7:0]), .B(B[7:0]), .Result(Result[7:0]), .Carry_out(adder_8bit_1_carry_out));
  adder_8bit adder_8bit_2 (
    .Carry_in(adder_8bit_1_carry_out), .A(A[15:8]), .B(B[15:8]), .Result(Result[15:8]), .Carry_out(Carry_out));
  // Probe on Carry_out
endmodule

module multiadder_16bit (
  input  [15:0] A1,
  input  [15:0] A2,
  input  [15:0] A3,
  input  [15:0] A4,
  input  [15:0] B1,
  input  [15:0] B2,
  input  [15:0] B3,
  input  [15:0] B4,
  output [15:0] R1,
  output [15:0] R2,
  output [15:0] R3,
  output [15:0] R4,
  output C1,
  output C2,
  output C3,
  output C4
);

  adder_16bit adder_16bit_1 (.A(A1), .B(B1), .Result(R1), .Carry_out(C1));  // open: Carry_in
  adder_16bit adder_16bit_2 (.A(A2), .B(B2), .Result(R2), .Carry_out(C2));  // open: Carry_in
  adder_16bit adder_16bit_3 (.A(A3), .B(B3), .Result(R3), .Carry_out(C3));  // open: Carry_in
  adder_16bit adder_16bit_4 (.A(A4), .B(B4), .Result(R4), .Carry_out(C4));  // open: Carry_in
endmodule

module sum_4val (
  input  [15:0] sum1,
  input  [15:0] sum2,
  input  [15:0] sum3,
  input  [15:0] sum4,
  output [15:0] result,
  output carry
);

  wire [15:0] adder_16bit_1_result, adder_16bit_2_result;

  adder_16bit adder_16bit_1 (.A(sum1), .B(sum2), .Result(adder_16bit_1_result));  // open: Carry_in, Carry_out
  adder_16bit adder_16bit_2 (.A(sum3), .B(sum4), .Result(adder_16bit_2_result));  // open: Carry_in, Carry_out
  adder_16bit adder_16bit_3 (
    .A(adder_16bit_1_result), .B(adder_16bit_2_result), .Result(result), .Carry_out(carry));  // open: Carry_in
endmodule

module adder_32bit (
  input  Carry_in,
  input  [31:0] First_Value,
  input  [31:0] Second_Value,
  output [31:0] Result,
  output Carry_out
);

  wire adder_8bit_1_carry_out, adder_8bit_2_carry_out, adder_8bit_3_carry_out;

  // Probe on First_Value
  // Probe on Second_Value
  // Probe on Carry_in
  adder_8bit adder_8bit_1 (
    .Carry_in(Carry_in), .A(First_Value[7:0]), .B(Second_Value[23:16]), .Result(Result[7:0]),
    .Carry_out(adder_8bit_1_carry_out));
  adder_8bit adder_8bit_2 (
    .Carry_in(adder_8bit_1_carry_out), .A(First_Value[15:8]), .B(Second_Value[15:8]), .Result(Result[15:8]),
    .Carry_out(adder_8bit_2_carry_out));
  adder_8bit adder_8bit_3 (
    .Carry_in(adder_8bit_2_carry_out), .A(First_Value[23:16]), .B(Second_Value[7:0]), .Result(Result[23:16]),
    .Carry_out(adder_8bit_3_carry_out));
  adder_8bit adder_8bit_4 (
    .Carry_in(adder_8bit_3_carry_out), .A(First_Value[31:24]), .B(Second_Value[31:24]),
    .Result(Result[31:24]), .Carry_out(Carry_out));
  // Probe on Result
endmodule

module adder_8bit (
  input  Carry_in,
  input  [7:0] A,
  input  [7:0] B,
  output [7:0] Result,
  output Carry_out
);

  wire adder_4bit_1_out_5;

  // Probe on A
  // Probe on B
  adder_4bit adder_4bit_1 (
    .in_1(Carry_in), .in_2(A[3:0]), .in_3(B[3:0]), .out_4(Result[3:0]), .out_5(adder_4bit_1_out_5));
  adder_4bit adder_4bit_2 (
    .in_1(adder_4bit_1_out_5), .in_2(A[7:4]), .in_3(B[7:4]), .out_4(Result[7:4]), .out_5(Carry_out));
  // Probe on Result
  // Probe on Carry_out
endmodule

module adder_4bit (
  input  in_1,
  input  [3:0] in_2,
  input  [3:0] in_3,
  output [3:0] out_4,
  output out_5
);

  wire adder_2bit_1_out_5;

  // Probe on in_2
  // Probe on in_3
  adder_2bit adder_2bit_1 (
    .InitialCarry(in_1), .A(in_2[1:0]), .B(in_3[1:0]), .sum(out_4[1:0]), .out_5(adder_2bit_1_out_5));
  adder_2bit adder_2bit_2 (
    .InitialCarry(adder_2bit_1_out_5), .A(in_2[3:2]), .B(in_3[3:2]), .sum(out_4[3:2]), .out_5(out_5));
  // Probe on out_4
  // Probe on out_5
endmodule

module adder_2bit (
  input  InitialCarry,
  input  [1:0] A,
  input  [1:0] B,
  output [1:0] sum,
  output out_5
);

  wire adder_1bit_1_carry_out;

  adder_1bit adder_1bit_1 (
    .A(A[0]), .B(B[0]), .Carry_in(InitialCarry), .Sum(sum[0]), .Carry_out(adder_1bit_1_carry_out));
  // Probe on sum
  adder_1bit adder_1bit_2 (.A(A[1]), .B(B[1]), .Carry_in(adder_1bit_1_carry_out), .Sum(sum[1]), .Carry_out(out_5));
endmodule

module adder_1bit (
  input  A,
  input  B,
  input  Carry_in,
  output Sum,
  output Carry_out
);

  wire and_1_out, and_2_out, xor_1_out;

  xor xor_1 (xor_1_out, A, B);
  and and_1 (and_1_out, A, B);
  xor xor_2 (Sum, xor_1_out, Carry_in);
  and and_2 (and_2_out, xor_1_out, Carry_in);
  or or_1 (Carry_out, and_2_out, and_1_out);
endmodule

module test_tiling (
  input  in_1,
  input  [7:0] in_2
);

  wire clock_1_out, clock_2_out;
  wire [3:0] rom_1_data;
  wire [7:0] counter_1_q, counter_2_q, counter_3_q;
  wire [15:0] ram_1_dout, ram_2_dout;

  ROM #(.dataWidth(4)) rom_1 (.addr(counter_1_q), .data(rom_1_data));
  Counter counter_1 (.Q(counter_1_q), .clk(clock_1_out));  // open: load, D, count, carry, up, clr
  Clock clock_1 (.out(clock_1_out));
  Counter #(.max('hf)) counter_2 (
    .count(rom_1_data[3]), .Q(counter_2_q), .clk(clock_1_out));  // open: load, D, carry, up, clr
  Counter #(.max('hf)) counter_3 (
    .load(rom_1_data[1]), .D(8'h8), .count(rom_1_data[2]), .Q(counter_3_q), .clk(clock_1_out),
    .clr(rom_1_data[0]));  // open: carry, up
  RAM #(.dataWidth(16)) ram_1 (.addr(counter_2_q), .clk(clock_1_out), .dout(ram_1_dout));  // open: we, oe, din
  RAM #(.dataWidth(16)) ram_2 (.addr(counter_3_q), .clk(clock_1_out), .dout(ram_2_dout));  // open: we, oe, din
  // Probe on ram_1_dout
  // Probe on ram_2_dout
  Clock clock_2 (.out(clock_2_out));
  Counter counter_4 (.load(in_1), .D(in_2), .clk(clock_2_out));  // open: count, Q, carry, up, clr

  // Notes on the sheet:
  //   contents of rom_1 (hex, n*v repeats v):
  //   8*c 1 15*c e 8*c
  //   Test Case for seeing how to use counters in normal tiling 
endmodule

module decoder_custom (
  input  x1,
  input  x2,
  input  x3,
  input  x4,
  input  Enable,
  output y1,
  output y2,
  output y3,
  output y4,
  output y5,
  output y6,
  output y7,
  output y8,
  output y9,
  output y10,
  output y11,
  output y12,
  output y13,
  output y14,
  output y15,
  output y16
);

  wire not_1_out, not_2_out, not_3_out, not_4_out;

  not not_1 (not_1_out, x1);
  not not_2 (not_2_out, x2);
  not not_3 (not_3_out, x3);
  not not_4 (not_4_out, x4);
  and and_1 (y1, not_1_out, not_2_out, Enable, not_3_out, not_4_out);
  and and_2 (y2, x1, not_2_out, Enable, not_3_out, not_4_out);
  and and_3 (y3, not_1_out, x2, Enable, not_3_out, not_4_out);
  and and_4 (y4, x1, x2, Enable, not_3_out, not_4_out);
  and and_5 (y5, not_1_out, not_2_out, Enable, x3, not_4_out);
  and and_6 (y6, x1, not_2_out, Enable, x3, not_4_out);
  and and_7 (y7, not_1_out, x2, Enable, x3, not_4_out);
  and and_8 (y8, x1, x2, Enable, x3, not_4_out);
  and and_9 (y9, not_1_out, not_2_out, Enable, not_3_out, x4);
  and and_10 (y10, x1, not_2_out, Enable, not_3_out, x4);
  and and_11 (y11, not_1_out, x2, Enable, not_3_out, x4);
  and and_12 (y12, x1, x2, Enable, not_3_out, x4);
  and and_13 (y13, not_1_out, not_2_out, Enable, x3, x4);
  and and_14 (y14, x1, not_2_out, Enable, x3, x4);
  and and_15 (y15, not_1_out, x2, Enable, x3, x4);
  and and_16 (y16, x1, x2, Enable, x3, x4);
endmodule

module Decoder_4val (
  input  x1,
  input  x2,
  input  x3,
  input  x4,
  input  Enable,
  output y1,
  output y2,
  output y3,
  output y4
);

  wire not_1_out, not_2_out, not_3_out, not_4_out;

  not not_1 (not_1_out, x1);
  not not_2 (not_2_out, x2);
  not not_3 (not_3_out, x3);
  not not_4 (not_4_out, x4);
  and and_1 (y1, not_1_out, not_2_out, Enable, not_3_out, not_4_out);
  and and_2 (y2, x1, not_2_out, Enable, not_3_out, not_4_out);
  and and_3 (y3, not_1_out, x2, Enable, not_3_out, not_4_out);
  and and_4 (y4, x1, x2, Enable, not_3_out, not_4_out);
endmodule

module Info_LoadA (
  input  [3:0] Dim_A_In,
  input  [7:0] Add_A_In,
  input  WE_A,
  input  Clock_A,
  output [3:0] Dim_A_out,
  output [7:0] Addres_A_out
);

  Register #(.width(4)) Dim_A (.D(Dim_A_In), .en(WE_A), .clk(Clock_A), .Q(Dim_A_out));  // open: clr
  Register Address_A (.D(Add_A_In), .en(WE_A), .clk(Clock_A), .Q(Addres_A_out));  // open: clr
endmodule

module Info_loadB (
  input  [3:0] Dim_B_In,
  input  [7:0] Add_B_In,
  input  WE_B,
  input  Clock_B,
  output [3:0] Dim_B_out,
  output [7:0] Addres_B_out
);

  Register #(.width(4)) Dim_B (.D(Dim_B_In), .en(WE_B), .clk(Clock_B), .Q(Dim_B_out));  // open: clr
  Register Address_B (.D(Add_B_In), .en(WE_B), .clk(Clock_B), .Q(Addres_B_out));  // open: clr
endmodule

module Info_mmult (
  input  [3:0] Dim_B_In,
  input  [7:0] Add_B_In,
  input  WE_M,
  input  Clock_M,
  output [3:0] Dim_Mmult,
  output [7:0] Addres_Mmult
);

  Register #(.width(4)) Dim_M (.D(Dim_B_In), .en(WE_M), .clk(Clock_M), .Q(Dim_Mmult));  // open: clr
  Register Address_M (.D(Add_B_In), .en(WE_M), .clk(Clock_M), .Q(Addres_Mmult));  // open: clr
endmodule

module Info_stoC (
  input  [3:0] Dim_Store_In,
  input  [7:0] Add_Store_In,
  input  WE_Store,
  input  Clock_Store,
  output [3:0] Dim_Store_Out,
  output [7:0] Addres_Store_Out
);

  Register #(.width(4)) Dim_Store (.D(Dim_Store_In), .en(WE_Store), .clk(Clock_Store), .Q(Dim_Store_Out));  // open: clr
  Register Address_Store (.D(Add_Store_In), .en(WE_Store), .clk(Clock_Store), .Q(Addres_Store_Out));  // open: clr
endmodule

module test_fix_decoder (
  input  x1,
  input  x2,
  input  x3,
  input  x4,
  input  Enable,
  output y1,
  output y2,
  output y3,
  output y4,
  output y5,
  output y6,
  output y7,
  output y8,
  output y9,
  output y10,
  output y11,
  output y12,
  output y13,
  output y14,
  output y15,
  output y16
);

  wire not_1_out, not_2_out, not_3_out, not_4_out;

  not not_1 (not_1_out, x1);
  not not_2 (not_2_out, x2);
  not not_3 (not_3_out, x3);
  not not_4 (not_4_out, x4);
  and and_1 (y1, not_1_out, not_2_out, Enable, not_3_out, not_4_out);
  and and_2 (y2, x1, not_2_out, Enable, not_3_out, not_4_out);
  and and_3 (y3, not_1_out, x2, Enable, not_3_out, not_4_out);
  and and_4 (y4, x1, x2, Enable, not_3_out, not_4_out);
  and and_5 (y5, not_1_out, not_2_out, Enable, x3, not_4_out);
  and and_6 (y6, x1, not_2_out, Enable, x3, not_4_out);
  and and_7 (y7, not_1_out, x2, Enable, x3, not_4_out);
  and and_8 (y8, x1, x2, Enable, x3, not_4_out);
  and and_9 (y9, not_1_out, not_2_out, Enable, not_3_out, x4);
  and and_10 (y10, x1, not_2_out, Enable, not_3_out, x4);
  and and_11 (y11, not_1_out, x2, Enable, not_3_out, x4);
  and and_12 (y12, x1, x2, Enable, not_3_out, x4);
  and and_13 (y13, not_1_out, not_2_out, Enable, x3, x4);
  and and_14 (y14, x1, not_2_out, Enable, x3, x4);
  and and_15 (y15, not_1_out, x2, Enable, x3, x4);
  and and_16 (y16, x1, x2, Enable, x3, x4);
endmodule

module Tiling_add (
  input  [15:0] v1,
  input  [15:0] v2,
  input  [15:0] v3,
  input  [15:0] v4,
  input  [15:0] v5,
  input  [15:0] v6,
  input  [15:0] v7,
  input  [15:0] v8,
  input  [15:0] v9,
  input  [15:0] v10,
  input  [15:0] v11,
  input  [15:0] v12,
  input  [15:0] v13,
  input  [15:0] v14,
  input  [15:0] v15,
  input  [15:0] v16,
  input  WE,
  input  Clock,
  output [15:0] R1,
  output [15:0] R2,
  output [15:0] R3,
  output [15:0] R4,
  output [15:0] R5,
  output [15:0] R6,
  output [15:0] R7,
  output [15:0] R8,
  output [15:0] R9,
  output [15:0] R10,
  output [15:0] R11,
  output [15:0] R12,
  output [15:0] R13,
  output [15:0] R14,
  output [15:0] R15,
  output [15:0] R16
);

  wire [15:0] adder_1_out, adder_2_out, adder_3_out, adder_4_out, adder_5_out, adder_6_out, adder_7_out,
       adder_8_out, adder_9_out, adder_10_out, adder_11_out, adder_12_out, adder_13_out, adder_14_out,
       adder_15_out, adder_16_out;

  Adder #(.width(16)) adder_1 (.a(R1), .b(v1), .out(adder_1_out));  // open: cin, cout
  Adder #(.width(16)) adder_2 (.a(R2), .b(v2), .out(adder_2_out));  // open: cin, cout
  Adder #(.width(16)) adder_3 (.a(R3), .b(v3), .out(adder_3_out));  // open: cin, cout
  Adder #(.width(16)) adder_4 (.a(R4), .b(v4), .out(adder_4_out));  // open: cin, cout
  Adder #(.width(16)) adder_5 (.a(R5), .b(v5), .out(adder_5_out));  // open: cin, cout
  Adder #(.width(16)) adder_6 (.a(R6), .b(v6), .out(adder_6_out));  // open: cin, cout
  Adder #(.width(16)) adder_7 (.a(R7), .b(v7), .out(adder_7_out));  // open: cin, cout
  Adder #(.width(16)) adder_8 (.a(R8), .b(v8), .out(adder_8_out));  // open: cin, cout
  Adder #(.width(16)) adder_9 (.a(R9), .b(v9), .out(adder_9_out));  // open: cin, cout
  Adder #(.width(16)) adder_10 (.a(R10), .b(v10), .out(adder_10_out));  // open: cin, cout
  Adder #(.width(16)) adder_11 (.a(R11), .b(v11), .out(adder_11_out));  // open: cin, cout
  Adder #(.width(16)) adder_12 (.a(R12), .b(v12), .out(adder_12_out));  // open: cin, cout
  Adder #(.width(16)) adder_13 (.a(R13), .b(v13), .out(adder_13_out));  // open: cin, cout
  Adder #(.width(16)) adder_14 (.a(R14), .b(v14), .out(adder_14_out));  // open: cin, cout
  Adder #(.width(16)) adder_15 (.a(R15), .b(v15), .out(adder_15_out));  // open: cin, cout
  Adder #(.width(16)) adder_16 (.a(R16), .b(v16), .out(adder_16_out));  // open: cin, cout
  Register #(.width(16)) register_1 (.D(adder_1_out), .en(WE), .clk(Clock), .Q(R1));  // open: clr
  Register #(.width(16)) register_2 (.D(adder_2_out), .en(WE), .clk(Clock), .Q(R2));  // open: clr
  Register #(.width(16)) register_3 (.D(adder_3_out), .en(WE), .clk(Clock), .Q(R3));  // open: clr
  Register #(.width(16)) register_4 (.D(adder_4_out), .en(WE), .clk(Clock), .Q(R4));  // open: clr
  Register #(.width(16)) register_5 (.D(adder_5_out), .en(WE), .clk(Clock), .Q(R5));  // open: clr
  Register #(.width(16)) register_6 (.D(adder_6_out), .en(WE), .clk(Clock), .Q(R6));  // open: clr
  Register #(.width(16)) register_7 (.D(adder_7_out), .en(WE), .clk(Clock), .Q(R7));  // open: clr
  Register #(.width(16)) register_8 (.D(adder_8_out), .en(WE), .clk(Clock), .Q(R8));  // open: clr
  Register #(.width(16)) register_9 (.D(adder_9_out), .en(WE), .clk(Clock), .Q(R9));  // open: clr
  Register #(.width(16)) register_10 (.D(adder_10_out), .en(WE), .clk(Clock), .Q(R10));  // open: clr
  Register #(.width(16)) register_11 (.D(adder_11_out), .en(WE), .clk(Clock), .Q(R11));  // open: clr
  Register #(.width(16)) register_12 (.D(adder_12_out), .en(WE), .clk(Clock), .Q(R12));  // open: clr
  Register #(.width(16)) register_13 (.D(adder_13_out), .en(WE), .clk(Clock), .Q(R13));  // open: clr
  Register #(.width(16)) register_14 (.D(adder_14_out), .en(WE), .clk(Clock), .Q(R14));  // open: clr
  Register #(.width(16)) register_15 (.D(adder_15_out), .en(WE), .clk(Clock), .Q(R15));  // open: clr
  Register #(.width(16)) register_16 (.D(adder_16_out), .en(WE), .clk(Clock), .Q(R16));  // open: clr
endmodule

module Matrix_Acumulator (
  input  [15:0] V1,
  input  [15:0] V2,
  input  [15:0] V3,
  input  [15:0] V4,
  input  [15:0] V5,
  input  [15:0] V6,
  input  [15:0] V7,
  input  [15:0] V8,
  input  [15:0] V9,
  input  [15:0] V10,
  input  [15:0] V11,
  input  [15:0] V12,
  input  [15:0] V13,
  input  [15:0] V14,
  input  [15:0] V15,
  input  [15:0] V16,
  input  [3:0] Tile_Num,
  input  clock,
  input  Enable,
  output [15:0] a1,
  output [15:0] a2,
  output [15:0] a3,
  output [15:0] a4,
  output [15:0] a5,
  output [15:0] a6,
  output [15:0] a7,
  output [15:0] a8,
  output [15:0] a9,
  output [15:0] a10,
  output [15:0] a11,
  output [15:0] a12,
  output [15:0] a13,
  output [15:0] a14,
  output [15:0] a15,
  output [15:0] a16,
  output [15:0] b1,
  output [15:0] b2,
  output [15:0] b3,
  output [15:0] b4,
  output [15:0] b5,
  output [15:0] b6,
  output [15:0] b7,
  output [15:0] b8,
  output [15:0] b9,
  output [15:0] b10,
  output [15:0] b11,
  output [15:0] b12,
  output [15:0] b13,
  output [15:0] b14,
  output [15:0] b15,
  output [15:0] b16,
  output [15:0] c1,
  output [15:0] c2,
  output [15:0] c3,
  output [15:0] c4,
  output [15:0] c5,
  output [15:0] c6,
  output [15:0] c7,
  output [15:0] c8,
  output [15:0] c9,
  output [15:0] c10,
  output [15:0] c11,
  output [15:0] c12,
  output [15:0] c13,
  output [15:0] c14,
  output [15:0] c15,
  output [15:0] c16
);

  wire comparator_1_eq, comparator_2_eq, comparator_3_eq, comparator_4_eq, decoder_4val_1_y1,
       decoder_4val_1_y2, decoder_4val_1_y3, xor_1_out;
  wire [3:0] controlled_buffer_1_out, counter_1_q, counter_2_q;

  assign controlled_buffer_1_out = comparator_1_eq ? 4'b0011 : 4'bz;  // Controlled_Buffer controlled_buffer_1
  Comparator #(.width(4)) comparator_1 (.a(Tile_Num), .b(4'b0100), .eq(comparator_1_eq));  // open: gt, lt
  Comparator #(.width(4)) comparator_2 (.a(Tile_Num), .b(4'b1001), .eq(comparator_2_eq));  // open: gt, lt
  assign controlled_buffer_1_out = comparator_2_eq ? 4'b0100 : 4'bz;  // Controlled_Buffer controlled_buffer_2
  xor xor_1 (xor_1_out, Enable, comparator_4_eq);
  Counter #(.max('hf), .width(4)) counter_1 (
    .count(xor_1_out), .Q(counter_1_q), .clk(clock), .clr(comparator_3_eq));  // open: load, D, carry, up
  Comparator #(.mode("unsigned"), .width(4)) comparator_3 (
    .a(counter_1_q), .b(controlled_buffer_1_out), .eq(comparator_3_eq));  // open: gt, lt
  Counter #(.max('hf), .width(4)) counter_2 (
    .count(comparator_3_eq), .Q(counter_2_q), .clk(clock));  // open: load, D, carry, up, clr
  Comparator #(.width(4)) comparator_4 (
    .a(counter_2_q), .b(controlled_buffer_1_out), .eq(comparator_4_eq));  // open: gt, lt
  Decoder_4val decoder_4val_1 (
    .x1(counter_1_q[0]), .x2(counter_1_q[1]), .x3(counter_1_q[2]), .x4(counter_1_q[3]), .Enable(xor_1_out),
    .y1(decoder_4val_1_y1), .y2(decoder_4val_1_y2), .y3(decoder_4val_1_y3));  // open: y4
  Tiling_add tiling_add_1 (
    .v1(V1), .v2(V2), .v3(V3), .v4(V4), .v5(V5), .v6(V6), .v7(V7), .v8(V8), .v9(V9), .v10(V10), .v11(V11),
    .v12(V12), .v13(V13), .v14(V14), .v15(V15), .v16(V16), .WE(decoder_4val_1_y1), .Clock(clock), .R1(a1),
    .R2(a2), .R3(a3), .R4(a4), .R5(a5), .R6(a6), .R7(a7), .R8(a8), .R9(a9), .R10(a10), .R11(a11), .R12(a12),
    .R13(a13), .R14(a14), .R15(a15), .R16(a16));
  Tiling_add tiling_add_2 (
    .v1(V1), .v2(V2), .v3(V3), .v4(V4), .v5(V5), .v6(V6), .v7(V7), .v8(V8), .v9(V9), .v10(V10), .v11(V11),
    .v12(V12), .v13(V13), .v14(V14), .v15(V15), .v16(V16), .WE(decoder_4val_1_y2), .Clock(clock), .R1(b1),
    .R2(b2), .R3(b3), .R4(b4), .R5(b5), .R6(b6), .R7(b7), .R8(b8), .R9(b9), .R10(b10), .R11(b11), .R12(b12),
    .R13(b13), .R14(b14), .R15(b15), .R16(b16));
  Tiling_add tiling_add_3 (
    .v1(V1), .v2(V2), .v3(V3), .v4(V4), .v5(V5), .v6(V6), .v7(V7), .v8(V8), .v9(V9), .v10(V10), .v11(V11),
    .v12(V12), .v13(V13), .v14(V14), .v15(V15), .v16(V16), .WE(decoder_4val_1_y3), .Clock(clock), .R1(c1),
    .R2(c2), .R3(c3), .R4(c4), .R5(c5), .R6(c6), .R7(c7), .R8(c8), .R9(c9), .R10(c10), .R11(c11), .R12(c12),
    .R13(c13), .R14(c14), .R15(c15), .R16(c16));
endmodule

module Vec_mem (
  input  [15:0] a1,
  input  [15:0] b1,
  input  [15:0] c1,
  input  [15:0] a2,
  input  [15:0] b2,
  input  [15:0] c2,
  input  [15:0] a3,
  input  [15:0] b3,
  input  [15:0] c3,
  input  [15:0] a4,
  input  [15:0] b4,
  input  [15:0] c4,
  input  [15:0] a5,
  input  [15:0] b5,
  input  [15:0] c5,
  input  [15:0] a6,
  input  [15:0] b6,
  input  [15:0] c6,
  input  [15:0] a7,
  input  [15:0] b7,
  input  [15:0] c7,
  input  [15:0] a8,
  input  [15:0] b8,
  input  [15:0] c8,
  input  [15:0] a9,
  input  [15:0] b9,
  input  [15:0] c9,
  input  [15:0] a10,
  input  [15:0] b10,
  input  [15:0] c10,
  input  [15:0] a11,
  input  [15:0] b11,
  input  [15:0] c11,
  input  [15:0] a12,
  input  [15:0] b12,
  input  [15:0] c12,
  input  [15:0] a13,
  input  [15:0] b13,
  input  [15:0] c13,
  input  [15:0] a14,
  input  [15:0] b14,
  input  [15:0] c14,
  input  [15:0] a15,
  input  [15:0] b15,
  input  [15:0] c15,
  input  [15:0] a16,
  input  [15:0] b16,
  input  [15:0] c16
);

  wire decoder_custom_1_y1, decoder_custom_1_y2, decoder_custom_1_y3, decoder_custom_1_y4,
       decoder_custom_1_y5, decoder_custom_1_y6, decoder_custom_1_y7, decoder_custom_1_y8,
       decoder_custom_1_y9, decoder_custom_1_y10, decoder_custom_1_y11, decoder_custom_1_y12,
       decoder_custom_1_y13, decoder_custom_1_y14, decoder_custom_1_y15, decoder_custom_1_y16;
  wire [15:0] controlled_buffer_1_out, controlled_buffer_17_out, controlled_buffer_33_out;

  assign controlled_buffer_1_out = decoder_custom_1_y1 ? a1 : 16'bz;  // Controlled_Buffer controlled_buffer_1
  assign controlled_buffer_1_out = decoder_custom_1_y2 ? a2 : 16'bz;  // Controlled_Buffer controlled_buffer_2
  assign controlled_buffer_1_out = decoder_custom_1_y3 ? a3 : 16'bz;  // Controlled_Buffer controlled_buffer_3
  decoder_custom decoder_custom_1 (
    .y1(decoder_custom_1_y1), .y2(decoder_custom_1_y2), .y3(decoder_custom_1_y3), .y4(decoder_custom_1_y4),
    .y5(decoder_custom_1_y5), .y6(decoder_custom_1_y6), .y7(decoder_custom_1_y7), .y8(decoder_custom_1_y8),
    .y9(decoder_custom_1_y9), .y10(decoder_custom_1_y10), .y11(decoder_custom_1_y11),
    .y12(decoder_custom_1_y12), .y13(decoder_custom_1_y13), .y14(decoder_custom_1_y14),
    .y15(decoder_custom_1_y15), .y16(decoder_custom_1_y16));  // open: x1, x2, x3, x4, Enable
  assign controlled_buffer_1_out = decoder_custom_1_y4 ? a4 : 16'bz;  // Controlled_Buffer controlled_buffer_4
  assign controlled_buffer_1_out = decoder_custom_1_y5 ? a5 : 16'bz;  // Controlled_Buffer controlled_buffer_5
  assign controlled_buffer_1_out = decoder_custom_1_y6 ? a6 : 16'bz;  // Controlled_Buffer controlled_buffer_6
  assign controlled_buffer_1_out = decoder_custom_1_y7 ? a7 : 16'bz;  // Controlled_Buffer controlled_buffer_7
  assign controlled_buffer_1_out = decoder_custom_1_y8 ? a8 : 16'bz;  // Controlled_Buffer controlled_buffer_8
  assign controlled_buffer_1_out = decoder_custom_1_y9 ? a9 : 16'bz;  // Controlled_Buffer controlled_buffer_9
  assign controlled_buffer_1_out = decoder_custom_1_y10 ? a10 : 16'bz;  // Controlled_Buffer controlled_buffer_10
  assign controlled_buffer_1_out = decoder_custom_1_y11 ? a11 : 16'bz;  // Controlled_Buffer controlled_buffer_11
  assign controlled_buffer_1_out = decoder_custom_1_y12 ? a12 : 16'bz;  // Controlled_Buffer controlled_buffer_12
  assign controlled_buffer_1_out = decoder_custom_1_y13 ? a13 : 16'bz;  // Controlled_Buffer controlled_buffer_13
  assign controlled_buffer_1_out = decoder_custom_1_y14 ? a14 : 16'bz;  // Controlled_Buffer controlled_buffer_14
  assign controlled_buffer_1_out = decoder_custom_1_y15 ? a15 : 16'bz;  // Controlled_Buffer controlled_buffer_15
  assign controlled_buffer_1_out = decoder_custom_1_y16 ? a16 : 16'bz;  // Controlled_Buffer controlled_buffer_16
  RAM #(.addrWidth(4), .dataWidth(16)) ram_1 (.din(controlled_buffer_1_out));  // open: addr, we, oe, clk, dout
  RAM #(.addrWidth(4), .dataWidth(16)) ram_2 (.din(controlled_buffer_1_out));  // open: addr, we, oe, clk, dout
  RAM #(.addrWidth(4), .dataWidth(16)) ram_3 (.din(controlled_buffer_1_out));  // open: addr, we, oe, clk, dout
  assign controlled_buffer_17_out = decoder_custom_1_y1 ? b1 : 16'bz;  // Controlled_Buffer controlled_buffer_17
  assign controlled_buffer_17_out = decoder_custom_1_y2 ? b2 : 16'bz;  // Controlled_Buffer controlled_buffer_18
  assign controlled_buffer_17_out = decoder_custom_1_y3 ? b3 : 16'bz;  // Controlled_Buffer controlled_buffer_19
  assign controlled_buffer_17_out = decoder_custom_1_y4 ? b4 : 16'bz;  // Controlled_Buffer controlled_buffer_20
  assign controlled_buffer_17_out = decoder_custom_1_y5 ? b5 : 16'bz;  // Controlled_Buffer controlled_buffer_21
  assign controlled_buffer_17_out = decoder_custom_1_y6 ? b6 : 16'bz;  // Controlled_Buffer controlled_buffer_22
  assign controlled_buffer_17_out = decoder_custom_1_y7 ? b7 : 16'bz;  // Controlled_Buffer controlled_buffer_23
  assign controlled_buffer_17_out = decoder_custom_1_y8 ? b8 : 16'bz;  // Controlled_Buffer controlled_buffer_24
  assign controlled_buffer_17_out = decoder_custom_1_y9 ? b9 : 16'bz;  // Controlled_Buffer controlled_buffer_25
  assign controlled_buffer_17_out = decoder_custom_1_y10 ? b10 : 16'bz;  // Controlled_Buffer controlled_buffer_26
  assign controlled_buffer_17_out = decoder_custom_1_y11 ? b11 : 16'bz;  // Controlled_Buffer controlled_buffer_27
  assign controlled_buffer_17_out = decoder_custom_1_y12 ? b12 : 16'bz;  // Controlled_Buffer controlled_buffer_28
  assign controlled_buffer_17_out = decoder_custom_1_y13 ? b13 : 16'bz;  // Controlled_Buffer controlled_buffer_29
  assign controlled_buffer_17_out = decoder_custom_1_y14 ? b14 : 16'bz;  // Controlled_Buffer controlled_buffer_30
  assign controlled_buffer_17_out = decoder_custom_1_y15 ? b15 : 16'bz;  // Controlled_Buffer controlled_buffer_31
  assign controlled_buffer_17_out = decoder_custom_1_y16 ? b16 : 16'bz;  // Controlled_Buffer controlled_buffer_32
  RAM #(.addrWidth(4), .dataWidth(16)) ram_4 (.din(controlled_buffer_17_out));  // open: addr, we, oe, clk, dout
  RAM #(.addrWidth(4), .dataWidth(16)) ram_5 ();  // open: addr, we, oe, clk, din, dout
  RAM #(.addrWidth(4), .dataWidth(16)) ram_6 (.din(controlled_buffer_17_out));  // open: addr, we, oe, clk, dout
  assign controlled_buffer_33_out = decoder_custom_1_y1 ? c1 : 16'bz;  // Controlled_Buffer controlled_buffer_33
  assign controlled_buffer_33_out = decoder_custom_1_y2 ? c2 : 16'bz;  // Controlled_Buffer controlled_buffer_34
  assign controlled_buffer_33_out = decoder_custom_1_y3 ? c3 : 16'bz;  // Controlled_Buffer controlled_buffer_35
  assign controlled_buffer_33_out = decoder_custom_1_y4 ? c4 : 16'bz;  // Controlled_Buffer controlled_buffer_36
  assign controlled_buffer_33_out = decoder_custom_1_y5 ? c5 : 16'bz;  // Controlled_Buffer controlled_buffer_37
  assign controlled_buffer_33_out = decoder_custom_1_y6 ? c6 : 16'bz;  // Controlled_Buffer controlled_buffer_38
  assign controlled_buffer_33_out = decoder_custom_1_y7 ? c7 : 16'bz;  // Controlled_Buffer controlled_buffer_39
  assign controlled_buffer_33_out = decoder_custom_1_y8 ? c8 : 16'bz;  // Controlled_Buffer controlled_buffer_40
  assign controlled_buffer_33_out = decoder_custom_1_y9 ? c9 : 16'bz;  // Controlled_Buffer controlled_buffer_41
  assign controlled_buffer_33_out = decoder_custom_1_y10 ? c10 : 16'bz;  // Controlled_Buffer controlled_buffer_42
  assign controlled_buffer_33_out = decoder_custom_1_y11 ? c11 : 16'bz;  // Controlled_Buffer controlled_buffer_43
  assign controlled_buffer_33_out = decoder_custom_1_y12 ? c12 : 16'bz;  // Controlled_Buffer controlled_buffer_44
  assign controlled_buffer_33_out = decoder_custom_1_y13 ? c13 : 16'bz;  // Controlled_Buffer controlled_buffer_45
  assign controlled_buffer_33_out = decoder_custom_1_y14 ? c14 : 16'bz;  // Controlled_Buffer controlled_buffer_46
  assign controlled_buffer_33_out = decoder_custom_1_y15 ? c15 : 16'bz;  // Controlled_Buffer controlled_buffer_47
  assign controlled_buffer_33_out = decoder_custom_1_y16 ? c16 : 16'bz;  // Controlled_Buffer controlled_buffer_48
  RAM #(.addrWidth(4), .dataWidth(16)) ram_7 (.din(controlled_buffer_33_out));  // open: addr, we, oe, clk, dout
  RAM #(.addrWidth(4), .dataWidth(16)) ram_8 (.din(controlled_buffer_33_out));  // open: addr, we, oe, clk, dout
  RAM #(.addrWidth(4), .dataWidth(16)) ram_9 (.din(controlled_buffer_33_out));  // open: addr, we, oe, clk, dout
endmodule
